# Fritzing sketch 1r-DAC (saved by Fritzing 0.4.3b)
breadboards: 1

parts:
  Arduino1 = Arduino
  R1 = Resistor [resistance=22k package=THT]
  J1 = Screw terminal - 2 pins [package=THT]

nets:
  N1: Arduino1.GND, R1.Pin_1, J1.pin2
  N2: Arduino1.D7, Arduino1.D6, Arduino1.D5, Arduino1.D4, R1.Pin_0, J1.pin1
