# Fritzing sketch 3buzzers (saved by Fritzing 0.4.3b)

parts:
  Arduino1 = Arduino
  J2 = Piezo Speaker
  J3 = Piezo Speaker
  J4 = Piezo Speaker

nets:
  N1: Arduino1.D13, J4.pin1
  N2: Arduino1.D12, J2.pin1
  N3: Arduino1.D11, J3.pin1
  N4: Arduino1.+5V, J2.pin2, J3.pin2, J4.pin2

notes:
  Video for how its work, and arduino code visit http://barangulesen.blogspot.com/2010/02/playing-buzzers.html
