# Fritzing sketch 4r-DAC (saved by Fritzing 0.4.3b)
breadboards: 1

parts:
  Arduino1 = Arduino
  R1 = Resistor [resistance=22k package=THT]
  J1 = Screw terminal - 2 pins [package=THT]
  R2 = Resistor [resistance=22k package=THT]
  R3 = Resistor [resistance=22k package=THT]
  R4 = Resistor [resistance=220 package=THT]

nets:
  N1: Arduino1.GND, J1.pin2
  N2: Arduino1.D11, R2.Pin_1
  N3: Arduino1.D10, R3.Pin_1
  N4: Arduino1.D9, R4.Pin_1
  N5: Arduino1.D8, R1.Pin_1
  N6: Arduino1.D7, Arduino1.D6, Arduino1.D5, Arduino1.D4, R1.Pin_0, J1.pin1, R2.Pin_0, R3.Pin_0, R4.Pin_0
