# Fritzing sketch 555TimerDelay (saved by Fritzing 0.4.3b)
breadboards: 1

parts:
  U2 = 555 Timer [package="DIP8 [THT]"]
  C1 = Ceramic Capacitor [package=THT]
  R1 = Resistor [resistance=10k package=THT]
  R2 = Rotary Potentiometer (Small)
  K1 = Relay [package=THT]
  C2 = Electrolytic Capacitor [package=THT]
  D1 = Rectifier Diode [package="300 mil [THT]"]
  D1_2 = Rectifier Diode [package="300 mil [THT]"]
  S1 = Pushbutton [package=THT]
  L1 = Solenoid
  D1_3 = Rectifier Diode [package="300 mil [THT]"]
  9VDC = Battery block 9V

nets:
  N1: U2.Ground, C1.pin_1, K1.COIL1, C2.-, D1.anode, S1.leg0, L1.pin1, 9VDC.-
  N2: U2.Trigger, R1.Pin_1, S1.leg1
  N3: U2.Output, D1_2.anode
  N4: U2.Reset, U2.Vcc_Supply_Voltage, R1.Pin_0, R2.leg1, R2.wiper, K1.C1, K1.C2, 9VDC.+
  N5: U2.Control_Voltage, C1.pin_0
  N6: U2.Threshold, U2.Discharge, R2.leg2, C2.+
  N7: K1.COIL2, D1.cathode, D1_2.cathode, D1_3.anode
  N8: K1.B, L1.pin2, D1_3.cathode
