# Fritzing sketch 7Seg (saved by Fritzing 0.5.2b)
breadboards: 1

parts:
  Arduino1 = Arduino
  DI1 = 7-Segment LED Display [package=THT]
  R1 = Resistor [resistance=33k package=THT]
  S1 = Square Pushbutton

nets:
  N1: Arduino1.GND, R1.Pin_0
  N2: Arduino1.D11, S1.leg1
  N3: Arduino1.D10, R1.Pin_1, S1.leg0
  N4: Arduino1.D6, DI1.cathodeG
  N5: Arduino1.D5, DI1.cathodeF
  N6: Arduino1.D4, DI1.cathodeA
  N7: Arduino1.D3, DI1.commAnode#7
  N8: Arduino1.D2, DI1.cathodeB
  N9: Arduino1.A1, DI1.cathodeE
  N10: Arduino1.A2, DI1.cathodeD
  N11: Arduino1.A3, DI1.commAnode#2
  N12: Arduino1.A4, DI1.cathodeC
  N13: Arduino1.A5, DI1.cathodeDP
