# Fritzing sketch 7Segment_Mod (saved by Fritzing 0.3.19b)
breadboards: 1

parts:
  DI1 = 7-Segment LED Display [package=THT]
  S1 = Tilt Switch [package=THT]
  S2 = Tilt Switch [package=THT]
  S3 = Tilt Switch [package=THT]
  S4 = Tilt Switch [package=THT]
  S5 = Tilt Switch [package=THT]
  S6 = Tilt Switch [package=THT]
  S7 = Tilt Switch [package=THT]
  S8 = Tilt Switch [package=THT]
  VCC1 = obsolete Battery
  R1 = Resistor [resistance=150 package=THT]
  R1_2 = Resistor [resistance=150 package=THT]
  R1_3 = Resistor [resistance=150 package=THT]
  R1_4 = Resistor [resistance=150 package=THT]
  R1_5 = Resistor [resistance=150 package=THT]
  R1_6 = Resistor [resistance=150 package=THT]
  R1_7 = Resistor [resistance=150 package=THT]
  R1_8 = Resistor [resistance=150 package=THT]

nets:
  N1: DI1.cathodeE, R1.Pin_0
  N2: DI1.cathodeD, R1_2.Pin_0
  N3: DI1.commAnode#2, VCC1.+
  N4: DI1.cathodeC, R1_3.Pin_0
  N5: DI1.cathodeDP, R1_4.Pin_0
  N6: DI1.cathodeB, R1_8.Pin_1
  N7: DI1.cathodeA, R1_7.Pin_1
  N8: DI1.cathodeF, R1_6.Pin_1
  N9: DI1.cathodeG, R1_5.Pin_1
  N10: S1.Pin_1, S2.Pin_1, S3.Pin_1, S4.Pin_1, S5.Pin_1, S6.Pin_1, S7.Pin_1, S8.Pin_1, VCC1.-
  N11: S1.Pin_2, R1_5.Pin_0
  N12: S2.Pin_2, R1_6.Pin_0
  N13: S3.Pin_2, R1_7.Pin_0
  N14: S4.Pin_2, R1_8.Pin_0
  N15: S5.Pin_2, R1.Pin_1
  N16: S6.Pin_2, R1_2.Pin_1
  N17: S7.Pin_2, R1_3.Pin_1
  N18: S8.Pin_2, R1_4.Pin_1
