# Fritzing sketch 8-pin-LCD (saved by Fritzing 0.4.2b)
breadboards: 1

parts:
  LCD1 = LCD screen
  Arduino1 = Arduino
  R1 = Trimmer Potentiometer [package=THT]

nets:
  VSS: LCD1.VSS, Arduino1.GND, R1.wiper
  VDD: LCD1.VDD, Arduino1.+5V
  N1: LCD1.V0, R1.leg2
  N2: LCD1.RS, Arduino1.D12
  N3: LCD1.R/W, Arduino1.D10
  N4: LCD1.E, Arduino1.D11
  N5: LCD1.DB0, Arduino1.D2
  N6: LCD1.DB1, Arduino1.D3
  N7: LCD1.DB2, Arduino1.D4
  N8: LCD1.DB3, Arduino1.D5
  N9: LCD1.DB4, Arduino1.D6
  N10: LCD1.DB5, Arduino1.D7
  N11: LCD1.DB6, Arduino1.D8
  N12: LCD1.DB7, Arduino1.D9
