# Fritzing sketch A_ref (saved by Fritzing 0.4.3b)
breadboards: 1

parts:
  Arduino1 = Arduino
  R1 = Trimmer Potentiometer [package=THT]
  R2 = Trimmer Potentiometer [package=THT]
  C1 = Ceramic Capacitor [package=THT]
  VCC1 = Battery block 9V
  U1 = Voltage Regulator - 5V [package="TO220 [THT]"]
  D1 = Rectifier Diode [package="300 mil [THT]"]
  R3 = Resistor [resistance=220 package=THT]

nets:
  N1: Arduino1.aref, R2.wiper, C1.pin_0, R3.Pin_1
  N2: Arduino1.+5V, R1.leg2, R3.Pin_0
  GND: Arduino1.GND, R1.leg1, R2.leg1, C1.pin_1, VCC1.-, U1.GND
  N3: Arduino1.A0, R1.wiper
  N4: R2.leg2, U1.output_voltage, D1.anode
  N5: VCC1.+, U1.input_voltage, D1.cathode

notes:
  Referenz-
  Spannung
  Zu messende
  Spannung
  Bei Verwendung einer externen Referenzspannung unbedingt bei
  void setup()
  analogReference(EXTERNAL);
  einfügen !
  ?????
  ?????
  Der Widerstand zwischen 5V und Aref bereitet mir noch einige Probleme. Anregungen und/oder Berichtigungen sind ausdrücklich erwünscht !!
