# Fritzing sketch A_ref_ohne_Arduino (saved by Fritzing 0.4.3b)
breadboards: 1

parts:
  R1 = Trimmer Potentiometer [package=THT]
  R2 = Trimmer Potentiometer [package=THT]
  C1 = Ceramic Capacitor [package=THT]
  ATMEGA3281 = ATMEGA328
  VCC1 = Battery block 9V
  U1 = Voltage Regulator - 5V [package="TO220 [THT]"]
  D1 = Rectifier Diode [package="300 mil [THT]"]
  U2 = Voltage Regulator - 5V [package="TO220 [THT]"]
  VCC2 = Battery block 9V
  D2 = Rectifier Diode [package="300 mil [THT]"]
  R3 = Resistor [resistance=220 package=THT]

nets:
  GND: R1.leg1, R2.leg1, C1.pin_1, ATMEGA3281.connector7, ATMEGA3281.connector21, VCC1.-, U1.GND, U2.GND, VCC2.-
  N1: R1.wiper, ATMEGA3281.connector22
  N2: R1.leg2, ATMEGA3281.connector6, ATMEGA3281.connector19, U2.output_voltage, D2.anode, R3.Pin_0
  N3: R2.wiper, C1.pin_0, ATMEGA3281.connector20
  N4: R2.leg2, U1.output_voltage, D1.anode, R3.Pin_1
  N5: VCC1.+, U1.input_voltage, D1.cathode
  N6: U2.input_voltage, VCC2.+, D2.cathode

notes:
  Referenz-
  Spannung
  Zu messende
  Spannung
  Bei Verwendung einer externen Referenzspannung unbedingt bei void setup()
  analogReference(EXTERNAL);
  einfügen !
  ????
  ???? Das ist noch ein Problem für mich, der Widerstand zwischen 5V und Aref. Kommentare und/oder Berichtigungen ausdrücklich erwünscht !
