# Fritzing sketch Analog5 (saved by Fritzing 0.4.3b)
breadboards: 1

parts:
  Arduino1 = Arduino
  DI1 = 7-Segment LED Display [package=THT]
  R1 = Resistor [resistance=470 package=THT]
  R2 = Resistor [resistance=470 package=THT]
  R3 = Resistor [resistance=470 package=THT]
  R4 = Resistor [resistance=470 package=THT]
  R5 = Resistor [resistance=470 package=THT]
  R6 = Resistor [resistance=470 package=THT]
  R7 = Resistor [resistance=470 package=THT]
  R8 = Rotary Potentiometer (Large) [package=THT]
  R9 = Resistor [resistance=470 package=THT]

nets:
  N1: Arduino1.D12, R2.Pin_1
  N2: Arduino1.D11, R1.Pin_1
  N3: Arduino1.D10, R7.Pin_1
  N4: Arduino1.D9, R5.Pin_0
  N5: Arduino1.D8, R6.Pin_0
  N6: Arduino1.D7, R4.Pin_0
  N7: Arduino1.D6, R3.Pin_0
  N8: Arduino1.+5V, R8.leg2, R9.Pin_0
  N9: Arduino1.GND, DI1.commAnode#2, R8.leg1
  N10: Arduino1.A0, R8.wiper
  N11: DI1.cathodeE, R6.Pin_1
  N12: DI1.cathodeD, R5.Pin_1
  N13: DI1.cathodeC, R7.Pin_0
  N14: DI1.cathodeDP, R9.Pin_1
  N15: DI1.cathodeB, R1.Pin_0
  N16: DI1.cathodeA, R2.Pin_0
  N17: DI1.cathodeF, R3.Pin_1
  N18: DI1.cathodeG, R4.Pin_1

notes:
  Bei meinem Mercedes 220 Baujahr 1964 musste die Hinterachse gewechslt werden. Da diese eine andere Übersetzung hat, stimmt die Tachoanzeige nicht mehr.
  Die Frequenz des Zündkontakts wird über einen LM2917 in eine Spannung gewandelt. Das Poti in dem oben gezeigten Aufbau simuliert den LM2917.
  Bei 30 km/h zeigt die 7-Segmentanzeige eine 3, bei 50 eine 5, 70 ist 7, 80 zeigt 8, 90 ist 9 und 100 km/h gleich 1. Das gilt natürlich nur für den 4. Gang.
  With my Mercedes 220 built in 1964 had the rear axle change. Since this has a different translation, does not the speedometer.
  The frequency of the ignition contact is converted into a voltage with a LM2917. The pot in the structure shown above simulates the LM2917.
  At 30 km / h shows the 7-segment display shows a 3, at 50 a 5, 70, 7, 80 8, 9 and 90 is 100 km / h equal to 1 This of course only for the 4th Transition.
  Google Translation:
