# Fritzing sketch ArduMeteo (saved by Fritzing 0.6.2b)
breadboards: 1

parts:
  Arduino1 = Arduino
  U4 = mystery part, 3 pins [chip_label=DS18B20 spacing=300mil]
  U5 = mystery part, 3 pins [chip_label=DS18B20 spacing=300mil]
  R4 = Resistor [tolerance=±5% resistance=4.7k package=THT]
  IC6 = IC, DIP package, 4 pins [chip_label=IC spacing=300mil]
  IC7 = IC, DIP package, 4 pins [chip_label=IC spacing=300mil]
  IC8 = IC, DIP package, 4 pins [chip_label=IC spacing=300mil]
  IC9 = IC, DIP package, 4 pins [chip_label=IC spacing=300mil]
  IC10 = IC, DIP package, 4 pins [chip_label=IC spacing=300mil]
  R12 = Resistor [tolerance=±5% resistance=10k package=THT]
  R13 = Resistor [tolerance=±5% resistance=10k package=THT]
  R14 = Resistor [tolerance=±5% resistance=10k package=THT]
  R15 = Resistor [tolerance=±5% resistance=10k package=THT]
  R16 = Resistor [tolerance=±5% resistance=10k package=THT]
  R17 = Resistor [tolerance=±5% resistance=220 package=THT]
  R18 = Resistor [tolerance=±5% resistance=220 package=THT]
  R19 = Resistor [tolerance=±5% resistance=220 package=THT]
  R20 = Resistor [tolerance=±5% resistance=220 package=THT]
  R21 = Resistor [tolerance=±5% resistance=220 package=THT]
  M2 = DC Motor
  U6 = mystery part, 3 pins [chip_label=hall spacing=300mil]

nets:
  N1: Arduino1.D4, U4.pin2, U5.pin2
  N2: Arduino1.D2, U6.pin3
  N3: Arduino1.GND, U4.pin1, U4.pin3, U5.pin1, U5.pin3, IC6.pin1, IC6.pin4, IC7.pin4, IC8.pin4, IC9.pin4, IC10.pin4, R12.Pin_1, R13.Pin_1, R14.Pin_1, R15.Pin_1, R16.Pin_1, U6.pin2
  N4: Arduino1.VIN, M2.pin_2
  N5: Arduino1.A0, M2.pin_1
  N6: Arduino1.A1, IC6.pin2, R12.Pin_0
  N7: Arduino1.A2, IC10.pin2, R13.Pin_0
  N8: Arduino1.A3, IC8.pin2, R15.Pin_0
  N9: Arduino1.A4, IC9.pin2, R14.Pin_0
  N10: Arduino1.A5, IC7.pin2
  N11: R4.Pin_0, R17.Pin_1, R18.Pin_1, R19.Pin_1, R20.Pin_1, R21.Pin_1, U6.pin1
  N12: IC6.pin3, R20.Pin_0
  N13: IC7.pin3, R17.Pin_0
  N14: IC8.pin3, R19.Pin_0
  N15: IC9.pin3, R21.Pin_0
  N16: IC10.pin3, R18.Pin_0
