# Fritzing sketch Arduino-DCCdecoder (saved by Fritzing 0.4.3b)
breadboards: 1

parts:
  LED1 = Red LED - 5mm
  IC1 = IC, DIP package, 8 pins [chip_label=6N137 spacing=300mil]
  R1 = Resistor [resistance=1k package=THT]
  R2 = Resistor [resistance=10k package=THT]
  Arduino1 = Arduino
  J1 = Screw terminal - 2 pins [package=THT]

nets:
  N1: LED1.cathode, IC1.pin2, R1.Pin_1
  N2: LED1.anode, IC1.pin3, J1.pin2
  GND: IC1.pin5, Arduino1.GND
  N3: IC1.pin6, R2.Pin_1, Arduino1.D8
  5V: IC1.pin7, IC1.pin8, R2.Pin_0, Arduino1.+5V
  N4: R1.Pin_0, J1.pin1

notes:
  DCC Track power
  From DCC Track power
  Arduino as a DCC Decoder
