# Fritzing sketch ArduinoISP (saved by Fritzing 0.3.20b)
breadboards: 1

parts:
  R1 = Resistor [resistance=1k package=THT]
  Arduino_ISP = Arduino
  ATMEGA = atmega168 [package="DIP28 [THT]"]
  OSC = Resonator [package=THT]
  RESET = Pushbutton [package="[THT]"]
  R2 = Resistor [resistance=220 package=THT]
  HELLO = green LED - 5mm
  ERROR = Red LED - 5mm
  R3 = Resistor [resistance=220 package=THT]
  R4 = Resistor [resistance=220 package=THT]
  R5 = Resistor [resistance=220 package=THT]
  PROG = yellow LED - 5mm
  PULSE = green LED - 5mm

nets:
  5V: R1.Pin_0, Arduino_ISP.+5V, ATMEGA.Pin_7, ATMEGA.Pin_20
  N1: R1.Pin_1, Arduino_ISP.D10, ATMEGA.Pin_1, RESET.Pin_1, RESET.Pin_2
  GND: Arduino_ISP.GND, ATMEGA.Pin_8, ATMEGA.Pin_22, OSC.GND, RESET.Pin_3, RESET.Pin_4, R2.Pin_0, R3.Pin_1, R4.Pin_1, R5.Pin_1
  N2: Arduino_ISP.D13, ATMEGA.Pin_19
  N3: Arduino_ISP.D12, ATMEGA.Pin_18
  N4: Arduino_ISP.D11, ATMEGA.Pin_17
  N5: Arduino_ISP.D9, PULSE.anode
  N6: Arduino_ISP.D8, ERROR.anode
  N7: Arduino_ISP.D7, PROG.anode
  N8: ATMEGA.Pin_9, OSC.0
  N9: ATMEGA.Pin_10, OSC.pin_1
  N10: ATMEGA.Pin_14, HELLO.anode
  N11: R2.Pin_1, HELLO.cathode
  N12: ERROR.cathode, R4.Pin_0
  N13: R3.Pin_0, PULSE.cathode
  N14: R5.Pin_0, PROG.cathode

notes:
  Using an Arduino as ISP:
  http://arduino.cc/en/Tutorial/ArduinoISP
