# Fritzing sketch ArduinoMAX7219 (saved by Fritzing 0.5.2b)
breadboards: 1

parts:
  Arduino_ISP = Arduino
  IC1 = IC, DIP package, 24 pins [chip_label=IC spacing=300mil]
  J1 = female pin header, 4 pins [form="♀ (female)"]
  R1 = Resistor [resistance=10k package=THT]
  J2 = female pin header, 4 pins [form="♀ (female)"]
  J3 = female pin header, 4 pins [form="♀ (female)"]
  J4 = Piezo Speaker
  LED1 = RGB LED - (4 legs) [package="5 mm [THT]"]
  R2 = Resistor [resistance=220 package=THT]
  LED2 = RGB LED - (4 legs) [package="5 mm [THT]"]
  LED3 = Red LED - 5mm [package="5 mm [THT]"]
  R3 = Resistor [resistance=150 package=THT]
  R4 = Resistor [resistance=100 package=THT]
  LED4 = RGB LED - (4 legs) [package="5 mm [THT]"]
  LED5 = RGB LED - (4 legs) [package="5 mm [THT]"]

nets:
  GND: Arduino_ISP.GND, IC1.pin4, IC1.pin9, J4.pin1, R2.Pin_0
  N1: Arduino_ISP.D13, J4.pin2
  N2: Arduino_ISP.D12, IC1.pin13
  N3: Arduino_ISP.D11, LED2.red_cathode
  N4: Arduino_ISP.D10, LED2.green_cathode
  N5: Arduino_ISP.D9, LED2.blue_cathode
  N6: Arduino_ISP.D8, IC1.pin12
  N7: Arduino_ISP.D7, LED3.cathode
  N8: Arduino_ISP.D6, LED1.blue_cathode
  N9: Arduino_ISP.D5, LED1.green_cathode
  N10: Arduino_ISP.D4, LED1.common_anode, R3.Pin_1, R4.Pin_0, R4.Pin_1, LED4.common_anode, LED5.common_anode
  N11: Arduino_ISP.D3, LED1.red_cathode
  N12: Arduino_ISP.D2, IC1.pin1
  5V: Arduino_ISP.+5V, IC1.pin19, R1.Pin_0
  N13: Arduino_ISP.A0, LED4.red_cathode
  N14: Arduino_ISP.A1, LED5.red_cathode
  N15: Arduino_ISP.A2, LED5.green_cathode
  N16: Arduino_ISP.A3, LED5.blue_cathode
  N17: Arduino_ISP.A4, LED4.green_cathode
  N18: Arduino_ISP.A5, LED4.blue_cathode
  N19: IC1.pin2, J1.pin4
  N20: IC1.pin6, J1.pin3
  N21: IC1.pin7, J1.pin2
  N22: IC1.pin11, J1.pin1
  N23: IC1.pin14, J2.pin1
  N24: IC1.pin15, J2.pin2
  N25: IC1.pin16, J2.pin3
  N26: IC1.pin17, J2.pin4
  N27: IC1.pin18, R1.Pin_1
  N28: IC1.pin20, J3.pin1
  N29: IC1.pin21, J3.pin2
  N30: IC1.pin23, J3.pin3
  N31: IC1.pin24, J3.pin4
  N32: R2.Pin_1, LED2.common_anode
  N33: LED3.anode, R3.Pin_0

notes:
  Using an Arduino as ISP:
  http://arduino.cc/en/Tutorial/ArduinoISP
