# Fritzing sketch Arduino_PC_Fan_RPM (saved by Fritzing 0.3.19b)
breadboards: 1

parts:
  Arduino1 = Arduino
  R1 = Resistor [resistance=10k package=THT]

nets:
  N1: Arduino1.D2, R1.Pin_1
  N2: Arduino1.+5V, R1.Pin_0

notes:
  Yellow wire = Fan RPM signal
  Black Wire = Fan Ground
  Red Wire = Fan Power 12v
  +12v DC
  GND
  **PC Fan RPM via Arduino**
  Schematic by: Charles Gantt
  Code by: Crenn
