# Fritzing sketch Arduino_controlled_2_sensor_temp_display (saved by Fritzing 0.3.19b)

parts:
  Arduino1 = Arduino
  LCD1 = LCD screen
  R1 = Temperature Sensor (Thermistor) [package=THT]
  R2 = Temperature Sensor (Thermistor) [package=THT]
  R3 = Resistor [resistance=220 package=THT]
  R4 = Resistor [resistance=220 package=THT]
  R5 = Trimmer Potentiometer [package=THT]

nets:
  N1: Arduino1.GND, R4.Pin_0
  N2: Arduino1.D12, LCD1.DB7
  N3: Arduino1.D11, LCD1.DB6
  N4: Arduino1.D10, LCD1.DB5
  N5: Arduino1.D9, LCD1.DB4
  N6: Arduino1.D8, LCD1.E
  N7: Arduino1.D7, LCD1.RS
  N8: Arduino1.+5V, R1.pin_1
  N9: Arduino1.A0, R1.pin_0, R3.Pin_1
  N10: Arduino1.A1, R2.pin_0, R4.Pin_1
  N11: LCD1.V0, R5.wiper
