# Fritzing sketch Atmega32LBrokeOut-updated (saved by Fritzing 0.4.3b)
breadboards: 4

parts:
  Atmel's_Atmega32L_Microchip1 = AVR-Atmega32 [package="DIP (Dual Inline)"]
  XTAL1 = Crystal [package=THT]
  R1 = Resistor [resistance=10k package=THT]
  S1 = Pushbutton [package="[THT]"]
  Arduino1 = Arduino
  LED2 = Red LED - 5mm
  LED1 = Blue LED - 5mm
  LED3 = green LED - 5mm
  R2 = Resistor [resistance=220 package=THT]

nets:
  N1: Atmel's_Atmega32L_Microchip1.pin_6, Arduino1.D11
  N2: Atmel's_Atmega32L_Microchip1.pin_7, Arduino1.D12
  N3: Atmel's_Atmega32L_Microchip1.pin_8, Arduino1.D13
  N4: Atmel's_Atmega32L_Microchip1.pin_9, R1.Pin_0, Arduino1.D10
  N5: Atmel's_Atmega32L_Microchip1.pin_10, Atmel's_Atmega32L_Microchip1.pin_30, R1.Pin_1, S1.Pin_2, Arduino1.+5V
  N6: Atmel's_Atmega32L_Microchip1.pin_11, Atmel's_Atmega32L_Microchip1.pin_31, S1.Pin_4, Arduino1.GND, R2.Pin_0
  N7: Atmel's_Atmega32L_Microchip1.pin_12, XTAL1.pin_1
  N8: Atmel's_Atmega32L_Microchip1.pin_13, XTAL1.pin_0
  N9: Arduino1.D9, LED1.anode
  N10: Arduino1.D8, LED2.anode
  N11: Arduino1.D7, LED3.anode
  N12: LED2.cathode, LED1.cathode, LED3.cathode, R2.Pin_1

notes:
  RX/TX Lines / Multipurpose I/O
  AHREF
  Reset
  16mhz Oscillator
  ADC Mutipurpose I/O
  Bi-Directional I/O + JTAG Function Lines
  Multipurpose I/O
  ICSP Programming Lines
  Programming leds:
  Blue: ICSP Heartbeat
  Red: Programming
  Error
  Green: Programming in
  progress

custom parts:
  AVR-Atmega32: Atmel's Atmega32. A beast of an 8 bit microchip to behold! This is not your dad's arduino chip! Also the DIP version of the microchip that is at the helm of the Arduino Mega. For more info, consult the datasheet: http://www.atmel.com/dyn/resources/prod_documents/doc2503.pdf
