# Fritzing sketch Audio-Meter-lm3915 (saved by Fritzing 0.6.5b)
breadboards: 2

parts:
  IC1 = PICAXE-18 [package=THT]
  LED1 = LED - 5mm [color="Green (570nm)" package="5 mm [THT]"]
  LED2 = LED - 5mm [color="Green (570nm)" package="5 mm [THT]"]
  LED3 = LED - 5mm [color="Green (570nm)" package="5 mm [THT]"]
  LED4 = LED - 5mm [color="Green (570nm)" package="5 mm [THT]"]
  LED5 = LED - 5mm [color="Green (570nm)" package="5 mm [THT]"]
  LED6 = LED - 5mm [color="Yellow (595nm)" package="5 mm [THT]"]
  LED7 = LED - 5mm [color="Orange (620nm)" package="5 mm [THT]"]
  LED8 = LED - 5mm [color="Orange (620nm)" package="5 mm [THT]"]
  LED9 = LED - 5mm [color="Red (633nm)" package="5 mm [THT]"]
  LED10 = LED - 5mm [color="Red (633nm)" package="5 mm [THT]"]
  VCC1 = 4 x AAA Battery Mount
  C1 = Electrolytic Capacitor [capacitance=2.2µF voltage=50V package="100 mil [THT, electrolytic]"]
  R1 = Resistor [tolerance=±5% resistance=1k package=THT]
  R2 = Resistor [tolerance=±5% resistance=1M package=THT]
  C2 = Ceramic Capacitor [capacitance=0.1µF package="100 mil [THT, multilayer]"]
  D1 = Rectifier Diode [part_number=1N914 package="300 mil [THT]"]
  R3 = Resistor [tolerance=±5% resistance=1k package=THT]
  C3 = Ceramic Capacitor [capacitance=0.1µF package="100 mil [THT, multilayer]"]
  R5 = Resistor [tolerance=±5% resistance=619k package=THT]
  TRS1 = Stereo Jack (TRS) 3.5mm [package="PG203J [THT]"]
  R6 = Resistor [tolerance=±5% resistance=100k package=THT]
  S1 = Toggle Switch [package=THT]
  Q1 = PNP-Transistor [part_number=2N3906 package="TO92 [THT]"]

nets:
  N1: IC1.In_2, LED1.cathode
  N2: IC1.Serial_Out, IC1.Reset, IC1.Out_2, VCC1.-, C1.+, R1.Pin_1, R2.Pin_1, C2.1, TRS1.Sleeve, R6.Pin_0, Q1.C
  N3: IC1.Serial_In, LED1.anode, LED2.anode, LED3.anode, LED4.anode, LED5.anode, LED6.anode, LED7.anode, LED8.anode, LED9.anode, LED10.anode, VCC1.+, C1.-, R5.Pin_0, S1.COM
  N4: IC1.0V, R2.Pin_0, C2.0, D1.cathode
  N5: IC1.Out_0, IC1.Out_1, R1.Pin_0
  N6: IC1.Out_3, S1.L2
  N7: IC1.Out_4, LED10.cathode
  N8: IC1.Out_5, LED9.cathode
  N9: IC1.Out_6, LED8.cathode
  N10: IC1.Out_7, LED7.cathode
  N11: IC1.+V, LED6.cathode
  N12: IC1.In_6, LED5.cathode
  N13: IC1.In_7, LED4.cathode
  N14: IC1.In_0, LED3.cathode
  N15: IC1.In_1, LED2.cathode
  N16: D1.anode, R5.Pin_1, Q1.E
  N17: R3.Pin_0, Q1.B
  N18: R3.Pin_1, C3.0, R6.Pin_1
  N19: C3.1, TRS1.Ring

notes:
  DOT/BAR
  Audio
  IN
  3V bis 20V
  Part List
  1x LM3915 IC
  2x 0.1uF Ceramic Disk Capacitor
  1x 2.2uF 25V Electrolytic Capacitor
  1x 1N914 Silicon Diode
  1x 2N3906 PNP Transistor
  1x 619K 1/4W Resistor
  2x 1K 1/4W Resistor
  1x 100K 1/4W Resistor
  1x 1M 1/4W Resistor
  10x Standard LED or BarGraph
  L2 L3 L4 L5 L6 L7 L8 L9 L10
  LM3915
  L1 V- V+ RLO SIG RHI VR ADJ MDE
