# Fritzing sketch BODYSUIT-snesors-arduino (saved by Fritzing 0.4.0b)

parts:
  R1 = 10 Ω Resistor [package=THT]
  Part1 = Arduino Diecimila (deprecated) [package=THT]
  J1 = Basic Force Sensing Resistor (FSR) [package=THT]

nets:
  GND: R1.Pin_0, Part1.GND
  N1: R1.Pin_1, Part1.A0, J1.pin_0
  N2: Part1.+5V, J1.pin_1

notes:
  10K Homs risisotr
