# Fritzing sketch Bend_sensor_to_eobody (saved by Fritzing 0.4.2b)
breadboards: 1

parts:
  U1 = LM 358 Dual Op-Amp [package="DIP8 [THT]"]
  R1 = Basic Flex Resistor
  RG = Resistor [resistance=15 package=THT]
  DC_Power1 = DC Power [voltage=5]

nets:
  N1: U1.connector0, RG.Pin_1
  N2: U1.connector1, R1.pin_1, RG.Pin_0
  5V/GND: U1.connector2, R1.Pin_2, DC_Power1.V+, DC_Power1.GND

notes:
  signal (yellow) connected to eobody input
  the issue is VREF and how in this schematic to wire/connect a 5v input to create a -5v reference voltage.
