# Fritzing sketch BinaryChronometer (saved by Fritzing 0.5.2b)

parts:
  LED30 = white LED - 5mm [package="5 mm [THT]"]
  Arduino1 = Arduino
  LED20 = white LED - 5mm [package="5 mm [THT]"]
  LED10 = white LED - 5mm [package="5 mm [THT]"]
  LED00 = white LED - 5mm [package="5 mm [THT]"]
  LED31 = white LED - 5mm [package="5 mm [THT]"]
  LED23 = white LED - 5mm [package="5 mm [THT]"]
  LED12 = white LED - 5mm [package="5 mm [THT]"]
  LED33 = white LED - 5mm [package="5 mm [THT]"]
  LED32 = white LED - 5mm [package="5 mm [THT]"]
  LED22 = white LED - 5mm [package="5 mm [THT]"]
  LED13 = white LED - 5mm [package="5 mm [THT]"]
  LED14 = white LED - 5mm [package="5 mm [THT]"]
  LED25 = white LED - 5mm [package="5 mm [THT]"]
  LED24 = white LED - 5mm [package="5 mm [THT]"]
  LED04 = white LED - 5mm [package="5 mm [THT]"]
  LED35 = white LED - 5mm [package="5 mm [THT]"]
  LED34 = white LED - 5mm [package="5 mm [THT]"]
  LED11 = white LED - 5mm [package="5 mm [THT]"]
  LED21 = white LED - 5mm [package="5 mm [THT]"]
  LED02 = white LED - 5mm [package="5 mm [THT]"]
  R3 = Resistor [resistance=220 package=THT]
  R2 = Resistor [resistance=220 package=THT]
  R1 = Resistor [resistance=220 package=THT]
  R0 = Resistor [resistance=220 package=THT]

nets:
  N1: LED30.cathode, Arduino1.D4, LED20.cathode, LED10.cathode, LED00.cathode
  N2: LED30.anode, LED31.anode, LED33.anode, LED32.anode, LED35.anode, LED34.anode, R3.Pin_1
  N3: Arduino1.D13, R3.Pin_0
  N4: Arduino1.D12, R2.Pin_0
  N5: Arduino1.D11, R1.Pin_0
  N6: Arduino1.D10, R0.Pin_0
  N7: Arduino1.D9, LED25.cathode, LED35.cathode
  N8: Arduino1.D8, LED14.cathode, LED24.cathode, LED04.cathode, LED34.cathode
  N9: Arduino1.D7, LED23.cathode, LED33.cathode, LED13.cathode
  N10: Arduino1.D6, LED12.cathode, LED32.cathode, LED22.cathode, LED02.cathode
  N11: Arduino1.D5, LED31.cathode, LED11.cathode, LED21.cathode
  N12: LED20.anode, LED23.anode, LED22.anode, LED25.anode, LED24.anode, LED21.anode, R2.Pin_1
  N13: LED10.anode, LED12.anode, LED13.anode, LED14.anode, LED11.anode, R1.Pin_1
  N14: LED00.anode, LED04.anode, LED02.anode, R0.Pin_1
