# Fritzing sketch Bluetooth (saved by Fritzing 0.6.2b)
breadboards: 1

parts:
  U1 = Mystery_Part___6_pins
  Power_plug1 = Power plug
  R1 = Resistor [tolerance=±5% resistance=1k package=THT]
  R2 = Resistor [tolerance=±5% resistance=1k package=THT]
  IC1 = IC, DIP package, 40 pins [chip_label=ATmega32L spacing=300mil]
  R3 = Temperature_Sensor__Thermistor [part_number=503at-2]
  R4 = Resistor [tolerance=±5% resistance=44k package=THT]

nets:
  N1: U1.connector0, Power_plug1.VCC, IC1.pin11, IC1.pin31, R4.Pin_0
  N2: U1.connector2, Power_plug1.GND, IC1.pin10, IC1.pin30, IC1.pin32, R3.connector1
  N3: U1.connector3, R1.Pin_0
  N4: U1.connector4, R2.Pin_0
  N5: R1.Pin_1, IC1.pin14
  N6: R2.Pin_1, IC1.pin15
  N7: IC1.pin40, R3.connector0, R4.Pin_1
