# Fritzing sketch CD4051_MUX (saved by Fritzing 0.3.14b)
breadboards: 1

parts:
  LED3 = Red LED - 5mm
  LED1 = Red LED - 5mm
  LED2 = Red LED - 5mm
  LED0 = Red LED - 5mm
  LED7 = Red LED - 5mm
  LED5 = Red LED - 5mm
  LED4 = Red LED - 5mm
  R0 = Resistor [resistance=220 package=THT]
  R1 = Resistor [resistance=220 package=THT]
  R3 = Resistor [resistance=220 package=THT]
  R4 = Resistor [resistance=220 package=THT]
  LED6 = Red LED - 5mm
  CdS0 = Photocell (LDR) [package=THT]
  CdS1 = Photocell (LDR) [package=THT]
  CdS2 = Photocell (LDR) [package=THT]
  CsS3 = Photocell (LDR) [package=THT]
  CdS4 = Photocell (LDR) [package=THT]
  CdS5 = Photocell (LDR) [package=THT]
  CdS6 = Photocell (LDR) [package=THT]
  CdS7 = Photocell (LDR) [package=THT]
  D0 = Signal Diode
  D1 = Signal Diode
  D2 = Signal Diode
  D3 = Signal Diode
  D4 = Signal Diode
  D5 = Signal Diode
  D6 = Signal Diode
  D7 = Signal Diode
  Arduino1 = Arduino
  IC1 = CD4051

nets:
  N1: LED3.connector0, LED2.connector1, IC1.connector13
  N2: LED3.connector1, LED2.connector0, R1.Pin_0
  N3: LED1.connector0, LED0.connector1, IC1.connector12
  N4: LED1.connector1, LED0.connector0, R0.Pin_0
  N5: LED7.connector0, LED6.connector1, IC1.connector11
  N6: LED7.connector1, R4.Pin_0, LED6.connector0
  N7: LED5.connector0, LED4.connector1, IC1.connector14
  N8: LED5.connector1, LED4.connector0, R3.Pin_0
  N9: R0.Pin_1, R1.Pin_1, R3.Pin_1, R4.Pin_1, D0.connector1, D1.connector0, D2.connector1, D3.connector0, D4.connector1, D5.connector0, D6.connector1, D7.connector0, Arduino1.A3
  N10: CdS0.pin_0, D0.connector0
  N11: CdS0.pin_1, CdS1.pin_1, IC1.connector0
  N12: CdS1.pin_0, D1.connector1
  N13: CdS2.pin_0, D2.connector0
  N14: CdS2.pin_1, CsS3.pin_1, IC1.connector4
  N15: CsS3.pin_0, D3.connector1
  N16: CdS4.pin_0, D4.connector0
  N17: CdS4.pin_1, CdS5.pin_1, IC1.connector1
  N18: CdS5.pin_0, D5.connector1
  N19: CdS6.pin_0, D6.connector0
  N20: CdS6.pin_1, CdS7.pin_1, IC1.connector3
  N21: CdS7.pin_0, D7.connector1
  N22: Arduino1.GND, IC1.connector5, IC1.connector6, IC1.connector7
  N23: Arduino1.+5V, IC1.connector15
  N24: Arduino1.A0, IC1.connector10
  N25: Arduino1.A1, IC1.connector9
  N26: Arduino1.A2, IC1.connector8
  N27: Arduino1.A4, IC1.connector2
