# Fritzing sketch CNY70 (saved by Fritzing 0.6.2b)
breadboards: 1

parts:
  Arduino1 = Arduino
  IC1 = IC, DIP package, 4 pins [chip_label=IC spacing=300mil]
  IC2 = IC, DIP package, 4 pins [chip_label=IC spacing=300mil]
  IC3 = IC, DIP package, 4 pins [chip_label=IC spacing=300mil]
  IC4 = IC, DIP package, 4 pins [chip_label=IC spacing=300mil]
  IC5 = IC, DIP package, 4 pins [chip_label=IC spacing=300mil]
  R2 = Resistor [tolerance=±5% resistance=10k package=THT]
  R3 = Resistor [tolerance=±5% resistance=10k package=THT]
  R4 = Resistor [tolerance=±5% resistance=10k package=THT]
  R5 = Resistor [tolerance=±5% resistance=10k package=THT]
  R6 = Resistor [tolerance=±5% resistance=10k package=THT]
  R7 = Resistor [tolerance=±5% resistance=220 package=THT]
  R8 = Resistor [tolerance=±5% resistance=220 package=THT]
  R9 = Resistor [tolerance=±5% resistance=220 package=THT]
  R10 = Resistor [tolerance=±5% resistance=220 package=THT]
  R11 = Resistor [tolerance=±5% resistance=220 package=THT]

nets:
  N1: Arduino1.+5V, IC1.pin1, IC2.pin1, IC3.pin1, IC4.pin1, IC5.pin1, R7.Pin_1, R8.Pin_1, R9.Pin_1, R10.Pin_1, R11.Pin_1
  N2: Arduino1.GND, IC1.pin4, IC2.pin4, IC3.pin4, IC4.pin4, IC5.pin4, R2.Pin_1, R3.Pin_1, R4.Pin_1, R5.Pin_1, R6.Pin_1
  N3: Arduino1.A1, IC1.pin2, R2.Pin_0
  N4: Arduino1.A2, IC2.pin2, R3.Pin_0
  N5: Arduino1.A3, IC3.pin2, R4.Pin_0
  N6: Arduino1.A4, IC4.pin2, R5.Pin_0
  N7: Arduino1.A5, IC5.pin2, R6.Pin_0
  N8: IC1.pin3, R11.Pin_0
  N9: IC2.pin3, R10.Pin_0
  N10: IC3.pin3, R9.Pin_0
  N11: IC4.pin3, R8.Pin_0
  N12: IC5.pin3, R7.Pin_0
