# Fritzing sketch Chaser.fus= (saved by Fritzing 0.5.2b)
breadboards: 1

parts:
  Arduino1 = Arduino
  LED1 = Red LED - 5mm [package="5 mm [THT]"]
  LED1_2 = Red LED - 5mm [package="5 mm [THT]"]
  LED1_3 = Red LED - 5mm [package="5 mm [THT]"]
  LED1_4 = Red LED - 5mm [package="5 mm [THT]"]
  LED1_5 = Red LED - 5mm [package="5 mm [THT]"]
  LED1_6 = Red LED - 5mm [package="5 mm [THT]"]
  LED1_7 = Red LED - 5mm [package="5 mm [THT]"]
  LED1_8 = Red LED - 5mm [package="5 mm [THT]"]
  LED1_9 = Red LED - 5mm [package="5 mm [THT]"]
  LED1_10 = Red LED - 5mm [package="5 mm [THT]"]
  LED1_11 = Red LED - 5mm [package="5 mm [THT]"]
  LED1_12 = Red LED - 5mm [package="5 mm [THT]"]
  VCC1 = Battery block 9V

nets:
  N1: Arduino1.GND, LED1.cathode, LED1_2.cathode, LED1_3.cathode, LED1_4.cathode, LED1_5.cathode, LED1_6.cathode, LED1_7.cathode, LED1_8.cathode, LED1_9.cathode, LED1_10.cathode, LED1_11.cathode, LED1_12.cathode, VCC1.-
  N2: Arduino1.D13, LED1.anode
  N3: Arduino1.D12, LED1_5.anode
  N4: Arduino1.D11, LED1_4.anode
  N5: Arduino1.D10, LED1_3.anode
  N6: Arduino1.D9, LED1_2.anode
  N7: Arduino1.D8, LED1_6.anode
  N8: Arduino1.D7, LED1_7.anode
  N9: Arduino1.D6, LED1_8.anode
  N10: Arduino1.D5, LED1_9.anode
  N11: Arduino1.D4, LED1_10.anode
  N12: Arduino1.D3, LED1_11.anode
  N13: Arduino1.D2, LED1_12.anode
  N14: Arduino1.VIN, VCC1.+
