# Fritzing sketch Coche_Fantastico (saved by Fritzing 0.6.3b)
breadboards: 1

parts:
  R2 = Resistor [tolerance=±5% resistance=220 package=THT]
  R1 = Resistor [tolerance=±5% resistance=220 package=THT]
  R3 = Resistor [tolerance=±5% resistance=220 package=THT]
  R4 = Resistor [tolerance=±5% resistance=220 package=THT]
  R5 = Resistor [tolerance=±5% resistance=220 package=THT]
  R6 = Resistor [tolerance=±5% resistance=220 package=THT]
  R7 = Resistor [tolerance=±5% resistance=220 package=THT]
  R8 = Resistor [tolerance=±5% resistance=220 package=THT]
  R9 = Resistor [tolerance=±5% resistance=220 package=THT]
  R10 = Resistor [tolerance=±5% resistance=220 package=THT]
  KnightRider_1_0 = Arduino
  R11 = Rotary Potentiometer (Small) [maximum_resistance=100kΩ]
  LED1 = LED - 5mm [color="Red (633nm)" package="5 mm [THT]"]
  LED2 = LED - 5mm [color="Red (633nm)" package="5 mm [THT]"]
  LED3 = LED - 5mm [color="Red (633nm)" package="5 mm [THT]"]
  LED4 = LED - 5mm [color="Red (633nm)" package="5 mm [THT]"]
  LED5 = LED - 5mm [color="Red (633nm)" package="5 mm [THT]"]
  LED6 = LED - 5mm [color="Red (633nm)" package="5 mm [THT]"]
  LED7 = LED - 5mm [color="Red (633nm)" package="5 mm [THT]"]
  LED8 = LED - 5mm [color="Red (633nm)" package="5 mm [THT]"]
  LED9 = LED - 5mm [color="Red (633nm)" package="5 mm [THT]"]
  LED10 = LED - 5mm [color="Red (633nm)" package="5 mm [THT]"]

nets:
  N1: R2.Pin_0, LED2.anode
  N2: R2.Pin_1, KnightRider_1_0.D12
  N3: R1.Pin_0, LED1.anode
  N4: R1.Pin_1, KnightRider_1_0.D13
  N5: R3.Pin_0, LED3.anode
  N6: R3.Pin_1, KnightRider_1_0.D11
  N7: R4.Pin_0, LED4.anode
  N8: R4.Pin_1, KnightRider_1_0.D10
  N9: R5.Pin_0, LED5.anode
  N10: R5.Pin_1, KnightRider_1_0.D9
  N11: R6.Pin_0, LED6.anode
  N12: R6.Pin_1, KnightRider_1_0.D8
  N13: R7.Pin_0, LED7.anode
  N14: R7.Pin_1, KnightRider_1_0.D7
  N15: R8.Pin_0, LED8.anode
  N16: R8.Pin_1, KnightRider_1_0.D6
  N17: R9.Pin_0, LED9.anode
  N18: R9.Pin_1, KnightRider_1_0.D5
  N19: R10.Pin_0, LED10.anode
  N20: R10.Pin_1, KnightRider_1_0.D4
  N21: KnightRider_1_0.+5V, R11.leg2
  N22: KnightRider_1_0.GND, R11.leg1, LED1.cathode, LED2.cathode, LED3.cathode, LED4.cathode, LED5.cathode, LED6.cathode, LED7.cathode, LED8.cathode, LED9.cathode, LED10.cathode
  N23: KnightRider_1_0.A0, R11.wiper
