# Fritzing sketch CountDownSwitch (saved by Fritzing 0.4.3b)
breadboards: 1

parts:
  U1000 = PkS-01
  S1111 = Pushbutton [package="[THT]"]
  S1112 = Pushbutton [package="[THT]"]
  R1121 = Resistor [resistance=220 package=THT]
  R1221 = Resistor [resistance=220 package=THT]
  VCC1 = Battery block 9V
  Side1 = Paper_A3_Horizontal
  LED1113 = Red LED-R - 3mm [package="T1.75 (3mm)"]
  LED1114 = Red LED-R - 3mm [package="T1.75 (3mm)"]
  LED1115 = Yellow LED-R - 3mm [package="T1.75 (3mm)"]
  LED1116 = Yellow LED-R - 3mm [package="T1.75 (3mm)"]
  LED1117 = Yellow LED-R - 3mm [package="T1.75 (3mm)"]
  LED1118 = Yellow LED-R - 3mm [package="T1.75 (3mm)"]
  LED1119 = Green LED-R - 3mm [package="T1.75 (3mm)"]
  LED1120 = Green LED-R - 3mm [package="T1.75 (3mm)"]
  LED1105 = Red LED-R - 3mm [package="T1.75 (3mm)"]
  LED1106 = Green LED-R - 3mm [package="T1.75 (3mm)"]

nets:
  N1: U1000.RA0, LED1105.anode
  N2: U1000.RA1, LED1106.anode
  N3: U1000.RB4, S1111.Pin_1, S1111.Pin_2, R1221.Pin_1
  N4: U1000.RB6, S1112.Pin_1, S1112.Pin_2, R1121.Pin_1
  N5: U1000.RC0, LED1113.anode
  N6: U1000.RC1, LED1114.anode
  N7: U1000.RC2, LED1115.anode
  N8: U1000.RC3, LED1116.anode
  N9: U1000.RC4, LED1117.anode
  N10: U1000.RC5, LED1118.anode
  N11: U1000.RC6, LED1119.anode
  N12: U1000.RC7, LED1120.anode
  N13: U1000.5V/1A, R1121.Pin_0, R1221.Pin_0
  N14: U1000.GND, S1111.Pin_3, S1111.Pin_4, S1112.Pin_3, S1112.Pin_4, VCC1.-, Side1.Project, LED1113.cathode, LED1114.cathode, LED1115.cathode, LED1116.cathode, LED1117.cathode, LED1118.cathode, LED1119.cathode, LED1120.cathode, LED1105.cathode, LED1106.cathode
  N15: U1000.VIN, VCC1.+

notes:
  On/Off Count Down Switch
  Reference Project of PROFESSIONALkitStamp
  mjf / 19.10.2010
  1/1
  05.09.2009
  On
  Off
  switching output
  Inverted
  switching output

custom parts:
  PkS-01: The PROFESSIONALkitStamp serves as the brains inside of electronics projects and applications that require a programmable microcontroller. It is able to control and monitor timers, keypads, motors, sensors, switches, relays, lights, and more. Programming is performed in MICHROCHIP(TM)- ASSEMBLER or C-Language with MPLAB IDE (TM) an easy-to-learn developing suite. Programmer is connected over a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
  Paper_A3_Horizontal: Paper A3 Vertical
  Red LED-R - 3mm: A generic red LED (~1.8V)
  Yellow LED-R - 3mm: A generic red LED (~1.8V)
  Green LED-R - 3mm: A generic red LED (~1.8V)
