# Fritzing sketch DC+Nunchuck (saved by Fritzing 0.4.3b)
breadboards: 1

parts:
  Arduino1 = Arduino
  IC1 = H-Bridge [package=THT]
  Motor_1 = DC Motor
  Motor_2 = DC Motor
  VCC_12_volts = obsolete Battery

nets:
  N1: Arduino1.D10, IC1.1_2EN
  N2: Arduino1.D9, IC1.3_4EN
  N3: Arduino1.D7, IC1.4A
  N4: Arduino1.D6, IC1.3A
  N5: Arduino1.D4, IC1.2A
  N6: Arduino1.D3, IC1.1A
  N7: Arduino1.+5V, IC1.VCC1
  GND: Arduino1.GND, IC1.GND1, IC1.GND2, IC1.GND3, IC1.GND4, VCC_12_volts.-
  N8: IC1.1Y, Motor_2.pin_1
  N9: IC1.2Y, Motor_2.pin_2
  N10: IC1.VCC2, VCC_12_volts.+
  N11: IC1.3Y, Motor_1.pin_2
  N12: IC1.4Y, Motor_1.pin_1

notes:
  SDA
  PWR
  GND
  SCL
