# Fritzing sketch DIY-IRChecker (saved by Fritzing 0.6.4b)
breadboards: 1

parts:
  LED1 = LED - 5mm [color="Red (633nm)" package="5 mm [THT]"]
  VCC1 = Battery block 9V
  R1 = Resistor [tolerance=±5% resistance=330 package=THT]
  LED2 = LED - 5mm [color="White (8000K)" package="5 mm [THT]"]

nets:
  N1: LED1.cathode, VCC1.-
  N2: LED1.anode, R1.Pin_0
  N3: VCC1.+, LED2.cathode
  N4: R1.Pin_1, LED2.anode
