# Fritzing sketch DS1307_SHIELD_v1 (saved by Fritzing 0.6.5b)
breadboards: 1

parts:
  IC_DS1307 = DS1307 [package=THT]
  Crystal = Crystal [frequency=0pMHz part_number="Crystal 32,768 KHz" package=THT]
  CR2032_-_3V_Battery = LilyPad Coin Cell Battery Holder
  R1 = Resistor [tolerance=±5% resistance=1k package=THT]
  R2 = Resistor [tolerance=±5% resistance=1k package=THT]
  PWR = male pin header, 2 pins [form="♂ (male)" part_number=PWR]
  Arduino1 = Arduino

nets:
  N1: IC_DS1307.X1_-_Crystal, Crystal.pin_0
  N2: IC_DS1307.X2_-_Crystal, Crystal.pin_1
  N3: IC_DS1307.Vbat_-_Backup_Supply, PWR.pin1
  N4: IC_DS1307.0V, CR2032_-_3V_Battery.-, Arduino1.GND
  N5: IC_DS1307.SDA_-_I2C_Data, R1.Pin_1, Arduino1.A4
  N6: IC_DS1307.SCL_-_I2C_Clock, R2.Pin_0, Arduino1.A5
  N7: IC_DS1307.+V, R1.Pin_0, R2.Pin_1, Arduino1.+5V
  N8: CR2032_-_3V_Battery.+, PWR.pin2

notes:
  RTC Shield v1.0
  Crystal: 32. 768 Khz
  1K Ohm Resistors
  Backup Battery CR2032 ( >8 years)
