# Fritzing sketch DS1337 (saved by Fritzing 0.4.1b)
breadboards: 1

parts:
  U1 = 555 Timer [package="DIP8 [THT]"]
  Arduino1 = Arduino
  R1 = Resistor [resistance=10k package=THT]
  R1_2 = Resistor [resistance=10k package=THT]
  R1_3 = Resistor [resistance=10k package=THT]
  R1_4 = Resistor [resistance=10k package=THT]
  XTAL1 = Crystal [package=THT]
  VCC1 = obsolete Battery
  D1 = Rectifier Diode [package="300 mil [THT]"]
  D1_2 = Rectifier Diode [package="300 mil [THT]"]
  C1 = Ceramic Capacitor [package=THT]

nets:
  N1: U1.Ground, XTAL1.pin_1
  N2: U1.Trigger, XTAL1.pin_0
  N3: U1.Output, Arduino1.D2, R1.Pin_0
  N4: U1.Reset, Arduino1.GND, VCC1.-, C1.pin_1
  N5: U1.Control_Voltage, Arduino1.A4, R1_2.Pin_1
  N6: U1.Threshold, Arduino1.A5, R1_3.Pin_1
  N7: U1.Discharge, Arduino1.D3, R1_4.Pin_1
  N8: U1.Vcc_Supply_Voltage, R1.Pin_1, R1_2.Pin_0, R1_3.Pin_0, R1_4.Pin_0, D1.cathode, D1_2.cathode, C1.pin_0
  N9: Arduino1.3V3, D1_2.anode
  N10: VCC1.+, D1.anode
