# Fritzing sketch Damnsmallduino (saved by Fritzing 0.5.2b)
breadboards: 1

parts:
  U1 = atmega168 [package="DIP28 [THT]"]
  R1 = Resistor [resistance=220 package=THT]
  XTAL1 = Crystal [package=THT]
  C1 = Ceramic Capacitor [capacitance=22µF rated_voltage=35V package="100 mil [THT, multilayer]"]
  C2 = Ceramic Capacitor [capacitance=22µF rated_voltage=35V package="200 mil [THT, multilayer]"]
  J1 = Screw terminal - 2 pins [package=THT]
  J2 = female pin header, 14 pins [form="♀ (female)"]
  J3 = female pin header, 14 pins [form="♀ (female)"]

nets:
  N1: U1.Pin_1, R1.Pin_0, J3.pin1
  N2: U1.Pin_2, J3.pin2
  N3: U1.Pin_3, J3.pin3
  N4: U1.Pin_4, J3.pin4
  N5: U1.Pin_5, J3.pin5
  N6: U1.Pin_6, J3.pin6
  N7: U1.Pin_7, U1.Pin_20, R1.Pin_1, J1.pin2, J2.pin9, J3.pin7
  N8: U1.Pin_8, U1.Pin_22, C1.0, C2.1, J1.pin1, J2.pin7, J3.pin8
  N9: U1.Pin_9, XTAL1.pin_1, C2.0, J3.pin9
  N10: U1.Pin_10, XTAL1.pin_0, C1.1, J3.pin10
  N11: U1.Pin_11, J3.pin11
  N12: U1.Pin_12, J3.pin12
  N13: U1.Pin_13, J3.pin13
  N14: U1.Pin_14, J3.pin14
  N15: U1.Pin_15, J2.pin14
  N16: U1.Pin_16, J2.pin13
  N17: U1.Pin_17, J2.pin12
  N18: U1.Pin_18, J2.pin11
  N19: U1.Pin_19, J2.pin10
  N20: U1.Pin_21, J2.pin8
  N21: U1.Pin_23, J2.pin6
  N22: U1.Pin_24, J2.pin5
  N23: U1.Pin_25, J2.pin4
  N24: U1.Pin_26, J2.pin3
  N25: U1.Pin_27, J2.pin2
  N26: U1.Pin_28, J2.pin1

notes:
  DamnSmallDuino
