# Fritzing sketch DrawBotX (saved by Fritzing 0.6.2b)

parts:
  Arduino1 = Arduino
  J1 = Basic Servo
  J2 = Basic Servo

nets:
  N1: Arduino1.D10, J1.pulse
  N2: Arduino1.D9, J2.pulse
  VCC: Arduino1.+5V, J1.vcc, J2.vcc
  GND: Arduino1.GND, J1.gnd, J2.gnd
