# Fritzing sketch EggTimer (saved by Fritzing 0.3.16b)
breadboards: 1

parts:
  Arduino1 = Arduino
  J2 = female pin header, 2 pins [form="♀ (female)"]
  J3 = Basic Servo
  S20 = Pushbutton [package=THT]
  SPKR30 = Loudspeaker
  S10 = Pushbutton [package=THT]
  R10 = Resistor [resistance=10k package=THT]
  R20 = Resistor [resistance=10k package=THT]
  R30 = Resistor [resistance=220 package=THT]
  LED2 = yellow LED - 5mm
  LED3 = green LED - 5mm
  LED1 = Red LED - 5mm
  R1 = Resistor [resistance=220 package=THT]
  R2 = Resistor [resistance=220 package=THT]
  R3 = Resistor [resistance=220 package=THT]
  R4 = Rotary Potentiometer (Small)
  Side1 = Paper_A3_Vertical  # not connected

nets:
  GND: Arduino1.GND, J2.pin1, J3.gnd, S20.leg0, SPKR30.pin1, S10.leg0, R1.Pin_0, R2.Pin_0, R3.Pin_0, R4.leg2
  N1: Arduino1.D13, LED3.anode
  N2: Arduino1.D12, LED2.anode
  N3: Arduino1.D11, LED1.anode
  N4: Arduino1.D9, J3.pulse
  N5: Arduino1.D8, R30.Pin_1
  N6: Arduino1.D3, S20.leg1, R20.Pin_1
  N7: Arduino1.D2, S10.leg1, R10.Pin_1
  +5V: Arduino1.+5V, J3.vcc, R10.Pin_0, R20.Pin_0, R4.leg1
  N8: Arduino1.VIN, J2.pin2
  N9: Arduino1.A0, R4.wiper
  N10: SPKR30.pin2, R30.Pin_0
  N11: LED2.cathode, R2.Pin_1
  N12: LED3.cathode, R3.Pin_1
  N13: LED1.cathode, R1.Pin_1

notes:
  Egg Timer
  Display minutes with servo
  Michael J. / 02.04.2010
  13.03.2010
  Here you can set the time
  with the poti (variable resistor).
  Servo displays the Time
  you've set.
  And it shows the estimated time
  With start / Stop button (left) you can start and pause the time you've set. Yellow LED indicates pause, green LED goes off.
  Also you can stop the alarm sound and the red LED by holding the button.
  With reset button (right) you can reset the time.
  Also you can stop the alarm- sound and the red LED by holding the button.
  Power connector

custom parts:
  Paper_A3_Vertical: Paper A3 Vertical
