# Fritzing sketch Eier-Timer (saved by Fritzing 0.5.2b)
breadboards: 1

parts:
  Arduino1 = Arduino
  S1 = Pushbutton [package=THT]
  LED1 = Red LED - 5mm [package="5 mm [THT]"]
  S1_2 = Pushbutton [package=THT]
  R1 = Rotary Potentiometer (Small)
  J1 = Basic Servo
  J2 = Piezo Speaker
  LED3 = green LED - 5mm [package="5 mm [THT]"]
  LED2 = yellow LED - 5mm [package="5 mm [THT]"]
  R2 = Resistor [resistance=220 package=THT]
  R2_2 = Resistor [resistance=220 package=THT]
  R2_3 = Resistor [resistance=220 package=THT]
  R2_4 = Resistor [resistance=220 package=THT]
  R2_5 = Resistor [resistance=220 package=THT]

nets:
  GND: Arduino1.GND, LED1.cathode, R1.leg1, J1.gnd, J2.pin1, LED3.cathode, LED2.cathode, R2.Pin_1, R2_2.Pin_1
  N1: Arduino1.D12, S1_2.leg0, R2_2.Pin_0
  N2: Arduino1.D9, J1.pulse
  N3: Arduino1.D7, R2_3.Pin_1
  N4: Arduino1.D6, R2_4.Pin_1
  N5: Arduino1.D5, R2_5.Pin_1
  N6: Arduino1.D4, S1.leg0, R2.Pin_0
  N7: Arduino1.D3, J2.pin2
  +5V: Arduino1.+5V, S1.leg1, S1_2.leg1, R1.leg2, J1.vcc
  N8: Arduino1.A0, R1.wiper
  N9: LED1.anode, R2_5.Pin_0
  N10: LED3.anode, R2_3.Pin_0
  N11: LED2.anode, R2_4.Pin_0

notes:
  Start/Stopp
  Zurücksetzen
