# Fritzing sketch Etch_a_stekch_shield (saved by Fritzing 0.4.3b)
breadboards: 1

parts:
  Arduino1 = Arduino
  R1 = Rotary Potentiometer (Small)
  R2 = Rotary Potentiometer (Large) [package=THT]
  S2 = Pushbutton [package=THT]
  R3 = Resistor [resistance=100k package=THT]
  J1 = female pin header, 2 pins [form="♀ (female)"]
  R4 = Resistor [resistance=1k package=THT]
  R5 = Resistor [resistance=470 package=THT]

nets:
  GND: Arduino1.GND, R1.leg1, R2.leg1, R3.Pin_1, J1.pin2
  N1: Arduino1.D9, R4.Pin_1
  N2: Arduino1.D7, R5.Pin_1
  N3: Arduino1.D5, S2.leg1, R3.Pin_0
  N4: Arduino1.+5V, R1.leg2, R2.leg2, S2.leg0
  N5: Arduino1.A0, R1.wiper
  N6: Arduino1.A1, R2.wiper
  N7: J1.pin1, R4.Pin_0, R5.Pin_0

notes:
  R1, R2 -100K
  R3 -100K
  R4- 1K
  R5 -480R
  J1-RCA Jack
  S2- PushButton
  Need TVOut library
