# Fritzing sketch FASCU11a (saved by Fritzing 0.4.3b)
breadboards: 1

parts:
  J1 = Basic Servo
  R3 = Rotary Potentiometer (Large) [package=THT]
  Arduino2 = Arduino
  LED3 = Blue LED - 5mm
  R1 = Rotary Potentiometer (Large) [package=THT]
  R2 = Rotary Potentiometer (Large) [package=THT]
  LED4 = yellow LED - 5mm
  LED2 = green LED - 5mm
  S1 = Pushbutton [package="[THT]"]
  S2 = Pushbutton [package="[THT]"]
  R4 = Slide Potentiometer
  LED1 = Red LED - 5mm
  S3 = Pushbutton [package="[THT]"]

nets:
  GND: J1.gnd, R3.leg2, Arduino2.GND, LED3.cathode, R1.leg2, R2.leg2, LED4.cathode, LED2.cathode, S2.Pin_3, S2.Pin_4, R4.leg1, LED1.cathode
  VCC: J1.vcc, R3.leg1, Arduino2.+5V, R1.leg1, R2.leg1, S1.Pin_3, S1.Pin_4, R4.leg2, S3.Pin_3, S3.Pin_4
  N1: J1.pulse, Arduino2.D9
  N2: R3.wiper, Arduino2.A2
  N3: Arduino2.D13, LED1.anode
  N4: Arduino2.D12, LED2.anode
  N5: Arduino2.D11, LED3.anode
  N6: Arduino2.D10, LED4.anode
  N7: Arduino2.D8, S1.Pin_1, S1.Pin_2
  N8: Arduino2.D5, S2.Pin_1, S2.Pin_2
  N9: Arduino2.D2, S3.Pin_1, S3.Pin_2
  N10: Arduino2.A0, R1.wiper
  N11: Arduino2.A1, R2.wiper
  N12: Arduino2.A3, R4.wiper
