# Fritzing sketch FLASHDumper (saved by Fritzing 0.3.10b)
breadboards: 1

parts:
  74HC5951 = 74HC595
  74HC5952 = 74HC595
  Part1 = Arduino Nano v2.3
  IC1 = IC, DIP package, 8 pins [chip_label=IC]
  IC2 = IC, DIP package, 8 pins [chip_label=IC]
  IC3 = IC, DIP package, 8 pins [chip_label=IC]
  M27C1001 = IC, DIP package, 8 pins [chip_label=IC]

nets:
  N1: 74HC5951.connector0, 74HC5952.connector0, Part1.D9
  N2: 74HC5951.connector1, Part1.D10
  N3: 74HC5951.connector2, 74HC5952.connector2, Part1.D11
  N4: 74HC5951.connector3, IC1.pin3
  N5: 74HC5951.connector4, IC1.pin6
  N6: 74HC5951.connector5, IC1.pin5
  N7: 74HC5951.connector6, IC1.pin4
  N8: 74HC5951.connector7, 74HC5952.connector7, Part1.GND, IC3.pin6, IC3.pin8, M27C1001.pin4
  N9: 74HC5951.connector9, 74HC5952.connector1
  N10: 74HC5951.connector10, IC2.pin7
  N11: 74HC5951.connector11, IC2.pin6
  N12: 74HC5951.connector12, IC3.pin7
  N13: 74HC5951.connector13, IC2.pin5
  N14: 74HC5951.connector14, 74HC5951.connector15, 74HC5952.connector14, 74HC5952.connector15, Part1.+5V, IC1.pin1, IC1.pin8
  N15: 74HC5952.connector3, IC2.pin1
  N16: 74HC5952.connector4, IC2.pin2
  N17: 74HC5952.connector5, IC2.pin3
  N18: 74HC5952.connector6, IC2.pin4
  N19: 74HC5952.connector10, IC3.pin4
  N20: 74HC5952.connector11, IC3.pin3
  N21: 74HC5952.connector12, IC3.pin2
  N22: 74HC5952.connector13, IC3.pin1
  N23: Part1.D2, M27C1001.pin1
  N24: Part1.D3, M27C1001.pin2
  N25: Part1.D4, M27C1001.pin3
  N26: Part1.D5, M27C1001.pin5
  N27: Part1.D6, M27C1001.pin6
  N28: Part1.D7, M27C1001.pin7
  N29: Part1.D8, M27C1001.pin8
  N30: Part1.D12, IC1.pin2
  N31: Part1.D13, IC3.pin5

notes:
  Outputs (green):
  D11: Strobe
  D10: Data
  D09: Clock
  D12: Data17thBit
  (address is 17 bits, our shift reg's deal with the lowest 16 and then D12 deals with the higest 17th)
  Inputs/Data In (white)
  Shiftreg patch (white)
  Address shiftreg to Flash (orangeh
  The 4f IC's are actually one
  M27C1001 flash chip. I will update and add the proper part in the next revision
  This chip is odd in the method of writing. First, you put the chip under UV which sets all bits to '1'. After this you can only selectively record 0's, you can never write 1's.
  IMPORTANT:
  I'm using HCF4094 shiftreg's and NOT the 74HC595 shown here. Wiring is just slightly different and I will update and add the parts in the next revision)
