# Fritzing sketch FritzTrommler (saved by Fritzing 0.3.15b)
breadboards: 1

parts:
  Arduino1 = Arduino
  BPM = Red LED - 5mm
  BPM_2 = Rotary Potentiometer (Large) [package=THT]
  Beat_Out = Relay [package=THT]
  Scratch_In = Photocell (LDR) [package=THT]
  R3 = Resistor [resistance=10k package=THT]
  Scratch_Out = Basic Servo
  Beat_In = Pushbutton [package=THT]
  Recording = Pushbutton [package=THT]

nets:
  GND: Arduino1.GND, BPM.cathode, BPM_2.leg2, Beat_Out.COIL2, R3.Pin_1, Scratch_Out.gnd, Beat_In.leg0, Recording.leg0
  N1: Arduino1.D13, BPM.anode
  N2: Arduino1.D12, Beat_Out.COIL1
  N3: Arduino1.D9, Scratch_Out.pulse
  N4: Arduino1.D5, Beat_In.leg1
  N5: Arduino1.D4, Recording.leg1
  5V: Arduino1.+5V, BPM_2.leg1, Scratch_In.pin_1, Scratch_Out.vcc
  N6: Arduino1.A0, Scratch_In.pin_0, R3.Pin_0
  N7: Arduino1.A1, BPM_2.wiper
  N8: Beat_Out.C1, Beat_Out.C2

notes:
  FritzTrommler
