# Fritzing sketch Full_Color_LED (saved by Fritzing 0.6.3b)
breadboards: 1

parts:
  Arduino1 = Arduino Mega
  LED1 = RGB LED (com. cathode, rbg) [package="5 mm [THT]"]
  R1 = Resistor [tolerance=±5% resistance=220 package=THT]

nets:
  N1: Arduino1.D4, LED1.green_anode
  N2: Arduino1.D3, LED1.blue_anode
  N3: Arduino1.D2, LED1.red_anode
  N4: Arduino1.+5V, R1.Pin_1
  N5: LED1.common_cathode, R1.Pin_0
