# Fritzing sketch GP2D150A-01 (saved by Fritzing 0.5.2b)
breadboards: 1

parts:
  Arduino1 = Arduino
  J1 = Infrared Proximity Sensor
  R1 = Resistor [resistance=10k package=THT]
  R2 = Resistor [resistance=1k package=THT]
  R3 = Resistor [resistance=1k package=THT]
  R4 = Resistor [resistance=220 package=THT]
  LED1 = Red LED - 5mm [package="5 mm [THT]"]

nets:
  N1: Arduino1.D7, R3.Pin_0
  +5V: Arduino1.+5V, J1.Vcc
  GND: Arduino1.GND, J1.GND, LED1.cathode
  N2: J1.Vout, R1.Pin_1, R4.Pin_1
  N3: R1.Pin_0, R2.Pin_1
  N4: R2.Pin_0, R3.Pin_1
  N5: R4.Pin_0, LED1.anode
