# Fritzing sketch GVEP102 (saved by Fritzing 0.6.2b)
breadboards: 1

parts:
  7805 = voltage regulator lying
  78051 = voltage regulator lying
  +)-_7_5_DC = Power plug
  104 = Ceramic Capacitor [capacitance=100nF package="100 mil [THT, multilayer]"]
  1n4001 = Rectifier Diode [part_number=1N4001 package="300 mil [THT]"]
  S2 = SPDT-tact-small
  S3 = SPDT-tact-small
  S6 = SPDT-tact-small
  10k = Big Potentiometer
  10k_2 = Big Potentiometer
  10k_3 = Big Potentiometer
  1 = header hole
  5V = header hole
  gnd = header hole
  5V_2 = header hole
  gnd_2 = header hole
  33k = Resistor [tolerance=±5% resistance=220 package=THT]
  22k = Resistor [tolerance=±5% resistance=220 package=THT]
  33k_2 = Resistor [tolerance=±5% resistance=220 package=THT]
  22k_2 = Resistor [tolerance=±5% resistance=220 package=THT]
  33k_3 = Resistor [tolerance=±5% resistance=220 package=THT]
  22k_3 = Resistor [tolerance=±5% resistance=220 package=THT]
  1_5k = Resistor [tolerance=±5% resistance=220 package=THT]
  R = header hole
  G = header hole
  1_5k_2 = Resistor [tolerance=±5% resistance=220 package=THT]
  1_5k_3 = Resistor [tolerance=±5% resistance=220 package=THT]
  2 = header hole
  3 = header hole
  IC1 = IC, DIP package, 12 pins [chip_label=IC spacing=300mil]
  4 = header hole
  5 = header hole
  6 = header hole
  7 = header hole
  8 = header hole
  9 = header hole
  1k = Resistor [tolerance=±5% resistance=220 package=THT]
  220 = Resistor [tolerance=±5% resistance=220 package=THT]
  220_2 = Resistor [tolerance=±5% resistance=220 package=THT]
  220_3 = Resistor [tolerance=±5% resistance=220 package=THT]
  220_4 = Resistor [tolerance=±5% resistance=220 package=THT]
  1k1 = Resistor [tolerance=±5% resistance=220 package=THT]
  220_5 = Resistor [tolerance=±5% resistance=220 package=THT]
  220_6 = Resistor [tolerance=±5% resistance=220 package=THT]
  1k2 = Resistor [tolerance=±5% resistance=220 package=THT]
  gnd1 = header hole
  5V1 = header hole
  B = header hole
  220_7 = Resistor [tolerance=±5% resistance=220 package=THT]
  220_8 = Resistor [tolerance=±5% resistance=220 package=THT]
  220_9 = Resistor [tolerance=±5% resistance=220 package=THT]
  PG = header hole
  PB = header hole
  PR = header hole
  220_10 = Resistor [tolerance=±5% resistance=220 package=THT]
  220_11 = Resistor [tolerance=±5% resistance=220 package=THT]
  220_12 = Resistor [tolerance=±5% resistance=220 package=THT]
  104_2 = Ceramic Capacitor [capacitance=100nF package="100 mil [THT, multilayer]"]
  104_3 = Ceramic Capacitor [capacitance=100nF package="100 mil [THT, multilayer]"]
  104_4 = Ceramic Capacitor [capacitance=100nF package="100 mil [THT, multilayer]"]
  23 = header hole
  25 = header hole
  27 = header hole
  28 = header hole
  29 = header hole
  30 = header hole
  31 = header hole
  32 = header hole
  33 = header hole
  35 = header hole
  37 = header hole
  38 = header hole
  39 = header hole
  40 = header hole
  41 = header hole
  42 = header hole
  43 = header hole
  45 = header hole
  47 = header hole
  48 = header hole
  49 = header hole
  50 = header hole
  51 = header hole
  52 = header hole
  53 = header hole
  54 = header hole
  55 = header hole
  56 = header hole
  57 = header hole
  58 = header hole
  59 = header hole
  60 = header hole
  61 = header hole
  62 = header hole
  63 = header hole
  64 = header hole
  65 = header hole
  66 = header hole
  67 = header hole
  68 = header hole
  69 = header hole
  70 = header hole
  71 = header hole
  72 = header hole
  S7 = Pushbutton [package="[THT]"]
  73 = header hole
  74 = header hole
  75 = header hole
  76 = header hole
  77 = header hole  # not connected
  78 = header hole
  79 = header hole  # not connected
  80 = header hole  # not connected
  81 = header hole  # not connected
  82 = header hole  # not connected
  83 = header hole  # not connected
  84 = header hole  # not connected
  85 = header hole  # not connected

nets:
  N1: 7805.input, 78051.input, +)-_7_5_DC.pin_1, 104.1, 1n4001.cathode
  N2: 7805.ground, 78051.ground, +)-_7_5_DC.pin_2, +)-_7_5_DC.pin_3, 104.0, 1n4001.anode, gnd.pin_0, gnd_2.pin_0, 22k.Pin_0, 22k_2.Pin_0, 22k_3.Pin_0, 220.Pin_1, 220_3.Pin_1, 220_5.Pin_1, gnd1.pin_0
  N3: 7805.output, 5V.pin_0
  N4: 78051.output, 5V_2.pin_0, 33k.Pin_0, 33k_2.Pin_0, 33k_3.Pin_0, 5V1.pin_0
  N5: S2.no_name_yet#1, 4.pin_0
  N6: S2.no_name_yet#2, 1k.Pin_1
  N7: S2.no_name_yet#3, 5.pin_0
  N8: S3.no_name_yet#1, 6.pin_0
  N9: S3.no_name_yet#2, 1k1.Pin_1
  N10: S3.no_name_yet#3, 7.pin_0
  N11: S6.no_name_yet#1, 8.pin_0
  N12: S6.no_name_yet#2, 1k2.Pin_1
  N13: S6.no_name_yet#3, 9.pin_0
  N14: 10k.leg2, 33k.Pin_1
  N15: 10k.no_name_yet#3, 1_5k.Pin_1
  N16: 10k.no_name_yet#4, 22k_3.Pin_1
  N17: 10k_2.leg2, 33k_2.Pin_1
  N18: 10k_2.no_name_yet#3, 1_5k_2.Pin_1
  N19: 10k_2.no_name_yet#4, 22k.Pin_1
  N20: 10k_3.leg2, 33k_3.Pin_1
  N21: 10k_3.no_name_yet#3, 1_5k_3.Pin_1
  N22: 10k_3.no_name_yet#4, 22k_2.Pin_1
  N23: 1.pin_0, 1_5k.Pin_0, 104_2.0
  N24: R.pin_0, 220_7.Pin_0, 220_12.Pin_0
  N25: G.pin_0, 220_8.Pin_0, 220_11.Pin_0
  N26: 1_5k_2.Pin_0, 2.pin_0, 104_4.0
  N27: 1_5k_3.Pin_0, 3.pin_0, 104_3.0
  N28: IC1.pin1, 220_2.Pin_0
  N29: IC1.pin2, 220_4.Pin_0
  N30: IC1.pin3, 220_6.Pin_1
  N31: IC1.pin4, 220_9.Pin_1
  N32: IC1.pin5, 220_8.Pin_1
  N33: IC1.pin6, 220_7.Pin_1
  N34: IC1.pin7, IC1.pin12, PR.pin_0
  N35: IC1.pin8, IC1.pin11, PG.pin_0
  N36: IC1.pin9, IC1.pin10, PB.pin_0
  N37: 1k.Pin_0, 220.Pin_0, 220_2.Pin_1
  N38: 220_3.Pin_0, 220_4.Pin_1, 1k1.Pin_0
  N39: 220_5.Pin_0, 220_6.Pin_0, 1k2.Pin_0
  N40: B.pin_0, 220_9.Pin_0, 220_10.Pin_0
  N41: 220_10.Pin_1, 104_3.1
  N42: 220_11.Pin_1, 104_4.1
  N43: 220_12.Pin_1, 104_2.1
  N44: 23.pin_0, 33.pin_0, 43.pin_0, 70.pin_0
  N45: 25.pin_0, 35.pin_0, 45.pin_0, 65.pin_0
  N46: 27.pin_0, 37.pin_0, 47.pin_0, 71.pin_0
  N47: 28.pin_0, 38.pin_0, 48.pin_0, 69.pin_0
  N48: 29.pin_0, 39.pin_0, 49.pin_0, 66.pin_0
  N49: 30.pin_0, 40.pin_0, 50.pin_0, 64.pin_0
  N50: 31.pin_0, 41.pin_0, 51.pin_0, 68.pin_0
  N51: 32.pin_0, 42.pin_0, 52.pin_0, 62.pin_0
  N52: 53.pin_0, 58.pin_0, 60.pin_0, 72.pin_0, 78.pin_0
  N53: 54.pin_0, 57.pin_0, 61.pin_0, 63.pin_0, 75.pin_0
  N54: 55.pin_0, 56.pin_0, 59.pin_0, 67.pin_0, 76.pin_0
  N55: S7.Pin_1, S7.Pin_2, 74.pin_0
  N56: S7.Pin_3, S7.Pin_4, 73.pin_0

custom parts:
  Power plug: power plug
  Big Potentiometer: A standard adjustable resistor (potentiometer).
  header hole: hole
