# Fritzing sketch IRobot (saved by Fritzing 0.6.5b)
breadboards: 1

parts:
  Part1 = Arduino Motor Shield
  Arduino1 = Arduino
  VCC1 = Battery
  VCC2 = Battery
  VCC3 = Battery
  M1 = DC Motor
  M2 = DC Motor
  S1 = Toggle Switch [package=THT]
  Part2 = IR Receiver Breakout [package=PCB]

nets:
  GND: Part1.GND, Arduino1.GND, VCC1.-, VCC2.-, VCC3.-, Part2.GND
  N1: Part1.OUT3, M1.pin_2
  N2: Part1.OUT4, M1.pin_1
  N3: Part1.OUT2, M2.pin_2
  N4: Part1.OUT1, M2.pin_1
  5V: Part1.5V, Arduino1.+5V, Part2.VCC
  N5: Part1.D9, Arduino1.D9
  N6: Part1.D10, Arduino1.D10
  N7: Part1.D11, Part2.OUT
  N8: Part1.D12, Arduino1.D12
  N9: Part1.D13, Arduino1.D13
  VIN: Part1.VIN, Arduino1.VIN, S1.L1
  N10: VCC1.+, VCC2.+, VCC3.+, S1.COM

notes:
  IR Reciever
  5v, GND, and Signal to Pin 11.
  6 AA batteries provide 9v to power motors and Arduino through Vin.
  Switch to power on/off.
  2 DC motors, on robot with wheels and gearboxes.
  There is no part for my shield (from NKC) but it is similar to this.
  Uses pins 9&10 to control speed on motors A&B using PWM. Uses pins 12&13 to control direction on motors A&B.
  The shield stacks on top, but I have shown the connections with wires.
  #include <IRremote.h>
  #include <IRremoteInt.h>
  // Robot With IR remote
  // by Neil Hendrick
  //
  //this imports the IR Library (must be present in libraries folder)
  int dirbpinB = 12; // Direction pin for motor B is Digital 12
  int speedbpinB = 9; // Speed pin for motor B is Digital 9 (PWM)
  int dirbpinA = 13; // Direction pin for motor A is Digital 13
  int speedbpinA = 10; // Speed pin for motor A is Digital 10 (PWM)
  int speed = 100;
  int dir = 0;
  int RECV_PIN = 11; // IR receiver
  IRrecv irrecv(RECV_PIN);
  decode_results results;
  void setup()
  {
  pinMode(dirbpinB, OUTPUT);
  pinMode(dirbpinA, OUTPUT);
  Serial.begin(9600); //begin serial connection, prints output to your PD
  irrecv.enableIRIn(); // Start the receiver
  }
  void loop(){ //start loop
  if (irrecv.decode(&results)) {
  if (results.value == 0x57439867) { //UP forward
  digitalWrite(dirbpinB, 1); // set direction
  digitalWrite(dirbpinA, 1); // set direction
  analogWrite(speedbpinB, speed); // set speed (PWM)
  analogWrite(speedbpinA, speed); // set speed (PWM)
  }// close UP
  else if (results.value == 0x57439966) { //UP forward
  digitalWrite(dirbpinB, 1); // set direction
  digitalWrite(dirbpinA, 1); // set direction
  analogWrite(speedbpinB, speed); // set speed (PWM)
  analogWrite(speedbpinA, speed); // set speed (PWM)
  }// close UP
  else if (results.value == 0x57439968) { //UP forward
  digitalWrite(dirbpinB, 1); // set direction
  digitalWrite(dirbpinA, 1); // set direction
  analogWrite(speedbpinB, speed); // set speed (PWM)
  analogWrite(speedbpinA, speed); // set speed (PWM)
  }// close UP
  else if (results.value == 0x5743CC33) { //DOWN backward
  digitalWrite(dirbpinB, 0); // set direction
  digitalWrite(dirbpinA, 0); // set direction
  analogWrite(speedbpinB, speed); // set speed (PWM)
  analogWrite(speedbpinA, speed); // set speed (PWM)
  }
  else if (results.value == 0x57437887) { //LEFT
  digitalWrite(dirbpinB, 1); // set direction
  digitalWrite(dirbpinA, 1); // set direction
  analogWrite(speedbpinB, speed); // set speed (PWM)
  analogWrite(speedbpinA, 50); // set speed (PWM)
  }
  else if (results.value == 0x5743B44B) { //RIGHT
  digitalWrite(dirbpinB, 1); // set direction
  digitalWrite(dirbpinA, 1); // set direction
  analogWrite(speedbpinB, 50); // set speed (PWM)
  analogWrite(speedbpinA, speed); // set speed (PWM)
  }
  else if (results.value == 0x57438679) { //STOP *
  analogWrite(speedbpinB, 0); // set speed (PWM)
  analogWrite(speedbpinA, 0); // set speed (PWM)
  }
  else if (results.value == 0x574354AB) { //STOP OK
  analogWrite(speedbpinB, 0); // set speed (PWM)
  analogWrite(speedbpinA, 0); // set speed (PWM)
  }
  else if (results.value == 0x574355AA) { //STOP OK
  analogWrite(speedbpinB, 0); // set speed (PWM)
  analogWrite(speedbpinA, 0); // set speed (PWM)
  }
  else if (results.value == 0x57432CD3) { // Spin Left RW
  digitalWrite(dirbpinB, 1); // set direction
  digitalWrite(dirbpinA, 0); // set direction
  analogWrite(speedbpinB, speed); // set speed (PWM)
  analogWrite(speedbpinA, speed); // set speed (PWM)
  }
  else if (results.value == 0x5743AB54) { //Spin Right FF
  digitalWrite(dirbpinB, 0); // set direction
  digitalWrite(dirbpinA, 1); // set direction
  analogWrite(speedbpinB, speed); // set speed (PWM)
  analogWrite(speedbpinA, speed); // set speed (PWM)
  }
  else if (results.value == 0x5743AA55) { //Spin Right FF
  digitalWrite(dirbpinB, 0); // set direction
  digitalWrite(dirbpinA, 1); // set direction
  analogWrite(speedbpinB, speed); // set speed (PWM)
  analogWrite(speedbpinA, speed); // set speed (PWM)
  }
  Serial.println(results.value, HEX); //sends the IR code to computer so you can see what codes you are sending
  irrecv.resume(); // Receive the next value
  }//close first IF "if (irrecv.decode(&results)){"
  } //close loop
  Here is the Sketch
  ************OVERVIEW*************
  This is a 2 motor robot controlled with an Infrared remote control.
  Arduino needs the IR Library included, you can get it from: http://www.arcfn.com/2009/08/multi-protocol-infrared-remote-library.html
  Ther is no FZ part for the Motor Control shield I used, a freeduino that I got from NKC for $12. (http://store.nkcelectronics.com/freeduino-arduino-motor-control-shield-kit.html).
  The whole Robot is built into a nice cardboard box that used to hold stationary.
  The DC motors run two wheels, there is a castor wheel for balance.
  The IR sensor is mounted on top of the BOX.
  The IR Remote is from my ROKU, but any IR Remote control will do.
  The IR sensor reads the button press from the remote, I have a line in the sketch that prints that to the Serial output so you can watch it on your output.
  When you put this together, you have to modify the IR codes in the sketch to reflect the codes that you are getting from your own remote.
  For Example, upload the sketch to the Arduino, have the IR senso hooked up. Open the Serial Monitor, NOW when I press the UP button on my remote, i see that UP sends a HEX number: 57439867
  So, you can see in the sketch, I include that in an IF statement:
  if (results.value == 0x57439867) { //UP forward
  Inside the IF statement, there are the speed and direction commands to make both motors go Forward.
  Use the serial monitor to decide what codes are associated with your remote. Then, replace my codes with your codes.
  You might find that the sensor can wiggle one digit either direction, just add more than one UP command to cover the different codes.
  57439867, 57439866, 57439868 all come from the UP arrow and tell the robot to go forward.
