# Fritzing sketch ImpulsegeneratorSymmetricalPulses (saved by Fritzing 0.4.3b)
breadboards: 1

parts:
  IC100 = 555 Timer [package="DIP8 [THT]"]
  C112 = Electrolytic Capacitor [package=THT]
  R116 = Resistor [resistance=33k package=THT]
  R117 = Resistor [resistance=33k package=THT]
  R114 = Resistor [resistance=4.7k package=THT]
  R113 = Resistor [resistance=1k package=THT]
  C118 = Ceramic Capacitor [package=THT]
  VCC1 = Battery block 9V
  Side1 = Paper_A3_Horizontal
  D126 = Rectifier Diode [package="300 mil [THT]"]
  LED1 = Red LED-R - 3mm [package="T1.75 (3mm)"]

nets:
  GND: IC100.Ground, C112.-, C118.pin_0, VCC1.-, Side1.Project, LED1.cathode
  N1: IC100.Trigger, IC100.Threshold, C112.+, R116.Pin_1, D126.cathode
  N2: IC100.Output, R113.Pin_0
  N3: IC100.Reset, R114.Pin_1
  N4: IC100.Discharge, R116.Pin_0, R117.Pin_1, D126.anode
  N5: IC100.Vcc_Supply_Voltage, R117.Pin_0, R114.Pin_0, C118.pin_1, VCC1.+
  N6: R113.Pin_1, LED1.anode

notes:
  555 Tutorial_Basic
  Impulsegenerator Symmetrical Pulses
  mjf / 14 July .2010
  07.2010
  mjf / 12 Dec. 2010
  Schematic schows symmetrical pulse generator.
  For R117=R116 you can use:
  1
  f = ---------------------------
  1.4 * C112 * R116
  For detail signal pulse pause differentiation use:
  1 1
  f= ------------------------------ = ---------------
  (timpulse + tpause) ( ti + tp )
  ti= 0.7 * C112 * R117
  tp=0.7 * C112 * R116
  Detailed calculation:
  1 1
  f = ----------------------------------- = -------------------------------
  0.7 * C112(R117+R116) 0.7* 10µF(33k+33k)
  1 1
  = -------------------------------------- = --------------------- = 2 Hz
  0,000007F* 66000 Ohm 0.462 sec

custom parts:
  Paper_A3_Horizontal: Paper A3 Vertical
  Red LED-R - 3mm: A generic red LED (~1.8V)
