# Fritzing sketch In-Out_temperature (saved by Fritzing 0.6.2b)
breadboards: 1

parts:
  Arduino1 = Arduino
  U4 = mystery part, 3 pins [chip_label=DS18B20 spacing=300mil]
  U5 = mystery part, 3 pins [chip_label=DS18B20 spacing=300mil]
  R4 = Resistor [tolerance=±5% resistance=4.7k package=THT]

nets:
  N1: Arduino1.D4, U4.pin2, U5.pin2
  N2: Arduino1.+5V, R4.Pin_0
  N3: Arduino1.GND, U4.pin1, U4.pin3, U5.pin1, U5.pin3
