# Fritzing sketch JJ-80 (saved by Fritzing 0.6.3b)
breadboards: 1

parts:
  XTAL1_-_3_530MHz = Crystal
  switch1 = Jack_1_4
  XTAL1_-_3_530MHz1 = Crystal
  XTAL1_-_3_530MHz2 = Crystal
  XTAL1_-_3_530MHz3 = Crystal
  XTAL1_-_3_530MHz4 = Crystal
  XTAL1_-_3_530MHz5 = Crystal

nets:
  N1: XTAL1_-_3_530MHz.connector0, switch1.connector11
  N2: XTAL1_-_3_530MHz.connector1, XTAL1_-_3_530MHz1.connector1, XTAL1_-_3_530MHz2.connector1, XTAL1_-_3_530MHz3.connector1, XTAL1_-_3_530MHz4.connector1, XTAL1_-_3_530MHz5.connector1
  N3: switch1.connector4, XTAL1_-_3_530MHz4.connector0
  N4: switch1.connector8, XTAL1_-_3_530MHz3.connector0
  N5: switch1.connector9, XTAL1_-_3_530MHz2.connector0
  N6: switch1.connector10, XTAL1_-_3_530MHz1.connector0
