# Fritzing sketch LCD-con-control-del-contraste (saved by Fritzing 0.3.16b)
breadboards: 1

parts:
  Arduino1 = Arduino
  LCD1 = LCD screen
  S1 = Pushbutton [package="[THT]"]
  S2 = Pushbutton [package="[THT]"]
  LED1 = Red LED - 5mm
  R1 = Resistor [resistance=220 package=THT]
  R2 = Resistor [resistance=10k package=THT]

nets:
  GND: Arduino1.GND, LCD1.VSS, LCD1.R/W, LCD1.LED-, R1.Pin_1, R2.Pin_1
  N1: Arduino1.D12, LCD1.DB7
  N2: Arduino1.D11, LCD1.DB6
  N3: Arduino1.D10, LCD1.DB5
  N4: Arduino1.D9, LCD1.DB4
  N5: Arduino1.D8, LCD1.E
  N6: Arduino1.D7, LCD1.RS
  N7: Arduino1.D6, LCD1.V0
  N8: Arduino1.D5, S1.Pin_1, S1.Pin_2, R2.Pin_0
  N9: Arduino1.D4, S2.Pin_1, S2.Pin_2, R1.Pin_0
  +5V: Arduino1.+5V, LCD1.VDD, LCD1.LED+, LED1.anode
  N10: S1.Pin_3, S1.Pin_4, S2.Pin_3, S2.Pin_4, LED1.cathode
