# Fritzing sketch LCD_3 (saved by Fritzing 0.4.3b)
breadboards: 1

parts:
  Arduino1 = Arduino
  LCD1 = LCD screen
  R1 = Trimmer Potentiometer [package=THT]
  R2 = Resistor [resistance=12 package=THT]
  R3 = Rotary Potentiometer (Small)
  R4 = Trimmer Potentiometer [package=THT]
  S1 = Pushbutton [package="[THT]"]
  S2 = Pushbutton [package="[THT]"]
  R5 = Resistor [resistance=10k package=THT]
  R6 = Resistor [resistance=10k package=THT]

nets:
  N1: Arduino1.D10, S2.Pin_3, S2.Pin_4, R5.Pin_1
  N2: Arduino1.D9, S1.Pin_1, S1.Pin_2, R6.Pin_1
  N3: Arduino1.D7, LCD1.RS
  N4: Arduino1.D6, LCD1.E
  N5: Arduino1.D5, LCD1.DB7
  N6: Arduino1.D4, LCD1.DB6
  N7: Arduino1.D3, LCD1.DB5
  N8: Arduino1.D2, LCD1.DB4
  +5V: Arduino1.+5V, LCD1.VDD, R1.leg1, R2.Pin_0, R3.leg2, R4.leg2, R5.Pin_0, R6.Pin_0
  GND: Arduino1.GND, LCD1.VSS, LCD1.R/W, LCD1.LED-, R1.leg2, R3.leg1, R4.leg1, S1.Pin_3, S1.Pin_4, S2.Pin_1, S2.Pin_2
  N9: Arduino1.A0, R3.wiper
  N10: Arduino1.A2, R4.wiper
  N11: LCD1.V0, R1.wiper
  N12: LCD1.LED+, R2.Pin_1

notes:
  Messwert-Simulator
  Messwert-
  Uebernahme
  Modus-
  Auswahl
  LCD-
  LED
  Messreihe
