# Fritzing sketch LEDBCDDCFUHR (saved by Fritzing 0.5.2b)
breadboards: 3

parts:
  32_768KHz = Crystal [package=THT]
  RTC = DS1307 [package=THT]
  3V_Bat = obsolete Battery
  Arduino_Mini = Arduino Mini
  5V_DC = Power plug
  DCF77 = mystery part, 3 pins [chip_label=? spacing=300mil]
  Q1 = NPN-Transistor [package="TO92 [THT]"]
  1K = Resistor [resistance=220 package=THT]
  Bank_0 = 74HC595 [package="DIP16 [THT]"]
  Bank_1 = 74HC595 [package="DIP16 [THT]"]
  Bank_2 = 74HC595 [package="DIP16 [THT]"]
  Bank_3 = 74HC595 [package="DIP16 [THT]"]
  220 = Resistor [resistance=220 package=THT]
  LED0 = yellow LED - 5mm [package="5 mm [THT]"]
  220_2 = Resistor [resistance=220 package=THT]
  220_3 = Resistor [resistance=220 package=THT]
  220_4 = Resistor [resistance=220 package=THT]
  220_5 = Resistor [resistance=220 package=THT]
  220_6 = Resistor [resistance=220 package=THT]
  220_7 = Resistor [resistance=220 package=THT]
  220_8 = Resistor [resistance=220 package=THT]
  LED7 = yellow LED - 5mm [package="5 mm [THT]"]
  LED6 = yellow LED - 5mm [package="5 mm [THT]"]
  LED5 = yellow LED - 5mm [package="5 mm [THT]"]
  LED4 = yellow LED - 5mm [package="5 mm [THT]"]
  LED3 = yellow LED - 5mm [package="5 mm [THT]"]
  LED2 = yellow LED - 5mm [package="5 mm [THT]"]
  LED1 = yellow LED - 5mm [package="5 mm [THT]"]

nets:
  N1: 32_768KHz.pin_0, RTC.X2_-_Crystal
  N2: 32_768KHz.pin_1, RTC.X1_-_Crystal
  N3: RTC.Vbat_-_Backup_Supply, 3V_Bat.+, Q1.C
  N4: RTC.SDA_-_I2C_Data, Arduino_Mini.A4
  N5: RTC.SCL_-_I2C_Clock, Arduino_Mini.A5
  VCC: RTC.+V, Arduino_Mini.+5V, 5V_DC.VCC, Bank_0.MR, Bank_0.VCC, Bank_1.MR, Bank_1.VCC, Bank_2.MR, Bank_2.VCC, Bank_3.MR, Bank_3.VCC
  GND: 3V_Bat.-, Arduino_Mini.GND, 5V_DC.GND, DCF77.pin1, Bank_0.GND, Bank_0.OE, Bank_1.GND, Bank_1.OE, Bank_2.GND, Bank_2.OE, Bank_3.GND, Bank_3.OE, LED0.cathode, LED7.cathode, LED6.cathode, LED5.cathode, LED4.cathode, LED3.cathode, LED2.cathode, LED1.cathode
  N6: Arduino_Mini.D11, Bank_0.DS
  N7: Arduino_Mini.D12, Bank_0.SH_CP, Bank_1.SH_CP, Bank_2.SH_CP, Bank_3.SH_CP
  N8: Arduino_Mini.D2, DCF77.pin3
  N9: Arduino_Mini.D3, 1K.Pin_1
  N10: Arduino_Mini.D8, Bank_0.ST_CP, Bank_1.ST_CP, Bank_2.ST_CP, Bank_3.ST_CP
  N11: DCF77.pin2, Q1.E
  N12: Q1.B, 1K.Pin_0
  N13: Bank_0.Q1, 220_8.Pin_1
  N14: Bank_0.Q2, 220_7.Pin_1
  N15: Bank_0.Q3, 220_5.Pin_1
  N16: Bank_0.Q4, 220_6.Pin_1
  N17: Bank_0.Q5, 220_3.Pin_1
  N18: Bank_0.Q6, 220_4.Pin_1
  N19: Bank_0.Q7, 220_2.Pin_1
  N20: Bank_0.Q7', Bank_1.DS
  N21: Bank_0.Q0, 220.Pin_1
  N22: Bank_1.Q7', Bank_2.DS
  N23: Bank_2.Q7', Bank_3.DS
  N24: 220.Pin_0, LED0.anode
  N25: 220_2.Pin_0, LED7.anode
  N26: 220_3.Pin_0, LED5.anode
  N27: 220_4.Pin_0, LED6.anode
  N28: 220_5.Pin_0, LED3.anode
  N29: 220_6.Pin_0, LED4.anode
  N30: 220_7.Pin_0, LED2.anode
  N31: 220_8.Pin_0, LED1.anode

notes:
  LEDs und Vorwider-stände analog an den anderen drei 74HC595.
