# Fritzing sketch LED_blinker_dual (saved by Fritzing 0.3.8b)
breadboards: 1

parts:
  LED2 = Red LED - 5mm
  VCC1 = obsolete Battery
  LED3 = Red LED - 5mm [package="T1.75 (5mm)"]
  R1 = 220 Ω Resistor [package=THT]

nets:
  N1: LED2.cathode, LED3.cathode, R1.Pin_0
  N2: LED2.anode, VCC1.+, LED3.anode
  N3: VCC1.-, R1.Pin_1

notes:
  Alternating two LED blinker. One LED is special "blinking LED" red or green, the other one is a blue LED. The LED's will be alternativly on and off, as the Blue LED goes on when blinking LED is off. Tested with real hardware too! Instead of the blue LED it is possible to use red/green/yellow LED with series diode.
  First published in Antti Brain October 2009 Issue. http://www.antti-brain.com

custom parts:
  Red LED - 5mm: A generic red LED (~1.8V)
