# Fritzing sketch Lochraster-Beschriftet (saved by Fritzing 0.6.3b)
breadboards: 1

parts:
  Arduino1 = Arduino
  U1 = mystery part, 16 pins [chip_label=? spacing=100mil]
  U2 = mystery part, 24 pins [chip_label=? spacing=100mil]
  U3 = mystery part, 12 pins [chip_label=? spacing=100mil]
  U4 = mystery part, 28 pins [chip_label=? spacing=100mil]
  U5 = mystery part, 42 pins [chip_label=? spacing=100mil]  # not connected
  U6 = mystery part, 42 pins [chip_label=? spacing=100mil]  # not connected
  U7 = mystery part, 42 pins [chip_label=? spacing=100mil]  # not connected
  U8 = mystery part, 42 pins [chip_label=? spacing=100mil]  # not connected
  U9 = mystery part, 42 pins [chip_label=? spacing=100mil]  # not connected
  U10 = mystery part, 42 pins [chip_label=? spacing=100mil]  # not connected

nets:
  N1: Arduino1.aref, U2.pin5, U2.pin20
  N2: Arduino1.GND, U2.pin6, U2.pin19, U4.pin12, U4.pin13, U4.pin16, U4.pin17
  N3: Arduino1.D13, U2.pin7, U2.pin18
  N4: Arduino1.D12, U2.pin8, U2.pin17
  N5: Arduino1.D11, U2.pin9, U2.pin16
  N6: Arduino1.D10, U2.pin10, U2.pin15
  N7: Arduino1.D9, U2.pin11, U2.pin14
  N8: Arduino1.D8, U2.pin12, U2.pin13
  N9: Arduino1.D7, U1.pin1, U1.pin16
  N10: Arduino1.D6, U1.pin2, U1.pin15
  N11: Arduino1.D5, U1.pin3, U1.pin14
  N12: Arduino1.D4, U1.pin4, U1.pin13
  N13: Arduino1.D3, U1.pin5, U1.pin12
  N14: Arduino1.D2, U1.pin6, U1.pin11
  N15: Arduino1.D1TX, U1.pin7, U1.pin10
  N16: Arduino1.D0RX, U1.pin8, U1.pin9
  N17: Arduino1.RST, U4.pin9, U4.pin20
  N18: Arduino1.3V3, U4.pin10, U4.pin19
  N19: Arduino1.+5V, U4.pin11, U4.pin18
  N20: Arduino1.VIN, U4.pin14, U4.pin15
  N21: Arduino1.A0, U3.pin1, U3.pin12
  N22: Arduino1.A1, U3.pin2, U3.pin11
  N23: Arduino1.A2, U3.pin3, U3.pin10
  N24: Arduino1.A3, U3.pin4, U3.pin9
  N25: Arduino1.A4, U3.pin5, U3.pin8
  N26: Arduino1.A5, U3.pin6, U3.pin7
  N27: U2.pin1, U2.pin24
  N28: U2.pin2, U2.pin23
  N29: U2.pin3, U2.pin22
  N30: U2.pin4, U2.pin21
  N31: U4.pin1, U4.pin28
  N32: U4.pin2, U4.pin27
  N33: U4.pin3, U4.pin26
  N34: U4.pin4, U4.pin25
  N35: U4.pin5, U4.pin24
  N36: U4.pin6, U4.pin23
  N37: U4.pin7, U4.pin22
  N38: U4.pin8, U4.pin21

notes:
  A0
  A1
  A2
  A3
  A4
  A5
  0
  1
  2
  3P
  4
  5P
  6P
  7
  8
  9P
  10P
  11P
  12
  13
  GND
  AREF
  Vin
  5V
  3V3
  Reset
