# Fritzing sketch Messwertbearbeitung (saved by Fritzing 0.4.3b)
breadboards: 1

parts:
  ATMEGA3281 = ATMEGA328
  U1 = Voltage Regulator - 5V [package="TO220 [THT]"]
  VCC1 = Battery block 9V
  D1 = Rectifier Diode [package="300 mil [THT]"]
  XTAL1 = Crystal [package=THT]
  C1 = Ceramic Capacitor [package=THT]
  C2 = Ceramic Capacitor [package=THT]
  EL_1602_B1 = EL1602B
  R1 = Trimmer Potentiometer [package=THT]
  R2 = Resistor [resistance=10 package=THT]
  R3 = Rotary Potentiometer (Small)
  R4 = Resistor [resistance=10k package=THT]
  R5 = Resistor [resistance=10k package=THT]
  S1 = Pushbutton [package="[THT]"]
  S2 = Pushbutton [package="[THT]"]

nets:
  N1: ATMEGA3281.connector3, EL_1602_B1.connector5
  N2: ATMEGA3281.connector4, EL_1602_B1.connector4
  N3: ATMEGA3281.connector5, EL_1602_B1.connector3
  N4: ATMEGA3281.connector8, XTAL1.pin_0, C1.pin_1
  N5: ATMEGA3281.connector9, XTAL1.pin_1, C2.pin_0
  N6: ATMEGA3281.connector10, EL_1602_B1.connector2
  N7: ATMEGA3281.connector11, EL_1602_B1.connector10
  N8: ATMEGA3281.connector12, EL_1602_B1.connector12
  N9: ATMEGA3281.connector14, R4.Pin_1, S1.Pin_3, S1.Pin_4
  N10: ATMEGA3281.connector15, R5.Pin_1, S2.Pin_3, S2.Pin_4
  N11: ATMEGA3281.connector19, U1.output_voltage, D1.anode, EL_1602_B1.connector14, EL_1602_B1.connector15, R1.leg2, R2.Pin_0
  N12: ATMEGA3281.connector21, U1.GND, VCC1.-, C1.pin_0, C2.pin_1, EL_1602_B1.connector11, EL_1602_B1.connector16, R1.leg1
  N13: ATMEGA3281.connector22, R3.wiper
  N14: U1.input_voltage, VCC1.+, D1.cathode
  N15: EL_1602_B1.connector13, R1.wiper
  N16: EL_1602_B1.connector17, R2.Pin_1
  N17: R3.leg2, R4.Pin_0, R5.Pin_0
  N18: S1.Pin_1, S1.Pin_2, S2.Pin_1, S2.Pin_2

notes:
  Write
  Read
  Modus
  Bereich
  Input
