# Fritzing sketch MicElettrete (saved by Fritzing 0.5.2b)
breadboards: 1

parts:
  R1 = Trimmer Potentiometer [package=THT]
  MIC1 = Microphone
  R2 = Resistor [resistance=220 package=THT]
  Q1 = NPN-Transistor [package="TO92 [THT]"]
  C1 = Electrolytic Capacitor [capacitance=100nF rated_voltage=35V package="100 mil [THT, electrolytic]"]
  R3 = Resistor [resistance=220 package=THT]
  Arduino1 = Arduino

nets:
  N1: R1.leg1, MIC1.pin2, Q1.B
  N2: R1.wiper, R3.Pin_1, Arduino1.+5V
  N3: MIC1.pin1, R2.Pin_1, C1.-, Arduino1.GND
  N4: R2.Pin_0, Q1.E, C1.+
  N5: Q1.C, R3.Pin_0, Arduino1.A0

notes:
  Regolare il trimmer R1 in modo che su A0 di Arduino vi siano 2,5 volt
  [scrivi qui le tue note]
