# Fritzing sketch MotorDriver (saved by Fritzing 0.3.8b)
breadboards: 2

parts:
  J1 = Screw terminal [package=THT]
  J2 = Screw terminal [package=THT]
  J3 = Screw terminal [package=THT]
  J4 = Screw terminal [package=THT]
  C1 = Ceramic Capacitor [package=THT]
  C2 = Ceramic Capacitor [package=THT]
  C3 = Ceramic Capacitor [package=THT]
  U1 = Voltage Regulator - 5V [package="TO220 [THT]"]
  C6 = Electrolytic Capacitor [package=THT]
  C7 = Electrolytic Capacitor [package=THT]
  VCC1 = obsolete Battery
  D1 = Rectifier Diode [package=THT]
  IC1 = H-Bridge [package=THT]
  C8 = Ceramic Capacitor [package=THT]
  C9 = Electrolytic Capacitor [package=THT]
  C10 = Electrolytic Capacitor [package=THT]
  C4 = Ceramic Capacitor [package=THT]

nets:
  N1: J1.pin1, IC1.1A
  N2: J1.pin2, IC1.2A
  N3: J2.pin1, IC1.4A
  N4: J2.pin2, IC1.3A
  N5: J3.pin1, C3.pin_1, IC1.3Y
  N6: J3.pin2, C1.pin_1, IC1.4Y
  N7: J4.pin1, IC1.1Y, C4.pin_0
  N8: J4.pin2, C2.pin_0, IC1.2Y
  GND: C1.pin_0, C2.pin_1, C3.pin_0, U1.GND, C6.+, C7.-, VCC1.-, IC1.GND1, IC1.GND2, IC1.GND3, IC1.GND4, C10.-, C4.pin_1
  N9: U1.input_voltage, C6.-, D1.cathode
  N10: U1.output_voltage, C7.+, IC1.1_2EN, IC1.VCC2, IC1.3_4EN, C8.pin_1, C9.-
  N11: VCC1.+, D1.anode, IC1.VCC1, C10.+
  N12: C8.pin_0, C9.+

notes:
  RED:
  Unregulated
  ORANGE:
  Regulated
  Inputs from Arduino
  Outputs to motors
