# Fritzing sketch Pong2.fzz (saved by Fritzing 0.6.3b)
breadboards: 4

parts:
  Arduino1 = Arduino
  LED1 = LED - 5mm [color="Red (633nm)" package="5 mm [THT]"]
  LED2 = LED - 5mm [color="Red (633nm)" package="5 mm [THT]"]
  LED3 = LED - 5mm [color="Red (633nm)" package="5 mm [THT]"]
  LED4 = LED - 5mm [color="Red (633nm)" package="5 mm [THT]"]
  LED5 = LED - 5mm [color="Red (633nm)" package="5 mm [THT]"]
  LED6 = LED - 5mm [color="Red (633nm)" package="5 mm [THT]"]
  LED7 = LED - 5mm [color="Red (633nm)" package="5 mm [THT]"]
  LED8 = LED - 5mm [color="Red (633nm)" package="5 mm [THT]"]
  LED9 = LED - 5mm [color="Red (633nm)" package="5 mm [THT]"]
  LED10 = LED - 5mm [color="Red (633nm)" package="5 mm [THT]"]
  LED11 = LED - 5mm [color="Red (633nm)" package="5 mm [THT]"]
  LED12 = LED - 5mm [color="Red (633nm)" package="5 mm [THT]"]
  LED13 = LED - 5mm [color="Red (633nm)" package="5 mm [THT]"]
  LED14 = LED - 5mm [color="Red (633nm)" package="5 mm [THT]"]
  LED15 = LED - 5mm [color="Red (633nm)" package="5 mm [THT]"]
  LED16 = LED - 5mm [color="Red (633nm)" package="5 mm [THT]"]
  LED17 = LED - 5mm [color="Red (633nm)" package="5 mm [THT]"]
  LED18 = LED - 5mm [color="Red (633nm)" package="5 mm [THT]"]
  LED19 = LED - 5mm [color="Red (633nm)" package="5 mm [THT]"]
  LED20 = LED - 5mm [color="Red (633nm)" package="5 mm [THT]"]
  S1 = Pushbutton [package=THT]
  R1 = Resistor [tolerance=±5% resistance=220 package=THT]
  S2 = Pushbutton [package=THT]
  R2 = Resistor [tolerance=±5% resistance=220 package=THT]
  S3 = Pushbutton [package=THT]
  S4 = Pushbutton [package=THT]
  R3 = Resistor [tolerance=±5% resistance=220 package=THT]
  R4 = Resistor [tolerance=±5% resistance=220 package=THT]
  LED21 = LED - 5mm [color="Red (633nm)" package="5 mm [THT]"]
  LED22 = LED - 5mm [color="Red (633nm)" package="5 mm [THT]"]
  LED23 = LED - 5mm [color="Red (633nm)" package="5 mm [THT]"]
  LED24 = LED - 5mm [color="Red (633nm)" package="5 mm [THT]"]
  J1 = Screw terminal - 2 pins [package=THT]  # not connected
  J2 = Screw terminal - 2 pins [package=THT]  # not connected
  J3 = Screw terminal - 2 pins [package=THT]  # not connected
  J4 = Screw terminal - 2 pins [package=THT]  # not connected

nets:
  N1: Arduino1.D13, Arduino1.D7, LED5.cathode, LED10.cathode, LED15.cathode, LED20.cathode, S4.leg0, R4.Pin_0, LED22.cathode
  N2: Arduino1.D12, S3.leg0, R3.Pin_0, LED21.cathode
  N3: Arduino1.D11, LED16.anode, LED17.anode, LED18.anode, LED19.anode, LED20.anode
  N4: Arduino1.D10, LED11.anode, LED12.anode, LED13.anode, LED14.anode, LED15.anode
  N5: Arduino1.D9, LED6.anode, LED7.anode, LED8.anode, LED9.anode, LED10.anode
  N6: Arduino1.D8, Arduino1.D4, LED1.anode, LED2.cathode, LED2.anode, LED3.anode, LED4.anode, LED5.anode, LED7.cathode, LED12.cathode, LED17.cathode
  N7: Arduino1.D6, LED4.cathode, LED8.cathode, LED14.cathode, LED19.cathode
  N8: Arduino1.D5, LED3.cathode, LED9.cathode, LED13.cathode, LED18.cathode
  N9: Arduino1.D3, Arduino1.D2, LED1.cathode, LED6.cathode, LED11.cathode, LED16.cathode
  N10: Arduino1.D1TX, Arduino1.D0RX, S1.leg0, R1.Pin_0, S2.leg0, R2.Pin_0, LED23.cathode, LED24.cathode
  N11: Arduino1.GND, Arduino1.A0, Arduino1.A1, S1.leg1, R1.Pin_1, S2.leg1, R2.Pin_1, S3.leg1, S4.leg1, R3.Pin_1, R4.Pin_1, LED21.anode, LED22.anode, LED23.anode, LED24.anode
