# Fritzing sketch PotMeter (saved by Fritzing 0.6.5b)
breadboards: 1

parts:
  Arduino1 = Arduino
  R1 = Resistor [tolerance=±5% resistance=220 package=THT]
  R2 = Resistor [tolerance=±5% resistance=220 package=THT]
  R3 = Resistor [tolerance=±5% resistance=220 package=THT]
  R4 = Resistor [tolerance=±5% resistance=220 package=THT]
  R5 = Resistor [tolerance=±5% resistance=220 package=THT]
  R6 = Resistor [tolerance=±5% resistance=220 package=THT]
  R7 = Resistor [tolerance=±5% resistance=220 package=THT]
  R8 = Resistor [tolerance=±5% resistance=220 package=THT]
  R9 = Resistor [tolerance=±5% resistance=220 package=THT]
  R10 = Resistor [tolerance=±5% resistance=220 package=THT]
  R11 = Resistor [tolerance=±5% resistance=220 package=THT]
  R12 = Resistor [tolerance=±5% resistance=220 package=THT]
  LED1 = LED - 5mm [color="Red (633nm)" package="5 mm [THT]"]
  LED2 = LED - 5mm [color="Red (633nm)" package="5 mm [THT]"]
  LED3 = LED - 5mm [color="Red (633nm)" package="5 mm [THT]"]
  LED4 = LED - 5mm [color="Red (635nm)" package="5 mm [THT]"]
  LED5 = LED - 5mm [color="Yellow (595nm)" package="5 mm [THT]"]
  LED7 = LED - 5mm [color="Yellow (595nm)" package="5 mm [THT]"]
  LED8 = LED - 5mm [color="Yellow (595nm)" package="5 mm [THT]"]
  LED13 = LED - 5mm [color="Yellow (592nm)" package="5 mm [THT]"]
  LED14 = LED - 5mm [color="Green (565nm)" package="5 mm [THT]"]
  LED15 = LED - 5mm [color="Green (565nm)" package="5 mm [THT]"]
  LED16 = LED - 5mm [color="Green (565nm)" package="5 mm [THT]"]
  LED17 = LED - 5mm [color="Green (565nm)" package="5 mm [THT]"]
  R13 = Trimmer Potentiometer [maximum_resistance=10kΩ package=THT]

nets:
  N1: Arduino1.D12, R3.Pin_0
  N2: Arduino1.D11, R8.Pin_0
  N3: Arduino1.D10, R7.Pin_0
  N4: Arduino1.D9, R4.Pin_0
  N5: Arduino1.D8, R12.Pin_0
  N6: Arduino1.D7, R11.Pin_0
  N7: Arduino1.D6, R1.Pin_0
  N8: Arduino1.D5, R2.Pin_0
  N9: Arduino1.D4, R9.Pin_0
  N10: Arduino1.D3, R10.Pin_0
  N11: Arduino1.D2, R6.Pin_0
  N12: Arduino1.D1TX, R5.Pin_0
  N13: Arduino1.+5V, R13.leg1
  N14: Arduino1.GND, LED1.cathode, LED2.cathode, LED3.cathode, LED4.cathode, LED5.cathode, LED7.cathode, LED8.cathode, LED13.cathode, LED14.cathode, LED15.cathode, LED16.cathode, LED17.cathode, R13.leg2
  N15: Arduino1.A0, R13.wiper
  N16: R1.Pin_1, LED8.anode
  N17: R2.Pin_1, LED13.anode
  N18: R3.Pin_1, LED1.anode
  N19: R4.Pin_1, LED4.anode
  N20: R5.Pin_1, LED17.anode
  N21: R6.Pin_1, LED16.anode
  N22: R7.Pin_1, LED3.anode
  N23: R8.Pin_1, LED2.anode
  N24: R9.Pin_1, LED14.anode
  N25: R10.Pin_1, LED15.anode
  N26: R11.Pin_1, LED7.anode
  N27: R12.Pin_1, LED5.anode
