# Fritzing sketch RC-Control (saved by Fritzing 0.5.2b)
breadboards: 1

parts:
  22N3904 = NPN-Transistor [package="TO92 [THT]"]
  22N3904_2 = NPN-Transistor [package="TO92 [THT]"]
  22N3904_3 = NPN-Transistor [package="TO92 [THT]"]
  22N3904_4 = NPN-Transistor [package="TO92 [THT]"]
  R1 = Resistor [resistance=2.2k package=THT]
  R2 = Resistor [resistance=2.2k package=THT]
  R3 = Resistor [resistance=2.2k package=THT]
  R4 = Resistor [resistance=2.2k package=THT]
  Arduino1 = Arduino
  RC_SWITCHES = mystery part, 5 pins [chip_label=RC-Switches spacing=300mil]
  ANT1 = Antenna  # not connected
  R5 = Resistor [resistance=220 package=THT]
  LED1 = Red LED - 5mm [package="5 mm [THT]"]
  R6 = Resistor [resistance=220 package=THT]
  R7 = Resistor [resistance=220 package=THT]
  R8 = Resistor [resistance=220 package=THT]
  LED2 = Red LED - 5mm [package="5 mm [THT]"]
  LED3 = Red LED - 5mm [package="5 mm [THT]"]
  LED4 = Red LED - 5mm [package="5 mm [THT]"]

nets:
  N1: 22N3904.E, 22N3904_2.E, 22N3904_3.E, 22N3904_4.E, Arduino1.GND, RC_SWITCHES.pin3, LED1.cathode, LED2.cathode, LED3.cathode, LED4.cathode
  N2: 22N3904.B, R1.Pin_1
  N3: 22N3904.C, RC_SWITCHES.pin5
  N4: 22N3904_2.B, R2.Pin_1
  N5: 22N3904_2.C, RC_SWITCHES.pin4
  N6: 22N3904_3.B, R3.Pin_1
  N7: 22N3904_3.C, RC_SWITCHES.pin2
  N8: 22N3904_4.B, R4.Pin_1
  N9: 22N3904_4.C, RC_SWITCHES.pin1
  N10: R1.Pin_0, Arduino1.D13, R5.Pin_0, R5.Pin_1, LED1.anode
  N11: R2.Pin_0, Arduino1.D12, R6.Pin_0, R6.Pin_1, LED2.anode
  N12: R3.Pin_0, Arduino1.D11, R7.Pin_0, R7.Pin_1, LED3.anode
  N13: R4.Pin_0, Arduino1.D10, R8.Pin_0, R8.Pin_1, LED4.anode

notes:
  Radio-Control
  yellow = forward
  orange = backward
  blue = right
  white = left
  black = GND
