# Fritzing sketch RS232share (saved by Fritzing 0.3.15b)
breadboards: 1

parts:
  U1 = RS232 level translator
  C1 = Tantalum Capacitor
  C2 = Tantalum Capacitor
  C3 = Tantalum Capacitor
  C4 = Tantalum Capacitor
  C5 = Tantalum Capacitor
  J1 = female pin header, 5 pins [form="♀ (female)"]
  CN1 = DB9_rt_female

nets:
  N1: U1.1_C1+, C1.POS
  N2: U1.2_V+, C3.POS
  N3: U1.3_C1-, C1.NEG
  N4: U1.4_C2+, C2.POS
  N5: U1.5_C2-, C2.NEG
  N6: U1.6_V-, C4.NEG
  N7: U1.7_T2OUT, CN1.2_RXD
  N8: U1.8_R2IN, CN1.3_TXD
  N9: U1.9_R2OUT, J1.pin4
  N10: U1.10_T2IN, J1.pin5
  N11: U1.15_GND, C3.NEG, C4.POS, C5.NEG, J1.pin2, CN1.5_GND, CN1.10_n/c
  N12: U1.16_VCC, C5.POS, J1.pin1

custom parts:
  RS232 level translator: MAX232 IC. RS232 logic level translator. Uses charge-pumps and capacitors to generate +/-voltages for RS232 levels from a +5V supply. Has 2 RS232 transmitters and 2 RS232 receivers.
  DB9_rt_female: RS232 connector, 9 pin, right-angle female. Minimum connections are RXD, TXD,GND
