# Fritzing sketch RTC1307 (saved by Fritzing 0.6.3b)
breadboards: 1

parts:
  Arduino1 = Arduino
  IC2 = DS1307 [package=THT]
  R1 = Resistor [tolerance=±5% resistance=2.2k package=THT]
  R2 = Resistor [tolerance=±5% resistance=2.2k package=THT]
  XTAL1 = Crystal
  VCC1 = Battery

nets:
  N1: Arduino1.GND, IC2.0V, VCC1.-
  N2: Arduino1.+5V, IC2.+V, R1.Pin_0, R2.Pin_0
  N3: Arduino1.A4, IC2.SDA_-_I2C_Data, R1.Pin_1
  N4: Arduino1.A5, IC2.SCL_-_I2C_Clock, R2.Pin_1
  N5: IC2.X1_-_Crystal, XTAL1.connector1
  N6: IC2.X2_-_Crystal, XTAL1.connector0
  N7: IC2.Vbat_-_Backup_Supply, VCC1.+

notes:
  Cristal 32,708 KHz
  2.2K
