# Fritzing sketch Receptor (saved by Fritzing 0.4.0b)
breadboards: 1

parts:
  Arduino1 = Arduino
  Servo_1 = Basic Servo
  Servo_2 = Basic Servo

nets:
  GND: Arduino1.GND, Servo_1.gnd
  N1: Arduino1.D7, Servo_2.pulse
  N2: Arduino1.D6, Servo_1.pulse

notes:
  Esquema Arduino Receptor
