# Fritzing sketch RgbLcdTermLum (saved by Fritzing 0.6.3b)
breadboards: 1

parts:
  LCD1 = LCD screen
  R1 = Rotary Potentiometer (Large) [maximum_resistance=100kΩ package=THT]
  LED1 = RGB LED - (4 legs) [package="5 mm [THT]"]
  R3 = Resistor [tolerance=±5% resistance=220 package=THT]
  R4 = Resistor [tolerance=±5% resistance=220 package=THT]
  R5 = Resistor [tolerance=±5% resistance=220 package=THT]
  U1 = Arduino Mega
  R6 = Photocell (LDR) [package=THT]
  T1 = LM35 Temperature Sensor [package="TO92 [THT]"]
  R8 = Resistor [tolerance=±5% resistance=220 package=THT]
  R9 = Resistor [tolerance=±5% resistance=220 package=THT]
  R10 = Resistor [tolerance=±5% resistance=220 package=THT]

nets:
  N1: LCD1.RS, U1.A11
  N2: LCD1.R/W, R1.leg2, LED1.green_cathode, U1.GND, T1.+Vs, R9.Pin_1
  N3: LCD1.E, U1.A12
  N4: LCD1.DB5, U1.A4
  N5: LCD1.DB6, U1.A3
  N6: R1.leg1, U1.+5V, R6.pin_1, R8.Pin_1, R10.Pin_1
  N7: LED1.red_cathode, R3.Pin_0
  N8: LED1.common_anode, R5.Pin_0
  N9: LED1.blue_cathode, R4.Pin_0
  N10: R3.Pin_1, U1.A10
  N11: R4.Pin_1, U1.A8
  N12: R5.Pin_1, U1.A9
  N13: U1.A0, R6.pin_0, R9.Pin_0
  N14: U1.A1, T1.Vout
  N15: T1.GND, R8.Pin_0
