# Fritzing sketch SHT71-Flyport (saved by Fritzing 0.4.3b)

parts:
  R1_10K = Resistor [resistance=10k package=THT]
  SHT71 = StarterKit Nest
  Componente3 = SHT71

nets:
  N1: R1_10K.Pin_0, SHT71.D/pwm2_out, Componente3.DATA
  +5V: R1_10K.Pin_1, SHT71.+5V, Componente3.VCC
  N2: SHT71.D/pwm1_out, Componente3.SCK
  GND: SHT71.GND, Componente3.GND
