# Fritzing sketch SSArduimometer2 (saved by Fritzing 0.4.3b)
breadboards: 3

parts:
  D1 = Rectifier Diode [package="300 mil [THT]"]
  U1 = Voltage Regulator - 5V [package="TO220 [THT]"]
  VCC1 = Battery block 9V
  C2 = Electrolytic Capacitor [package=THT]
  R1 = 1k Ω Resistor [package=THT]
  U2 = atmega168 [package="DIP28 [THT]"]
  Y1 = Resonator [package=THT]
  LED1 = green LED - 5mm
  R2 = Trimmer Potentiometer [package=THT]
  R3 = 10k Ω Resistor [package=THT]
  J2 = Generic male header - 16 pins [package=THT]
  J1 = Generic male header - 3 pins [package=THT]
  C3 = Ceramic Capacitor [package=THT]
  C1 = Ceramic Capacitor [package=THT]

nets:
  N1: D1.cathode, U1.input_voltage, C1.pin_1
  N2: D1.anode, VCC1.+
  GND: U1.GND, VCC1.-, C2.-, U2.Pin_8, U2.Pin_22, Y1.GND, LED1.cathode, R2.leg2, J2.pin1, J2.pin5, J2.pin16, J1.pin2, C3.pin_1, C1.pin_0
  N3: U1.output_voltage, C2.+, R1.Pin_1, U2.Pin_7, U2.Pin_20, R2.leg1, R3.Pin_1, J2.pin2, J2.pin15, J1.pin1, C3.pin_0
  N4: R1.Pin_0, LED1.anode
  N5: U2.Pin_4, R3.Pin_0, J1.pin3
  N6: U2.Pin_9, Y1.0
  N7: U2.Pin_10, Y1.pin_1
  N8: U2.Pin_13, J2.pin4
  N9: U2.Pin_14, J2.pin6
  N10: U2.Pin_15, J2.pin11
  N11: U2.Pin_16, J2.pin12
  N12: U2.Pin_17, J2.pin13
  N13: U2.Pin_18, J2.pin14
  N14: R2.wiper, J2.pin3

notes:
  Power supply
  ATMEGA328 Brains
  Staging Area
  3Pin Header to Hall Effect Sensor
  16Pin Header to LCD Screen.
