# Fritzing sketch Scanner (saved by Fritzing 0.4.3b)
breadboards: 1

parts:
  Arduino1 = Arduino
  Power_plug1 = Power plug
  R1 = Rotary Potentiometer (Large) [package=THT]
  J1 = Basic Servo
  J2 = Infrared Proximity Sensor
  LED1 = Red LED - 5mm
  R2 = Resistor [resistance=220 package=THT]

nets:
  VCC: Arduino1.aref, Power_plug1.VCC, R1.leg2, J1.vcc, J2.Vcc
  GND: Arduino1.GND, Power_plug1.GND, R1.leg1, J1.gnd, J2.GND, LED1.cathode
  N1: Arduino1.D8, J1.pulse
  N2: Arduino1.D6, R2.Pin_1
  N3: Arduino1.A0, R1.wiper
  N4: Arduino1.A1, J2.Vout
  N5: LED1.anode, R2.Pin_0
