# Fritzing sketch Servo_temp_control (saved by Fritzing 0.3.19b)

parts:
  Temp_Sensor = Temperature Sensor (Thermistor) [package=THT]
  10k_Ohm = Resistor [resistance=10k package=THT]
  Servo = Basic Servo
  Temperature_Based_Servo_Controller = Arduino
  10k_Ohm_2 = Resistor [resistance=220 package=THT]

nets:
  N1: Temp_Sensor.pin_0, 10k_Ohm.Pin_1, Temperature_Based_Servo_Controller.A0
  VCC: Temp_Sensor.pin_1, Servo.vcc, Temperature_Based_Servo_Controller.+5V
  GND: 10k_Ohm.Pin_0, Servo.gnd, Temperature_Based_Servo_Controller.GND, 10k_Ohm_2.Pin_0
  N2: Servo.pulse, Temperature_Based_Servo_Controller.D9
  5V: Temperature_Based_Servo_Controller.D7, 10k_Ohm_2.Pin_1

notes:
  +5VDC
