# Fritzing sketch Servos (saved by Fritzing 0.6.3b)
breadboards: 1

parts:
  Comprobador_de_Servos = Arduino
  Potenciometro = Rotary Potentiometer (Small) [maximum_resistance=100kΩ]
  Conexion_Servo = Basic Servo
  Pulsador = Pushbutton [package=THT]
  R1 = Resistor [tolerance=±5% resistance=1k package=THT]

nets:
  GND: Comprobador_de_Servos.GND, Potenciometro.leg1, Conexion_Servo.gnd, R1.Pin_1
  N1: Comprobador_de_Servos.D7, Conexion_Servo.pulse
  N2: Comprobador_de_Servos.D2, Pulsador.leg1, R1.Pin_0
  +5V: Comprobador_de_Servos.+5V, Potenciometro.leg2, Conexion_Servo.vcc, Pulsador.leg0
  N3: Comprobador_de_Servos.A0, Potenciometro.wiper
