# Fritzing sketch SnifferNano (saved by Fritzing 0.3.16b)
breadboards: 1

parts:
  Arduino1 = Arduino
  LCD1 = LCD screen
  R1 = Resistor [resistance=220 package=THT]
  IC1 = IC, DIP package, 14 pins [chip_label="Sniffer " spacing=600mil]
  L1 = Inductor [package="400 mil [THT]"]

nets:
  GND: Arduino1.GND, LCD1.VSS, LCD1.V0, R1.Pin_0, IC1.pin7
  N1: Arduino1.D12, LCD1.RS
  N2: Arduino1.D11, LCD1.R/W
  N3: Arduino1.D10, LCD1.E
  N4: Arduino1.D7, LCD1.DB4
  N5: Arduino1.D6, LCD1.DB5
  N6: Arduino1.D5, LCD1.DB6
  N7: Arduino1.D4, LCD1.DB7
  N8: Arduino1.D2, R1.Pin_1, IC1.pin10
  N9: Arduino1.D1TX, IC1.pin8
  N10: Arduino1.D0RX, IC1.pin9
  +5V: Arduino1.+5V, LCD1.VDD, IC1.pin6
  N11: IC1.pin13, L1.pin_0
  N12: IC1.pin14, L1.pin_1
