# Fritzing sketch Software_Multiplexer_2x3 (saved by Fritzing 0.6.2b)
breadboards: 1

parts:
  Green1 = green LED - 5mm [package="5 mm [THT]"]
  Green2 = green LED - 5mm [package="5 mm [THT]"]
  Yellow1 = yellow LED - 5mm [package="5 mm [THT]"]
  Yellow2 = yellow LED - 5mm [package="5 mm [THT]"]
  Red1 = Red LED - 5mm [package="5 mm [THT]"]
  RED2 = Red LED - 5mm [package="5 mm [THT]"]
  R1 = Rotary Potentiometer (Small) [maximum_resistance=100kΩ]
  Arduino_UNO = Arduino

nets:
  N1: Green1.cathode, Green2.cathode, Arduino_UNO.A2
  N2: Green1.anode, Yellow1.anode, Red1.anode, Arduino_UNO.D9
  N3: Green2.anode, Yellow2.anode, RED2.anode, Arduino_UNO.D8
  N4: Yellow1.cathode, Yellow2.cathode, Arduino_UNO.A1
  N5: Red1.cathode, RED2.cathode, Arduino_UNO.A0
  N6: R1.leg1, Arduino_UNO.+5V
  N7: R1.wiper, Arduino_UNO.A5
  N8: R1.leg2, Arduino_UNO.GND
