# Fritzing sketch Soundgenerator (saved by Fritzing 0.4.3b)
breadboards: 1

parts:
  IC200 = 555 Timer [package="DIP8 [THT]"]
  R216 = Resistor [resistance=33k package=THT]
  R217 = Resistor [resistance=33k package=THT]
  C218 = Ceramic Capacitor [package=THT]
  R214 = Resistor [resistance=10k package=THT]
  SPKR223 = Loudspeaker
  C213 = Electrolytic Capacitor [package=THT]
  R227 = Rotary Potentiometer (Small)
  VCC1 = Battery block 9V
  Side1 = Paper_A3_Horizontal
  C212 = Ceramic Capacitor [package=THT]

nets:
  GND: IC200.Ground, C218.pin_0, SPKR223.pin1, VCC1.-, Side1.Project, C212.pin_0
  N1: IC200.Trigger, IC200.Threshold, R216.Pin_1, C212.pin_1
  N2: IC200.Output, C213.+
  N3: IC200.Reset, R214.Pin_0
  N4: IC200.Discharge, R216.Pin_0, R217.Pin_1
  N5: IC200.Vcc_Supply_Voltage, C218.pin_1, R214.Pin_1, R227.wiper, R227.leg2, VCC1.+
  N6: R217.Pin_0, R227.leg1
  N7: SPKR223.pin2, C213.-

notes:
  555 Tutorial_Basic
  Impulsegenerator Soundgenerator
  12.Dec.2010/mjf
  07.2010
  25.07 July .2010
  Schematic schows an asymmetrical pulse generator.
  For R117=R116 you can use:
  1
  f = ---------------------------
  2.1 * C212 * R217
  For detail signal pulse pause differentiation use:
  1 1
  f= ------------------------------ = ---------------
  (timpulse + tpause) ( ti + tp )
  ti= 0.7 * C212 * R217+R216
  tp=0.7 * C212 * R216
  Detailed calculation:
  1 1
  f = ------------------------------------- = -------------------------------
  0.7 * C212(R217+2*R216) 0.7* 10nF(33k+66k)
  1 1
  = -------------------------------------- = --------------------- = 1443 Hz
  0,000007F* 66000 Ohm 0.462 sec

custom parts:
  Paper_A3_Horizontal: Paper A3 Vertical
