# Fritzing sketch Spectrum_Shield_LCD (saved by Fritzing 0.6.5b)
breadboards: 1

parts:
  Arduino2 = Arduino
  LCD1 = LCD screen
  R1 = Rotary Potentiometer (Small) [maximum_resistance=100kΩ]
  R2 = Rotary Potentiometer (Small) [maximum_resistance=100kΩ]
  TRS1 = Stereo Jack (TRS) 3.5mm [package="PG203J [THT]"]  # not connected
  TRS2 = Stereo Jack (TRS) 3.5mm [package="PG203J [THT]"]  # not connected

nets:
  N1: Arduino2.D12, LCD1.RS
  N2: Arduino2.D11, LCD1.E
  N3: Arduino2.D7, LCD1.DB4
  N4: Arduino2.D6, LCD1.DB5
  N5: Arduino2.D3, LCD1.DB6
  N6: Arduino2.D2, LCD1.DB7
  +5V: Arduino2.+5V, LCD1.VDD, R1.wiper
  GND: Arduino2.GND, LCD1.VSS, LCD1.R/W, LCD1.LED-, R2.wiper
  N7: LCD1.V0, R2.leg1
  N8: LCD1.LED+, R1.leg1

notes:
  Sparkfun Spectrum Shield
  sku: DEV-10306
  Contrast Adjust
  Brightness Adjust
