# Fritzing sketch Stupid_pet_tricks (saved by Fritzing 0.4.3b)
breadboards: 13

parts:
  VCC1 = obsolete Battery
  LED1 = white LED - 5mm  # not connected
  R1 = Resistor [resistance=1k package=THT]
  S1 = Pushbutton [package="[THT]"]
  Q1 = npn-Powertransistor [package="TO220 [THT]"]
  R3 = 1k Ω Resistor [package=THT]
  J1 = Basic Servo
  Arduino1 = Arduino
  R4 = 10k Ω Resistor [package=THT]
  J2 = Basic Force Sensing Resistor (FSR) [package=THT]

nets:
  N1: VCC1.-, R1.Pin_1
  N2: R1.Pin_0, S1.Pin_1, S1.Pin_2
  N3: S1.Pin_3, S1.Pin_4
  N4: Q1.base, R3.Pin_1
  N5: Q1.collector, Q1.emitter, Arduino1.GND
  N6: R3.Pin_0, Arduino1.D6
  N7: J1.gnd, R4.Pin_0
  VCC: J1.vcc, Arduino1.+5V, J2.pin_1
  N8: J1.pulse, Arduino1.D9
