# Fritzing sketch TRIGGER (saved by Fritzing 0.6.4b)
breadboards: 1

parts:
  Nano1 = Arduino Nano v2.3
  S1 = Pushbutton [package="[THT]"]
  R1 = Resistor [tolerance=±5% resistance=4.7k package=THT]
  J1 = Piezo Speaker
  R2 = Resistor [tolerance=±5% resistance=1M package=THT]
  LED1 = RGB LED (com. cathode, rbg) [package="5 mm [THT]"]
  R3 = Resistor [tolerance=±5% resistance=4.7k package=THT]
  R4 = Resistor [tolerance=±5% resistance=4.7k package=THT]
  U1 = mystery part, 2 pins [chip_label=CAM spacing=300mil part_number=CAMERA]  # not connected
  U2 = mystery part, 2 pins [chip_label=FLASH spacing=300mil]  # not connected
  Power_plug1 = Power plug
  U3 = Optocoupler [package=THT]  # not connected
  U4 = Optocoupler [package=THT]  # not connected

nets:
  GND: Nano1.GND, R1.Pin_0, J1.pin1, R2.Pin_0, Power_plug1.GND
  N1: Nano1.D5, S1.Pin_3, S1.Pin_4, R1.Pin_1
  N2: Nano1.D9, LED1.red_anode
  N3: Nano1.D11, LED1.common_cathode, R4.Pin_0
  N4: Nano1.D12, R3.Pin_0
  N5: Nano1.A0, J1.pin2, R2.Pin_1
  VIN: Nano1.VIN, S1.Pin_1, S1.Pin_2, Power_plug1.VCC
