# Fritzing sketch Telecommande (saved by Fritzing 0.3.14b)
breadboards: 1

parts:
  Arduino1 = Arduino
  S1 = Toggle Switch [package=THT]
  R1 = Resistor [resistance=1M package=THT]
  U1 = mystery part, 3 pins [chip_label="IRL106A2B " spacing=300mil]
  IR_LED_1 = Infrared LED
  R2 = Resistor [resistance=220 package=THT]

nets:
  N1: Arduino1.GND, R1.Pin_1, U1.pin2, IR_LED_1.connector0
  N2: Arduino1.D4, S1.L1, R1.Pin_0
  N3: Arduino1.D3, R2.Pin_1
  N4: Arduino1.D2, U1.pin1
  N5: Arduino1.+5V, S1.COM, U1.pin3
  N6: IR_LED_1.connector1, R2.Pin_0

notes:
  Mode switch
  Récepteur IR
  Emetteur IR
