# Fritzing sketch Termometer (saved by Fritzing 0.3.12b)
breadboards: 1

parts:
  Thermometer_Shield = Arduino
  U1 = 74HC595 [package="DIP16 [THT]"]
  R1 = Trimmer Potentiometer [package=THT]
  LCD = LCD
  Sensor = PNP-Transistor [package="TO92 [THT]"]
  R2 = Resistor [resistance=4.7k package=THT]
  J1 = Resistor [resistance=1 package=THT]
  J2 = Resistor [resistance=1 package=THT]

nets:
  GND: Thermometer_Shield.GND, U1.GND, U1.OE, R1.leg2, LCD.connector0, LCD.connector6, Sensor.E, Sensor.C, J1.Pin_0, J1.Pin_1, J2.Pin_0, J2.Pin_1
  N1: Thermometer_Shield.D12, Sensor.B, R2.Pin_1
  N2: Thermometer_Shield.D7, U1.DS
  N3: Thermometer_Shield.D6, U1.ST_CP
  N4: Thermometer_Shield.D5, U1.SH_CP
  +5V: Thermometer_Shield.+5V, U1.MR, U1.VCC, R1.leg1, LCD.connector1, LCD.connector7, R2.Pin_0
  N5: U1.Q1, LCD.connector3
  N6: U1.Q2, LCD.connector4
  N7: U1.Q3, LCD.connector5
  N8: U1.Q4, LCD.connector8
  N9: U1.Q5, LCD.connector9
  N10: U1.Q6, LCD.connector10
  N11: U1.Q7, LCD.connector11
  N12: R1.wiper, LCD.connector2
