# Fritzing sketch VM109 (saved by Fritzing 0.5.2b)
breadboards: 1

parts:
  > = jack
  DC+)- = Power plug
  1n4001 = Rectifier Diode [package="300 mil [THT]"]
  gnd = header hole
  hole1 = header hole
  hole1_2 = header hole
  hole1_3 = header hole  # not connected
  hole1_4 = header hole
  hole1_5 = header hole  # not connected
  100uf = Electrolytic Capacitor [package=THT]
  < = jack
  3906 = PNP-Transistor [package="TO92 [THT]"]
  3904 = NPN-Transistor [package="TO92 [THT]"]
  2_2k = Resistor [resistance=220 package=THT]
  220 = Resistor [resistance=220 package=THT]
  1k = Resistor [resistance=220 package=THT]
  470 = Resistor [resistance=220 package=THT]
  75 = Resistor [resistance=220 package=THT]
  470_2 = Resistor [resistance=220 package=THT]
  2n3904 = NPN-Transistor [package="TO92 [THT]"]
  Atmega328 = atmega168 [package="DIP28 [THT]"]
  100nf = Ceramic Capacitor [package=THT]
  S1 = DPDT 10SL005
  P2 = Big Potentiometer
  P2_2 = Big Potentiometer
  P3 = Big Potentiometer
  P4 = Big Potentiometer
  LM358 = LM 358 Dual Op-Amp [package="DIP8 [THT]"]
  100k = Resistor [resistance=220 package=THT]
  100k_2 = Resistor [resistance=220 package=THT]
  16mhz = Crystal [package=THT]
  varcap = Crystal
  47uf = Electrolytic Capacitor [package=THT]
  4_7k = Resistor [resistance=220 package=THT]
  75_2 = Resistor [resistance=220 package=THT]
  2n3904_2 = NPN-Transistor [package="TO92 [THT]"]
  75_3 = Resistor [resistance=220 package=THT]
  75_4 = Resistor [resistance=220 package=THT]
  1k_2 = Resistor [resistance=220 package=THT]
  2_2k_2 = Resistor [resistance=220 package=THT]
  LED1 = Red LED - 5mm
  LED1_2 = Red LED - 5mm
  LED1_3 = Red LED - 5mm
  1k_3 = header hole
  1k_4 = header hole
  1k_5 = header hole
  1k_6 = header hole
  1k_7 = header hole
  1k_8 = header hole
  840 = Resistor [resistance=220 package=THT]
  hole1_6 = header hole
  10k = header hole
  hole1_7 = header hole
  47 = header hole
  >_2 = mono mini jack
  47uf_2 = Electrolytic Capacitor [package=THT]
  MENU = Pushbutton 12mm omron
  <_2 = jack
  100nf_2 = ceramic capacitor
  7805 = voltage regulator lying
  10nf = ceramic capacitor
  47k = Resistor [resistance=220 package=THT]
  47k_2 = Resistor [resistance=220 package=THT]
  P1 = Big Potentiometer
  P3_2 = Big Potentiometer
  1uf = elect cap small
  4148 = small signal diode
  100k_3 = Resistor [resistance=220 package=THT]
  1uf_2 = elect cap small
  switch_toggle_sub_miniature_1 = toggle-switch
  4148_2 = small signal diode
  100uf_2 = Electrolytic Capacitor [package=THT]
  3904_2 = NPN-Transistor [package="TO92 [THT]"]
  4148_3 = small signal diode
  47_2 = Resistor [resistance=220 package=THT]
  1k_9 = Resistor [resistance=220 package=THT]
  LM1881 = LM 358 Dual Op-Amp [package="DIP8 [THT]"]
  10k_2 = Resistor [resistance=220 package=THT]
  220_2 = Resistor [resistance=220 package=THT]
  3904_3 = NPN-Transistor [package="TO92 [THT]"]
  4_7k_2 = Resistor [resistance=220 package=THT]
  2n3904_3 = NPN-Transistor [package="TO92 [THT]"]
  1n4001_2 = Rectifier Diode [package="300 mil [THT]"]
  4148_4 = small signal diode
  1k_10 = Resistor [resistance=220 package=THT]
  2n3904_4 = NPN-Transistor [package="TO92 [THT]"]
  22k = Resistor [resistance=220 package=THT]
  4_7k_3 = Resistor [resistance=220 package=THT]
  18pf = ceramic capacitor
  100nf_3 = ceramic capacitor
  680k = Resistor [resistance=220 package=THT]
  75_5 = Resistor [resistance=220 package=THT]
  100nf_4 = ceramic capacitor
  100nf_5 = ceramic capacitor
  CAPR = toggle-switch
  BW/C = toggle-switch
  L_-_R = DPDT pcb
  P5 = omeg
  gnd_2 = header hole
  75_6 = header hole
  2n3906 = PNP-Transistor [package="TO92 [THT]"]
  2n3904_5 = NPN-Transistor [package="TO92 [THT]"]
  2_2k_3 = Resistor [resistance=220 package=THT]
  470_3 = Resistor [resistance=220 package=THT]
  75_7 = Resistor [resistance=220 package=THT]
  470_4 = Resistor [resistance=220 package=THT]
  1k_11 = Resistor [resistance=220 package=THT]
  220_3 = Resistor [resistance=220 package=THT]
  2n3904_6 = NPN-Transistor [package="TO92 [THT]"]
  1k_12 = Resistor [resistance=220 package=THT]
  3904_4 = NPN-Transistor [package="TO92 [THT]"]
  75_8 = Resistor [resistance=220 package=THT]
  P1_2 = Big Potentiometer
  75_9 = Resistor [resistance=220 package=THT]
  47uf_3 = Electrolytic Capacitor [package=THT]
  I/P = toggle-switch
  47uf_4 = Electrolytic Capacitor [package=THT]
  4_7k_4 = Resistor [resistance=220 package=THT]
  100nf_6 = ceramic capacitor
  75_10 = Resistor [resistance=220 package=THT]
  100nf_7 = ceramic capacitor
  100nf_8 = ceramic capacitor
  10nf_2 = header hole
  hole1_8 = header hole
  10nf_3 = header hole
  10nf_4 = header hole
  1uf_3 = elect cap small
  1k_13 = Resistor [resistance=220 package=THT]
  5v = header hole
  75_11 = Resistor [resistance=220 package=THT]
  3904_5 = NPN-Transistor [package="TO92 [THT]"]
  2n3904_7 = NPN-Transistor [package="TO92 [THT]"]
  CAPR_2 = toggle-switch
  INVR = toggle-switch
  4_7k_5 = Resistor [resistance=220 package=THT]
  120 = Resistor [resistance=220 package=THT]
  75_12 = Resistor [resistance=220 package=THT]
  10nf_5 = ceramic capacitor
  100nf_9 = ceramic capacitor
  bat = small signal diode
  INVL = toggle-switch
  CAPL = toggle-switch
  2n3904_8 = NPN-Transistor [package="TO92 [THT]"]
  2n3904_9 = NPN-Transistor [package="TO92 [THT]"]
  75_13 = Resistor [resistance=220 package=THT]
  120_2 = Resistor [resistance=220 package=THT]
  4_7k_6 = Resistor [resistance=220 package=THT]
  75_14 = Resistor [resistance=220 package=THT]
  75_15 = Resistor [resistance=220 package=THT]
  bat_2 = small signal diode
  10nf_6 = ceramic capacitor
  100nf_10 = ceramic capacitor
  75_16 = Resistor [resistance=220 package=THT]
  gnd_3 = header hole
  10nf_7 = header hole
  CAPL_2 = toggle-switch
  100uf_3 = Electrolytic Capacitor [package=THT]  # not connected

nets (from the pcb view):
  N1: >.connector0, S1.connector4
  N2: >.connector1, >.connector2, >.connector3, DC+)-.connector1, DC+)-.connector2, 1n4001.anode, hole1_4.connector0, 100uf.-, <.connector1, <.connector2, <.connector3, 220.Pin_0, 1k.Pin_0, Atmega328.Pin_8, Atmega328.Pin_22, S1.connector7, P2.connector2, P2_2.connector2, P3.connector2, P4.connector2, LM358.connector3, 100k.Pin_1, varcap.connector1, varcap.connector2, 75_2.Pin_1, 75_3.Pin_1, 1k_6.connector0, 1k_7.connector0, 1k_8.connector0, 47.connector0, >_2.connector1, >_2.connector2, MENU.connector2, MENU.connector3, <_2.connector1, <_2.connector2, <_2.connector3, 100nf_2.connector1, 7805.connector1, P3_2.connector2, 100k_3.Pin_0, 1uf_2.connector0, 100uf_2.-, 3904_2.E, LM1881.connector3, 2n3904_3.E, 1n4001_2.anode, 2n3904_4.E, 680k.Pin_0, 100nf_4.connector1, CAPR.connector1, CAPR.connector2, BW/C.connector3, L_-_R.connector1, P5.connector2, 1k_11.Pin_0, 220_3.Pin_0, I/P.connector3, 100nf_7.connector0, 100nf_8.connector0, 2n3904_7.E, 75_12.Pin_1, bat.connector1, 2n3904_8.E, 75_13.Pin_1, bat_2.connector1, gnd_3.connector0, CAPL_2.connector2
  N3: DC+)-.connector0, 1n4001.cathode, 100uf.+, 7805.connector0
  N4: gnd.connector0, 100nf.pin_0
  N5: hole1.connector0, Atmega328.Pin_3, LED1_3.cathode
  N6: hole1_2.connector0, Atmega328.Pin_2
  N7: <.connector0, S1.connector1
  N8: 3906.E, 75.Pin_1
  N9: 3906.B, 3904.C, 470_2.Pin_1
  N10: 3906.C, 470.Pin_1, 47uf.+
  N11: 3904.E, 220.Pin_1, 470.Pin_0
  N12: 3904.B, 2_2k.Pin_1, 1k.Pin_1, 75_6.connector0
  N13: 2_2k.Pin_0, 75.Pin_0, 470_2.Pin_0, 2n3904.C, Atmega328.Pin_7, Atmega328.Pin_20, P2.connector4, P2_2.connector4, P3.connector4, LM358.connector7, 100k_2.Pin_1, 10k.connector0, 100nf_2.connector0, 7805.connector2, P3_2.connector4, 100uf_2.+, LM1881.connector7, 220_2.Pin_1, 22k.Pin_1, P5.connector4, 470_3.Pin_0, 75_7.Pin_0, 100nf_7.connector1, 5v.connector0, 3904_5.C, 120.Pin_0, 2n3904_9.C, 120_2.Pin_0, 10nf_7.connector0
  N14: 2n3904.E, 75_2.Pin_0, P1.connector4, 100nf_5.connector1, 10nf_4.connector0
  N15: 2n3904.B, 47uf.-, 4_7k.Pin_1
  N16: Atmega328.Pin_1, 100nf.pin_1, hole1_6.connector0
  N17: Atmega328.Pin_5, LED1_2.cathode
  N18: Atmega328.Pin_6, 1k_9.Pin_1
  N19: Atmega328.Pin_9, 16mhz.pin_1, 18pf.connector0
  N20: Atmega328.Pin_10, 16mhz.pin_0, varcap.connector0
  N21: Atmega328.Pin_11, 10k_2.Pin_1
  N22: Atmega328.Pin_12, 1k_12.Pin_1
  N23: Atmega328.Pin_13, 1k_2.Pin_0
  N24: Atmega328.Pin_14, LED1.cathode
  N25: Atmega328.Pin_15, 4148_2.connector1
  N26: Atmega328.Pin_16, L_-_R.connector2
  N27: Atmega328.Pin_17, L_-_R.connector0
  N28: Atmega328.Pin_18, BW/C.connector2
  N29: Atmega328.Pin_19, I/P.connector2
  N30: Atmega328.Pin_23, 2_2k_2.Pin_1
  N31: Atmega328.Pin_24, P2.connector3
  N32: Atmega328.Pin_25, P2_2.connector3
  N33: Atmega328.Pin_27, P5.connector3
  N34: Atmega328.Pin_28, MENU.connector0, MENU.connector1
  N35: S1.connector0, 47uf_2.-
  N36: S1.connector2, S1.connector5
  N37: S1.connector3, 75_3.Pin_0, 75_4.Pin_1, 840.Pin_0, 4148_3.connector1, 47_2.Pin_0, 75_9.Pin_1
  N38: P3.connector3, 4_7k.Pin_0
  N39: P4.connector3, 1uf_3.connector0
  N40: P4.connector4, 1uf.connector1
  N41: LM358.connector0, 10nf.connector0, 47k.Pin_1, 4148.connector1
  N42: LM358.connector1, 10nf.connector1, 47k.Pin_0, 1k_13.Pin_1
  N43: LM358.connector2, LM358.connector6, 47k_2.Pin_1
  N44: LM358.connector4, 100k.Pin_0, 100k_2.Pin_0
  N45: LM358.connector5, 47k_2.Pin_0
  N46: 2n3904_2.E, 75_4.Pin_0
  N47: 2n3904_2.B, 1k_2.Pin_1
  N48: 2n3904_2.C, INVL.connector1, 75_16.Pin_1
  N49: 2_2k_2.Pin_0, 4148.connector0, 100k_3.Pin_1, 1uf_2.connector1
  N50: LED1.anode, 1k_3.connector0
  N51: LED1_2.anode, 1k_4.connector0
  N52: LED1_3.anode, 1k_5.connector0
  N53: 840.Pin_1, 4148_2.connector0
  N54: hole1_7.connector0, 4148_3.connector0
  N55: >_2.connector0, 1uf.connector0
  N56: 47uf_2.+, gnd_2.connector0
  N57: <_2.connector0, 47uf_3.-
  N58: P1.connector2, P1.connector3, 10nf_3.connector0, INVL.connector2
  N59: P3_2.connector3, 4_7k_4.Pin_0
  N60: switch_toggle_sub_miniature_1.connector2, 3904_2.B
  N61: 3904_2.C, 47_2.Pin_1
  N62: LM1881.connector1, 100nf_3.connector0
  N63: LM1881.connector4, 4_7k_2.Pin_1
  N64: LM1881.connector5, 680k.Pin_1, 100nf_4.connector0
  N65: 10k_2.Pin_0, 3904_3.B
  N66: 220_2.Pin_0, 3904_3.C, 2n3904_3.C
  N67: 3904_3.E, 4148_4.connector1
  N68: 4_7k_2.Pin_0, 2n3904_3.B
  N69: 1n4001_2.cathode, 4_7k_3.Pin_1, 18pf.connector1
  N70: 4148_4.connector0, 1k_10.Pin_0
  N71: 1k_10.Pin_1, 2n3904_4.B
  N72: 2n3904_4.C, 22k.Pin_0, 4_7k_3.Pin_0
  N73: 100nf_3.connector1, 75_5.Pin_0
  N74: 75_5.Pin_1, L_-_R.connector4
  N75: CAPR.connector3, 100nf_6.connector0
  N76: 2n3906.E, 75_7.Pin_1
  N77: 2n3906.B, 2n3904_5.C, 470_3.Pin_1
  N78: 2n3906.C, 470_4.Pin_1, 47uf_4.+
  N79: 2n3904_5.E, 470_4.Pin_0, 220_3.Pin_1
  N80: 2n3904_5.B, 2_2k_3.Pin_1, 1k_11.Pin_1, 75_10.Pin_1
  N81: 2n3904_6.E, 75_9.Pin_0
  N82: 2n3904_6.B, 1k_12.Pin_0
  N83: 2n3904_6.C, INVR.connector1, 75_15.Pin_0
  N84: 3904_4.E, 75_8.Pin_1, P1_2.connector4, hole1_8.connector0
  N85: 3904_4.B, 47uf_4.-, 4_7k_4.Pin_1
  N86: P1_2.connector2, P1_2.connector3, 10nf_2.connector0, INVR.connector2
  N87: 47uf_3.+, 75_10.Pin_0
  N88: 1uf_3.connector1, 1k_13.Pin_0
  N89: 75_11.Pin_0, 3904_5.B
  N90: 75_11.Pin_1, 2n3904_7.C, 120.Pin_1
  N91: 3904_5.E, 75_12.Pin_0, 10nf_5.connector1, 100nf_9.connector1
  N92: 2n3904_7.B, 4_7k_5.Pin_0
  N93: CAPR_2.connector1, 100nf_9.connector0
  N94: CAPR_2.connector2, 10nf_5.connector0, bat.connector0, 75_15.Pin_1
  N95: INVR.connector3, 4_7k_5.Pin_1
  N96: INVL.connector3, 4_7k_6.Pin_1
  N97: CAPL.connector1, 100nf_10.connector0
  N98: CAPL.connector2, bat_2.connector0, 10nf_6.connector0, 75_16.Pin_0
  N99: 2n3904_8.B, 4_7k_6.Pin_0
  N100: 2n3904_8.C, 120_2.Pin_1, 75_14.Pin_1
  N101: 2n3904_9.E, 75_13.Pin_0, 10nf_6.connector1, 100nf_10.connector1
  N102: 2n3904_9.B, 75_14.Pin_0
