# Fritzing sketch WTR011 (saved by Fritzing 0.4.3b)
breadboards: 1

parts:
  pot = Big Potentiometer
  Power_plug1 = Power plug
  7805 = Voltage Regulator - 5V [package="TO220 [THT]"]
  4n28 = Optocoupler [package=THT]
  Atmega328 = atmega168 [package="DIP28 [THT]"]
  100u = Electrolytic Capacitor [package=THT]
  1uF = Electrolytic Capacitor [package=THT]
  100u_2 = Electrolytic Capacitor [package=THT]
  100nf = Ceramic Capacitor [package=THT]
  1n4001 = Rectifier Diode [package="300 mil [THT]"]
  3mm_hole1 = 3mm hole [form="♀ (female)"]  # not connected
  3mm_hole1_2 = 3mm hole [form="♀ (female)"]  # not connected
  jack = mono mini jack
  LED1 = Red LED - 5mm
  arrow1 = arrow  # not connected
  A1 = A  # not connected
  3mm_hole1_3 = 3mm hole [form="♀ (female)"]  # not connected
  100uF = Electrolytic Capacitor [package=THT]
  2_2k = Resistor [resistance=220 package=THT]
  100nf_2 = Ceramic Capacitor [package=THT]
  hole1 = header hole
  100nf_3 = header hole
  hole1_2 = header hole
  hole1_3 = header hole
  hole1_4 = header hole
  hole1_5 = header hole
  hole1_6 = header hole
  hole1_7 = header hole
  hole1_8 = header hole
  hole1_9 = header hole
  hole1_10 = header hole
  hole1_11 = header hole
  hole1_12 = header hole
  hole1_13 = header hole
  hole1_14 = header hole
  Gieskes_WTR = DIN-5 jack (MIDI)
  G = header hole
  5v = header hole
  470 = header hole
  hole1_15 = header hole
  >| = header hole
  hole1_16 = header hole
  220 = header hole
  hole1_17 = header hole
  100k = header hole
  220_2 = header hole
  hole1_18 = header hole
  hole1_19 = header hole
  2_2k_2 = header hole
  3mm_hole1_4 = 3mm hole [form="♀ (female)"]  # not connected
  3_3k = Resistor [resistance=220 package=THT]
  Switch1 = Pushbutton 12mm omron
  hole1_20 = header hole  # not connected
  hole1_21 = header hole  # not connected
  hole1_22 = header hole  # not connected
  hole1_23 = header hole  # not connected
  hole1_24 = header hole  # not connected
  hole1_25 = header hole  # not connected
  hole1_26 = header hole  # not connected
  hole1_27 = header hole  # not connected
  hole1_28 = header hole  # not connected
  hole1_29 = header hole  # not connected
  hole1_30 = header hole  # not connected
  hole1_31 = header hole  # not connected
  hole1_32 = header hole  # not connected
  hole1_33 = header hole  # not connected
  hole1_34 = header hole  # not connected
  hole1_35 = header hole  # not connected
  hole1_36 = header hole  # not connected
  hole1_37 = header hole  # not connected
  hole1_38 = header hole  # not connected
  hole1_39 = header hole  # not connected
  hole1_40 = header hole  # not connected
  hole1_41 = header hole  # not connected
  hole1_42 = header hole  # not connected
  hole1_43 = header hole  # not connected
  hole1_44 = header hole  # not connected
  hole1_45 = header hole  # not connected
  hole1_46 = header hole  # not connected
  hole1_47 = header hole  # not connected
  hole1_48 = header hole  # not connected
  hole1_49 = header hole
  hole1_50 = header hole
  16mhz = header hole
  10k = header hole
  220_3 = header hole
  supply1 = supply  # not connected
  gnd = header hole
  hole1_51 = header hole  # not connected
  hole1_52 = header hole  # not connected
  hole1_53 = header hole
  hole1_54 = header hole
  hole1_55 = header hole
  hole1_56 = header hole

nets:
  N1: pot.leg2, Power_plug1.pin_2, 7805.GND, 4n28.Pin_4, Atmega328.Pin_8, Atmega328.Pin_22, 100u.-, 100u_2.-, 1n4001.anode, jack.pin_2, 100uF.-, 2_2k.Pin_1, 100nf_2.pin_0, hole1.pin_0, G.pin_0, hole1_15.pin_0, Switch1.Pin_2, 16mhz.pin_0, gnd.pin_0, hole1_56.pin_0
  N2: pot.no_name_yet#3, Atmega328.Pin_27, hole1_12.pin_0
  N3: pot.no_name_yet#4, 7805.output_voltage, Atmega328.Pin_7, Atmega328.Pin_20, 100u_2.+, 100uF.+, 100nf_3.pin_0, 5v.pin_0, 3_3k.Pin_0, 10k.pin_0
  N4: Power_plug1.pin_1, 7805.input_voltage, 100u.+, 1n4001.cathode
  N5: 4n28.Pin_1, hole1_16.pin_0, 220.pin_0
  N6: 4n28.Pin_2, Gieskes_WTR.5, >|.pin_0
  N7: 4n28.Pin_5, Atmega328.Pin_2, 3_3k.Pin_1, hole1_53.pin_0
  N8: 4n28.Pin_6, 100k.pin_0
  N9: Atmega328.Pin_1, 100nf.pin_0, 220_3.pin_0
  N10: Atmega328.Pin_3, hole1_54.pin_0
  N11: Atmega328.Pin_4, Atmega328.Pin_5, 220_2.pin_0, Switch1.Pin_4
  N12: Atmega328.Pin_6, LED1.cathode
  N13: Atmega328.Pin_9, hole1_50.pin_0
  N14: Atmega328.Pin_10, hole1_49.pin_0
  N15: Atmega328.Pin_12, hole1_4.pin_0
  N16: Atmega328.Pin_13, hole1_3.pin_0
  N17: Atmega328.Pin_14, hole1_2.pin_0
  N18: Atmega328.Pin_15, hole1_19.pin_0
  N19: Atmega328.Pin_16, hole1_5.pin_0
  N20: Atmega328.Pin_17, hole1_6.pin_0
  N21: Atmega328.Pin_18, hole1_7.pin_0
  N22: Atmega328.Pin_19, hole1_8.pin_0
  N23: Atmega328.Pin_21, hole1_18.pin_0
  N24: Atmega328.Pin_23, hole1_9.pin_0
  N25: Atmega328.Pin_24, hole1_11.pin_0
  N26: Atmega328.Pin_25, hole1_10.pin_0
  N27: Atmega328.Pin_26, hole1_13.pin_0
  N28: Atmega328.Pin_28, hole1_14.pin_0
  N29: 1uF.-, jack.pin_1
  N30: 1uF.+, 2_2k.Pin_0, 100nf_2.pin_1, 2_2k_2.pin_0
  N31: 100nf.pin_1, hole1_55.pin_0
  N32: LED1.anode, 470.pin_0
  N33: Gieskes_WTR.4, hole1_17.pin_0

custom parts:
  Big Potentiometer: A standard adjustable resistor (potentiometer).
  Power plug: power plug
  3mm hole: Generic female header
  header hole: hole
  DIN-5 jack (MIDI): Female DIN connector with 5 pins, as used for MIDI and SYNC
  Pushbutton 12mm omron: A generic pushbutton. 12mm
