# Fritzing sketch WatchBinary (saved by Fritzing 0.5.2b)
breadboards: 1

parts:
  LED1 = Red LED - 5mm [package="5 mm [THT]"]
  R1 = Resistor [resistance=10 package=THT]
  R2 = Resistor [resistance=10 package=THT]
  LED2 = Red LED - 5mm [package="5 mm [THT]"]
  R3 = Resistor [resistance=10 package=THT]
  LED3 = Red LED - 5mm [package="5 mm [THT]"]
  R4 = Resistor [resistance=10 package=THT]
  LED4 = Red LED - 5mm [package="5 mm [THT]"]
  R5 = Resistor [resistance=10 package=THT]
  LED5 = Red LED - 5mm [package="5 mm [THT]"]
  R6 = Resistor [resistance=10 package=THT]
  LED6 = Red LED - 5mm [package="5 mm [THT]"]
  R7 = Resistor [resistance=10 package=THT]
  R8 = Resistor [resistance=10 package=THT]
  R9 = Resistor [resistance=10 package=THT]
  R10 = Resistor [resistance=10 package=THT]
  LED7 = Red LED - 5mm [package="5 mm [THT]"]
  LED8 = Red LED - 5mm [package="5 mm [THT]"]
  LED9 = Red LED - 5mm [package="5 mm [THT]"]
  LED10 = Red LED - 5mm [package="5 mm [THT]"]
  S1 = Pushbutton [package="[THT]"]
  S2 = Pushbutton [package="[THT]"]
  R11 = Resistor [resistance=10 package=THT]
  Arduino = Arduino
  R11_2 = Resistor [resistance=10 package=THT]

nets:
  N1: LED1.cathode, R1.Pin_0
  N2: LED1.anode, LED2.anode, LED3.anode, LED4.anode, LED5.anode, LED6.anode, LED7.anode, LED8.anode, LED9.anode, LED10.anode, R11.Pin_0, Arduino.GND, R11_2.Pin_0
  N3: R1.Pin_1, Arduino.D13
  N4: R2.Pin_0, LED2.cathode
  N5: R2.Pin_1, Arduino.D12
  N6: R3.Pin_0, LED3.cathode
  N7: R3.Pin_1, Arduino.D11
  N8: R4.Pin_0, LED4.cathode
  N9: R4.Pin_1, Arduino.D10
  N10: R5.Pin_0, LED5.cathode
  N11: R5.Pin_1, Arduino.D9
  N12: R6.Pin_0, LED6.cathode
  N13: R6.Pin_1, Arduino.D8
  N14: R7.Pin_0, LED7.cathode
  N15: R7.Pin_1, Arduino.D4
  N16: R8.Pin_0, LED8.cathode
  N17: R8.Pin_1, Arduino.D5
  N18: R9.Pin_0, LED9.cathode
  N19: R9.Pin_1, Arduino.D6
  N20: R10.Pin_0, LED10.cathode
  N21: R10.Pin_1, Arduino.D7
  N22: S1.Pin_1, S1.Pin_2, R11.Pin_1, Arduino.D3
  N23: S1.Pin_3, S1.Pin_4, S2.Pin_3, S2.Pin_4
  N24: S2.Pin_1, S2.Pin_2, Arduino.D2, R11_2.Pin_1
