# Fritzing sketch Wiring (saved by Fritzing 0.5.2b)
breadboards: 1

parts:
  Arduino = Arduino
  ADXL3451 = 3-Axis Accelerometer Breakout
  R1 = Resistor [resistance=10k package=THT]
  R2 = Resistor [resistance=10k package=THT]
  Blue_SMiRF = BlueSMiRF Silver
  S1 = Basic Servo
  S2 = Basic Servo

nets:
  GND: Arduino.GND, ADXL3451.connector17, ADXL3451.connector22, Blue_SMiRF.connector3, S1.gnd, S2.gnd
  N1: Arduino.D11, S1.pulse
  N2: Arduino.D10, S2.pulse
  N3: Arduino.D1TX, Blue_SMiRF.connector1
  N4: Arduino.D0RX, Blue_SMiRF.connector2
  N5: Arduino.3V3, ADXL3451.connector18, ADXL3451.connector19, R1.Pin_0, R2.Pin_0
  VCC: Arduino.+5V, Blue_SMiRF.connector4, S1.vcc, S2.vcc
  N6: Arduino.A4, ADXL3451.connector23, R2.Pin_1
  N7: Arduino.A5, ADXL3451.connector24, R1.Pin_1
