# Fritzing sketch Wiring (saved by Fritzing 0.5.2b)
breadboards: 1

parts:
  Arduino = Arduino
  ADXL3451 = 3-Axis Accelerometer Breakout
  R1 = Resistor [resistance=10k package=THT]
  R2 = Resistor [resistance=10k package=THT]
  Blue_SMiRF = BlueSMiRF Silver
  S1 = Basic Servo
  S2 = Basic Servo

nets:
  GND: Arduino.GND, ADXL3451.GND, ADXL3451.SDO, Blue_SMiRF.GND, S1.gnd, S2.gnd
  N1: Arduino.D11, S1.pulse
  N2: Arduino.D10, S2.pulse
  N3: Arduino.D1TX, Blue_SMiRF.RX
  N4: Arduino.D0RX, Blue_SMiRF.TX
  3V3: Arduino.3V3, ADXL3451.VCC, ADXL3451.CS, R1.Pin_0, R2.Pin_0
  VCC: Arduino.+5V, Blue_SMiRF.VCC, S1.vcc, S2.vcc
  N5: Arduino.A4, ADXL3451.SDA, R2.Pin_1
  N6: Arduino.A5, ADXL3451.SCL, R1.Pin_1

custom parts:
  3-Axis Accelerometer Breakout: Accelerometer for sensing three-dimensional orientation/acceleration on a breakout board.
  BlueSMiRF Silver: Small and conviently packaged bluetooth serial radio modem
