# Fritzing sketch advent (saved by Fritzing 0.6.3b)
breadboards: 1

parts:
  DI1 = 7-Segment LED Display [package=THT]
  DI2 = 7-Segment LED Display [package=THT]
  IC1 = IC, DIP package, 16 pins [chip_label=4026 spacing=300mil]
  IC2 = IC, DIP package, 16 pins [chip_label=4026 spacing=300mil]
  S1 = Pushbutton [package="[THT]"]
  VCC1 = Battery block 9V
  R1 = Resistor [tolerance=±5% resistance=10k package="0603 [SMD]"]
  R2 = Resistor [tolerance=±5% resistance=330 package=THT]
  R3 = Resistor [tolerance=±5% resistance=330 package=THT]

nets:
  N1: DI1.commAnode#7, R3.Pin_1
  N2: DI2.cathodeE, IC1.pin11
  N3: DI2.cathodeD, IC1.pin9
  N4: DI2.cathodeC, IC1.pin13
  N5: DI2.cathodeDP, IC1.pin3, IC1.pin16, IC2.pin3, IC2.pin16, S1.Pin_3, S1.Pin_4, VCC1.+
  N6: DI2.cathodeB, IC1.pin12
  N7: DI2.cathodeA, IC1.pin10
  N8: DI2.commAnode#7, R2.Pin_1
  N9: DI2.cathodeF, IC1.pin6
  N10: DI2.cathodeG, IC1.pin7
  N11: IC1.pin1, S1.Pin_1, S1.Pin_2, R1.Pin_0
  N12: IC1.pin2, IC1.pin4, IC1.pin8, IC1.pin14, IC1.pin15, IC2.pin2, IC2.pin4, IC2.pin8, IC2.pin14, IC2.pin15, VCC1.-, R1.Pin_1, R2.Pin_0, R3.Pin_0
  N13: IC1.pin5, IC2.pin1
