# Fritzing sketch amblone-v1 (saved by Fritzing 0.4.3b)
breadboards: 1

parts:
  Arduino1 = Arduino
  ULN2003a = ULN2003A [package="DIP16 [THT]"]
  Power_plug1 = Power plug
  Ethernet_to_Channel_1 = RJ45
  Ethernet_to_Channel_2 = RJ45

nets:
  GND: Arduino1.GND, ULN2003a.0V, Power_plug1.GND
  N1: Arduino1.D11, ULN2003a.In_1
  N2: Arduino1.D10, ULN2003a.In_2
  N3: Arduino1.D9, ULN2003a.In_3
  N4: Arduino1.D6, ULN2003a.In_4
  N5: Arduino1.D5, ULN2003a.In_5
  N6: Arduino1.D3, ULN2003a.In_6
  N7: ULN2003a.Out_7, Ethernet_to_Channel_2.connector4
  N8: ULN2003a.Out_6, Ethernet_to_Channel_2.connector2
  N9: ULN2003a.Out_5, Ethernet_to_Channel_2.connector0
  N10: ULN2003a.Out_3, Ethernet_to_Channel_1.connector4
  N11: ULN2003a.Out_2, Ethernet_to_Channel_1.connector2
  N12: ULN2003a.Out_1, Ethernet_to_Channel_1.connector0
  N13: Power_plug1.VCC, Ethernet_to_Channel_1.connector6, Ethernet_to_Channel_2.connector6

notes:
  12v Input
  To RGB LED Strip 1
  To RGB LED Strip 2
  This variation allows you to utilise standard ethernet cable + RJ45 Connections to provide power/control to your LED strips.
  If you wanted to you could get 2 strips running off one cable, I didn't because they were sitting a little way apart.
