# Fritzing sketch analog-input-potentiometer_AnalogInputPot (saved by Fritzing 0.3.2b)
breadboards: 1

parts:
  LED1 = Red LED - 5mm
  R1 = Rotary Potentiometer (Large) [package=THT]
  Arduino2 = Arduino

nets:
  N1: LED1.cathode, R1.leg2, Arduino2.GND
  N2: LED1.anode, Arduino2.D13
  N3: R1.leg1, Arduino2.+5V
  N4: R1.wiper, Arduino2.A3

notes:
  In this example, potentiometer values are read in through an 'Analog In' pin. The values are then used to control the blinking rate of an LED. Related example: http://arduino.cc/en/Tutorial/AnalogInput
