# Fritzing sketch analog-input-to-servo_AnalogInputToServo (saved by Fritzing 0.3.2b)
breadboards: 1

parts:
  J1 = Basic Servo
  R1 = Rotary Potentiometer (Large) [package=THT]
  Arduino2 = Arduino

nets:
  GND: J1.gnd, R1.leg2, Arduino2.GND
  VCC: J1.vcc, R1.leg1, Arduino2.+5V
  N1: J1.pulse, Arduino2.D9
  N2: R1.wiper, Arduino2.A2

notes:
  In this example, potentiometer values are read in through an 'Analog In' pin. The values are then used to control the position of a servo motor. Related examples: http://arduino.cc/en/Tutorial/AnalogInput http://arduino.cc/en/Tutorial/Knob
