# Fritzing sketch analogAV (saved by Fritzing 0.5.2b)
breadboards: 1

parts:
  4067 = IC, DIP package, 24 pins [chip_label=4067 spacing=600mil]
  4040 = IC, DIP package, 16 pins [chip_label=4040 spacing=300mil]
  40106 = IC, DIP package, 14 pins [chip_label=40106 spacing=300mil]
  R1 = Rotary Potentiometer (Large) [package=THT]
  R2 = Rotary Potentiometer (Large) [package=THT]
  R3 = Rotary Potentiometer (Large) [package=THT]
  R4 = Rotary Potentiometer (Large) [package=THT]
  C1 = Electrolytic Capacitor [capacitance=100nF rated_voltage=35V package="100 mil [THT, electrolytic]"]
  C2 = Ceramic Capacitor [capacitance=100nF rated_voltage=35V package="100 mil [THT, multilayer]"]
  R5 = Resistor [resistance=2.2k package=THT]
  R6 = Resistor [resistance=2.2k package=THT]
  R7 = Resistor [resistance=220 package=THT]
  R8 = Resistor [resistance=220 package=THT]
  R9 = Resistor [resistance=220 package=THT]
  R10 = Resistor [resistance=220 package=THT]
  R11 = Resistor [resistance=220 package=THT]
  R12 = Resistor [resistance=220 package=THT]
  R13 = Resistor [resistance=220 package=THT]
  R14 = Resistor [resistance=220 package=THT]
  R15 = Resistor [resistance=220 package=THT]
  R16 = Resistor [resistance=220 package=THT]
  R17 = Resistor [resistance=220 package=THT]
  R18 = Resistor [resistance=220 package=THT]
  R19 = Resistor [resistance=220 package=THT]
  R20 = Resistor [resistance=220 package=THT]
  R21 = Resistor [resistance=220 package=THT]
  R22 = Resistor [resistance=22k package=THT]
  R23 = Resistor [resistance=2.2k package=THT]
  jack = Stereo Jack (TRS) 3.5mm [package="PG203J [THT]"]
  R24 = Resistor [resistance=47k package=THT]
  C3 = Ceramic Capacitor [capacitance=0.33mF rated_voltage=35V package="100 mil [THT, multilayer]"]
  S1 = Toggle Switch [package=THT]
  D1 = Rectifier Diode [package="300 mil [THT]"]
  Power = Power plug
  LED1 = Red LED - 5mm [package="5 mm [THT]"]
  R25 = Resistor [resistance=1k package=THT]
  J1 = female pin header, 8 pins [form="♀ (female)"]
  J2 = female pin header, 8 pins [form="♀ (female)"]
  J1_2 = female pin header, 8 pins [form="♀ (female)"]
  J2_2 = female pin header, 8 pins [form="♀ (female)"]
  J4 = female pin header, 9 pins [form="♀ (female)"]
  J3 = female pin header, 9 pins [form="♀ (female)"]
  J3_2 = female pin header, 9 pins [form="♀ (female)"]
  J4_2 = female pin header, 9 pins [form="♀ (female)"]
  S2 = Toggle Switch [package=THT]  # not connected
  Parte1 = LCD DISPLAY (from obsolete laptops)

nets:
  N1: 4067.pin1, R4.wiper, R22.Pin_1, J4.pin1, J4_2.pin1
  N2: 4067.pin2, R13.Pin_0, R14.Pin_1, J4.pin2, J4_2.pin2
  N3: 4067.pin3, R12.Pin_0, R13.Pin_1, J4.pin3, J4_2.pin3, Parte1.connector1
  N4: 4067.pin4, R11.Pin_0, R12.Pin_1, J4.pin4, J4_2.pin4
  N5: 4067.pin5, R10.Pin_0, R11.Pin_1, J4.pin5, J4_2.pin5
  N6: 4067.pin6, R9.Pin_0, R10.Pin_1, J4.pin6, J4_2.pin6
  N7: 4067.pin7, R8.Pin_0, R9.Pin_1, J4.pin7, J4_2.pin7
  N8: 4067.pin8, R7.Pin_0, R8.Pin_1, J4.pin8, J4_2.pin8
  N9: 4067.pin9, 40106.pin12, R1.leg2, R7.Pin_1, J4.pin9, J4_2.pin9
  N10: 4067.pin10, 4040.pin9, J2.pin8, J2_2.pin8, Parte1.connector11
  N11: 4067.pin11, 4040.pin7, J1.pin7, J1_2.pin7
  GND: 4067.pin12, 4067.pin15, 4040.pin8, 4040.pin11, 40106.pin7, R4.leg2, C1.-, C2.0, R23.Pin_1, jack.Sleeve, C3.1, Power.GND, R25.Pin_1, J1.pin8, J2.pin6, J1_2.pin8, J2_2.pin6, Parte1.connector10
  N12: 4067.pin13, 4040.pin5, J1.pin5, J1_2.pin5
  N13: 4067.pin14, 4040.pin6, R24.Pin_1, J1.pin6, J1_2.pin6
  N14: 4067.pin16, R21.Pin_1, J3.pin9, J3_2.pin9
  N15: 4067.pin17, R20.Pin_1, R21.Pin_0, J3.pin8, J3_2.pin8
  N16: 4067.pin18, R19.Pin_1, R20.Pin_0, J3.pin7, J3_2.pin7
  N17: 4067.pin19, R18.Pin_1, R19.Pin_0, J3.pin6, J3_2.pin6
  N18: 4067.pin20, R17.Pin_1, R18.Pin_0, J3.pin5, J3_2.pin5
  N19: 4067.pin21, R16.Pin_1, R17.Pin_0, J3.pin4, J3_2.pin4, Parte1.connector4
  N20: 4067.pin22, R15.Pin_1, R16.Pin_0, J3.pin3, J3_2.pin3
  N21: 4067.pin23, R14.Pin_0, R15.Pin_0, J3.pin2, J3_2.pin2
  5V: 4067.pin24, 4040.pin16, 40106.pin14, D1.cathode, J2.pin1, J2_2.pin1, J3.pin1, J3_2.pin1
  N22: 4040.pin1, J1.pin1, J1_2.pin1
  N23: 4040.pin2, J1.pin2, J1_2.pin2, Parte1.connector6
  N24: 4040.pin3, J1.pin3, J1_2.pin3
  N25: 4040.pin4, J1.pin4, J1_2.pin4
  N26: 4040.pin10, 40106.pin2, R2.leg2, LED1.anode, J2.pin7, J2_2.pin7, Parte1.connector8
  N27: 4040.pin12, J2.pin5, J2_2.pin5
  N28: 4040.pin13, J2.pin4, J2_2.pin4
  N29: 4040.pin14, J2.pin3, J2_2.pin3
  N30: 4040.pin15, J2.pin2, J2_2.pin2
  N31: 40106.pin1, C1.+, R5.Pin_0
  N32: 40106.pin13, C2.1, R6.Pin_0
  N33: R1.wiper, R6.Pin_1
  N34: R2.wiper, R5.Pin_1
  N35: R3.leg1, jack.Tip, C3.0
  N36: R3.wiper, R24.Pin_0
  N37: R22.Pin_0, R23.Pin_0, jack.Ring
  N38: S1.L1, S1.L2, Power.VCC
  N39: S1.COM, D1.anode
  N40: LED1.cathode, R25.Pin_0

notes:
  Remix de un circuito de Sebastian Tomczak
  http://www.milkcrate.com.au/_other/sea-moss/
  laboratorio
  de
  juguete
  http://toylab.wordpress.com/
  Este circuito es una varación de un diseño de Sebastian Tomczak
  http://www.milkcrate.com.au/_other/sea-moss/
  Fue realizado especialmente para el taller AnalogAV en PANORAMICA
  http://www.panoramica.cc/
  Podés conectar al display LCD cualquier pulso proveniente de los pines hembra del circuito y hacer diferentes combinaciones. . Sólo recordá conectar al menos un cable a tierra (aunque puede funcionar de todas maneras). Usá cocodrilos para las conecciones y pintá los conectores con pintura de grafito y/o plata (probá ambas pues tienen diferente respuesta visual). Mirá http://www.flickr.com/photos/laboratoriodejuguete/5479448466/
  This circuit is a variation of a Sebastina Tomczak design:
  http://www.milkcrate.com.au/_other/sea-moss/
  It was specially done for AnalogAV workshop on PANORAMICA
  http://www.panoramica.cc/
  You can conect any pulse coming out of the female pin headers to the displays and try different combinations.. Just remember make at least one ground connection (even though it may work anyway). Use alligators to make this conections and silver and/or graphite paint to draw connections on the LCD displays (try both, they have different visual results). See http://www.flickr.com/photos/laboratoriodejuguete/5479448466/
  El primer CI (40106) a la izquierda tiene dos multivibradores astables. El primero (con el capacitor electrolítico) es el reloj del circuito. El segundo (con el capacitor cerámico) genera el tono que escuchamos.
  The first IC (40106) on the left has two astables multivibrators. The first one (with the electrolytic capacitor) is the main clock of the circuit, the other one (with the ceramic capacitor) generates the tone that we hear.
  El CI del medio (4040) "divide" la frecuencia principal (proveniente del reloj) y es usado para controlar el tercer CI. TAmbién tomamos estas frequencias "divididas" para excitar el display LCD.
  The IC on the middle (4040) "divides" the main frequency (coming out of the clock) and is used to control the third IC. We also pick this "divided" frequencies to excite the LCD Display
  El tercer integrado (4067) es un multiplexor/ demultiplexor de 16 canales. De acuerdo a las patas de control conectadas al 4040, conectará la salida (pin 1) a un intervalo específico en la escalera de resistencias en serie, generando un efecto de ataque y decaimiento.
  Third IC (4067) is a multiplexor / demultiplexor of 16 channels. According to which adress pins are connected to 4040, it will connect the output to a specific interval on the resistors array, generating an attack/decay effect
