# Fritzing sketch arduino-eeprom (saved by Fritzing 0.5.2b)
breadboards: 1

parts:
  Arduino1 = Arduino
  IC1 = 24LC01 [package=THT]

nets:
  N1: Arduino1.GND, IC1.A0, IC1.A1, IC1.A2, IC1.0V, IC1.WP_-_Write_Protect
  N2: Arduino1.+5V, IC1.+V
  N3: Arduino1.A4, IC1.SDA_-_I2C_Data
  N4: Arduino1.A5, IC1.SCL_-_I2C_Clock
