# Fritzing sketch arduino (saved by Fritzing 0.5.2b)
breadboards: 1

parts:
  Arduino1 = Arduino
  LED8 = green LED - 5mm [package="5 mm [THT]"]
  LED9 = white LED - 5mm [package="5 mm [THT]"]
  LED10 = Blue LED - 5mm [package="5 mm [THT]"]
  LED5 = green LED - 5mm [package="5 mm [THT]"]
  LED6 = white LED - 5mm [package="5 mm [THT]"]
  LED7 = Blue LED - 5mm [package="5 mm [THT]"]
  R7 = Resistor [resistance=150 package=THT]
  R6 = Resistor [resistance=150 package=THT]
  R5 = Resistor [resistance=150 package=THT]
  R10 = Resistor [resistance=150 package=THT]
  R9 = Resistor [resistance=150 package=THT]
  R8 = Resistor [resistance=150 package=THT]
  LED1 = green LED - 5mm [package="5 mm [THT]"]
  LED3 = green LED - 5mm [package="5 mm [THT]"]
  LED4 = Blue LED - 5mm [package="5 mm [THT]"]
  LED2 = Blue LED - 5mm [package="5 mm [THT]"]
  R1 = Resistor [resistance=150 package=THT]
  R2 = Resistor [resistance=150 package=THT]
  R4 = Resistor [resistance=150 package=THT]
  R4_2 = Resistor [resistance=150 package=THT]

nets:
  N1: Arduino1.GND, LED8.cathode, LED9.cathode, LED10.cathode, LED5.cathode, LED6.cathode, LED7.cathode, LED1.cathode, LED3.cathode, LED4.cathode, LED2.cathode
  N2: Arduino1.D12, R10.Pin_1
  N3: Arduino1.D11, R9.Pin_1
  N4: Arduino1.D10, R8.Pin_1
  N5: Arduino1.D9, R7.Pin_1
  N6: Arduino1.D8, R6.Pin_1
  N7: Arduino1.D7, R5.Pin_1
  N8: Arduino1.D6, R4.Pin_1
  N9: Arduino1.D5, R4_2.Pin_1
  N10: Arduino1.D4, R2.Pin_1
  N11: Arduino1.D3, R1.Pin_1
  N12: LED8.anode, R8.Pin_0
  N13: LED9.anode, R9.Pin_0
  N14: LED10.anode, R10.Pin_0
  N15: LED5.anode, R5.Pin_0
  N16: LED6.anode, R6.Pin_0
  N17: LED7.anode, R7.Pin_0
  N18: LED1.anode, R1.Pin_0
  N19: LED3.anode, R4_2.Pin_0
  N20: LED4.anode, R4.Pin_0
  N21: LED2.anode, R2.Pin_0
