# Fritzing sketch arduinosignalgenerator (saved by Fritzing 0.3.16b)
breadboards: 1

parts:
  R1 = Resistor [resistance=220 package=THT]
  R2 = Resistor [resistance=220 package=THT]
  R3 = Resistor [resistance=220 package=THT]
  R4 = Resistor [resistance=220 package=THT]
  R5 = Resistor [resistance=220 package=THT]
  R6 = Resistor [resistance=220 package=THT]
  R7 = Resistor [resistance=220 package=THT]
  R8 = Resistor [resistance=220 package=THT]
  R9 = Resistor [resistance=220 package=THT]
  R11 = Resistor [resistance=220 package=THT]
  R12 = Resistor [resistance=220 package=THT]
  R13 = Resistor [resistance=220 package=THT]
  R14 = Resistor [resistance=220 package=THT]
  R15 = Resistor [resistance=220 package=THT]
  R17 = Resistor [resistance=220 package=THT]
  Arduino1 = Arduino
  R18 = Resistor [resistance=220 package=THT]
  J1 = Screw terminal - 2 pins [package=THT]

nets:
  N1: R1.Pin_0, R2.Pin_1, J1.pin1
  N2: R1.Pin_1, Arduino1.D7
  N3: R2.Pin_0, R3.Pin_0, R4.Pin_0
  N4: R3.Pin_1, Arduino1.D6
  N5: R4.Pin_1, R5.Pin_0, R11.Pin_0
  N6: R5.Pin_1, R6.Pin_0, R15.Pin_0
  N7: R6.Pin_1, R7.Pin_0, R14.Pin_0
  N8: R7.Pin_1, R8.Pin_0, R12.Pin_0
  N9: R8.Pin_1, R9.Pin_0, R13.Pin_0
  N10: R9.Pin_1, R17.Pin_0
  N11: R11.Pin_1, Arduino1.D5
  N12: R12.Pin_1, Arduino1.D2
  N13: R13.Pin_1, Arduino1.D1TX
  N14: R14.Pin_1, Arduino1.D3
  N15: R15.Pin_1, Arduino1.D4
  N16: R17.Pin_1, Arduino1.D0RX
  N17: Arduino1.GND, R18.Pin_1, J1.pin2
