# Fritzing sketch barebones-arduino_Arduino-no-FTDI-no-PwrSupply (saved by Fritzing 0.6.3b)
breadboards: 1

parts:
  U2 = atmega168 [package="DIP28 [THT]"]
  R1 = 1k Ω Resistor [package=THT]
  C3 = Ceramic Disk Capacitor [package=THT]
  C4 = Ceramic Disk Capacitor [package=THT]
  XTAL1 = Crystal [package=THT]
  Power_plug1 = Power plug
  J1 = female pin header, 6 pins [form="♀ (female)"]
  J2 = female pin header, 5 pins [form="♀ (female)"]
  J3 = female pin header, 5 pins [form="♀ (female)"]
  J4 = female pin header, 4 pins [form="♀ (female)"]

nets:
  N1: U2.Pin_1, R1.Pin_1
  N2: U2.Pin_2, J3.pin1
  N3: U2.Pin_3, J3.pin2
  N4: U2.Pin_4, J3.pin3
  N5: U2.Pin_5, J3.pin4
  N6: U2.Pin_6, J3.pin5
  N7: U2.Pin_7, U2.Pin_20, U2.Pin_21, R1.Pin_0, Power_plug1.VCC
  N8: U2.Pin_8, U2.Pin_22, C3.pin_1, C4.pin_0, Power_plug1.GND
  N9: U2.Pin_9, C4.pin_1, XTAL1.pin_0
  N10: U2.Pin_10, C3.pin_0, XTAL1.pin_1
  N11: U2.Pin_11, J4.pin1
  N12: U2.Pin_12, J4.pin2
  N13: U2.Pin_13, J4.pin3
  N14: U2.Pin_14, J4.pin4
  N15: U2.Pin_15, J2.pin5
  N16: U2.Pin_16, J2.pin4
  N17: U2.Pin_17, J2.pin3
  N18: U2.Pin_18, J2.pin2
  N19: U2.Pin_19, J2.pin1
  N20: U2.Pin_23, J1.pin6
  N21: U2.Pin_24, J1.pin5
  N22: U2.Pin_25, J1.pin4
  N23: U2.Pin_26, J1.pin3
  N24: U2.Pin_27, J1.pin2
  N25: U2.Pin_28, J1.pin1

notes:
  This is a breadboard Arduino without an FTDI chip. You can program the chip with a USB-Serial breakout board, by using an external programmer or by programming the MCU in an Arduino board and then popping it into this circuit. The power source should be at least 7 VDC. Related example: http://itp.nyu.edu/physcomp/Tutorials/ArduinoBreadboard
  Arduino Minimal
