# Fritzing sketch blinking-led_Blink (saved by Fritzing 0.3.2b)

parts:
  LED1 = Red LED - 5mm
  Arduino2 = Arduino

nets:
  N1: LED1.cathode, Arduino2.GND
  N2: LED1.anode, Arduino2.D13

notes:
  In this very simple example, Arduino will be programmed to blink the LED on pin 13. Related example: http://arduino.cc/en/Tutorial/Blink
