# Fritzing sketch blinky3 (saved by Fritzing 0.4.3b)
breadboards: 1

parts:
  atmega328 = atmega168 [package="DIP28 [THT]"]
  R19 = Resistor [resistance=10k package=THT]
  SW1 = Pushbutton [package=THT]
  C4 = Ceramic Capacitor [package=THT]
  C5 = Ceramic Capacitor [package=THT]
  REG = Voltage Regulator - 5V [package="TO220 [THT]"]
  Power = Power plug
  C7 = Ceramic Capacitor [package=THT]
  C8 = Electrolytic Capacitor [package=THT]
  C6 = Electrolytic Capacitor [package=THT]
  J1 = female pin header, 6 pins [form="♀ (female)"]
  Y1 = Resonator [package=THT]
  R10 = Resistor [resistance=220 package=THT]
  R12 = Resistor [resistance=100 package=THT]
  R11 = Resistor [resistance=220 package=THT]
  R13 = Resistor [resistance=220 package=THT]
  R14 = Resistor [resistance=220 package=THT]
  R15 = Resistor [resistance=220 package=THT]
  R16 = Resistor [resistance=220 package=THT]
  R17 = Resistor [resistance=220 package=THT]
  R18 = Resistor [resistance=220 package=THT]
  R3 = Resistor [resistance=220 package=THT]
  R2 = Resistor [resistance=220 package=THT]
  R1 = Resistor [resistance=220 package=THT]
  R4 = Resistor [resistance=220 package=THT]
  R5 = Resistor [resistance=220 package=THT]
  R6 = Resistor [resistance=220 package=THT]
  R7 = Resistor [resistance=220 package=THT]
  R8 = Resistor [resistance=220 package=THT]
  R9 = Resistor [resistance=220 package=THT]
  LED1 = RGB LED - (4 legs)
  LED2 = RGB LED - (4 legs)
  LED3 = RGB LED - (4 legs)
  LED6 = RGB LED - (4 legs)
  LED5 = RGB LED - (4 legs)
  LED4 = RGB LED - (4 legs)

nets:
  N1: atmega328.Pin_1, R19.Pin_0, SW1.leg0, C5.pin_1
  N2: atmega328.Pin_2, J1.pin2
  N3: atmega328.Pin_3, J1.pin3
  N4: atmega328.Pin_4, R1.Pin_1
  N5: atmega328.Pin_5, R2.Pin_1
  N6: atmega328.Pin_6, R3.Pin_1
  N7: atmega328.Pin_7, atmega328.Pin_20, atmega328.Pin_21, R19.Pin_1, C4.pin_0, REG.output_voltage, C7.pin_1, C8.+
  GND: atmega328.Pin_8, atmega328.Pin_22, SW1.leg1, C4.pin_1, REG.GND, Power.GND, C7.pin_0, C8.-, C6.-, J1.pin5, J1.pin6, Y1.GND, LED1.connector1, LED2.connector1, LED3.connector1, LED6.connector1, LED5.connector1, LED4.connector1
  N8: atmega328.Pin_9, Y1.0
  N9: atmega328.Pin_10, Y1.pin_1
  N10: atmega328.Pin_11, R4.Pin_0
  N11: atmega328.Pin_12, R5.Pin_0
  N12: atmega328.Pin_13, R6.Pin_0
  N13: atmega328.Pin_14, R7.Pin_1
  N14: atmega328.Pin_15, R8.Pin_1
  N15: atmega328.Pin_16, R9.Pin_1
  N16: atmega328.Pin_17, R12.Pin_0
  N17: atmega328.Pin_18, R11.Pin_0
  N18: atmega328.Pin_19, R10.Pin_0
  N19: atmega328.Pin_23, R15.Pin_0
  N20: atmega328.Pin_24, R14.Pin_0
  N21: atmega328.Pin_25, R13.Pin_0
  N22: atmega328.Pin_26, R16.Pin_0
  N23: atmega328.Pin_27, R17.Pin_0
  N24: atmega328.Pin_28, R18.Pin_0
  N25: C5.pin_0, J1.pin1
  N26: REG.input_voltage, Power.VCC, C6.+
  N27: R10.Pin_1, LED4.connector3
  N28: R12.Pin_1, LED4.connector0
  N29: R11.Pin_1, LED4.connector2
  N30: R13.Pin_1, LED5.connector3
  N31: R14.Pin_1, LED5.connector2
  N32: R15.Pin_1, LED5.connector0
  N33: R16.Pin_1, LED6.connector0
  N34: R17.Pin_1, LED6.connector2
  N35: R18.Pin_1, LED6.connector3
  N36: R3.Pin_0, LED1.connector3
  N37: R2.Pin_0, LED1.connector2
  N38: R1.Pin_0, LED1.connector0
  N39: R4.Pin_1, LED2.connector0
  N40: R5.Pin_1, LED2.connector2
  N41: R6.Pin_1, LED2.connector3
  N42: R7.Pin_0, LED3.connector0
  N43: R8.Pin_0, LED3.connector2
  N44: R9.Pin_0, LED3.connector3

notes:
  porkypine
  oakland, ca
  by theentropyworks
  for little guy.  we miss you.
  so fucking much.
  CC3.0-by-sa
