# Fritzing sketch blow_up_shield (saved by Fritzing 0.3.7b)
breadboards: 2

parts:
  Arduino1 = Arduino
  U2 = Voltage Regulator - 3.3V [package="TO220 [THT]"]
  J2 = Generic male header - 3 pins [package=THT]
  R2 = 100k Ω Resistor [package=THT]
  R3 = 100k Ω Resistor [package=THT]
  R6 = 220 Ω Resistor [package=THT]
  J5 = Screw terminal [package=THT]
  J6 = Screw terminal [package=THT]
  R7 = 220 Ω Resistor [package=THT]
  R8 = 220 Ω Resistor [package=THT]
  D1 = Rectifier Diode [package=THT]
  D1_2 = Rectifier Diode [package=THT]
  J9 = Generic female header - metal rounded - 3 pins [package=THT]
  R10 = 1k Ω Resistor [package=THT]
  R10_2 = 1k Ω Resistor [package=THT]
  R10_3 = 1k Ω Resistor [package=THT]
  J9_2 = Generic female header - metal rounded - 3 pins [package=THT]
  R11 = 100 Ω Resistor [package=THT]
  R12 = 100 Ω Resistor [package=THT]
  LED2 = green LED - 5mm
  LED3 = green LED - 5mm
  LED4 = yellow LED - 5mm
  FET1 = Basic FET N-Channel [package="TO220 [THT]"]
  FET2 = Basic FET N-Channel [package="TO220 [THT]"]
  C3 = Electrolytic Capacitor [package=THT]
  C4 = Ceramic Capacitor [package=THT]

nets:
  N1: Arduino1.GND, U2.input_voltage, R2.Pin_1, R3.Pin_1, R10.Pin_1, R10_2.Pin_1, R10_3.Pin_1, LED2.cathode, LED3.cathode, LED4.anode, FET1.source, FET2.source, C3.-, C4.pin_0
  N2: Arduino1.D6, R8.Pin_1, R11.Pin_0
  N3: Arduino1.D3, R7.Pin_0, R12.Pin_1
  N4: Arduino1.+5V, J2.pin3, R6.Pin_0, J9_2.pin1, J9_2.pin2, J9_2.pin3
  N5: Arduino1.VIN, U2.output_voltage, C4.pin_1
  N6: Arduino1.A0, J9.pin3, R10_3.Pin_0
  N7: Arduino1.A1, J9.pin2, R10_2.Pin_0
  N8: Arduino1.A2, J9.pin1, R10.Pin_0
  N9: U2.GND, J2.pin1, C3.+
  N10: J2.pin2, J5.pin1, J6.pin1, D1.cathode, D1_2.cathode
  N11: R2.Pin_0, R11.Pin_1, FET1.gate
  N12: R3.Pin_0, R12.Pin_0, FET2.gate
  N13: R6.Pin_1, LED4.cathode
  N14: J5.pin2, D1.anode, FET1.drain
  N15: J6.pin2, D1_2.anode, FET2.drain
  N16: R7.Pin_1, LED2.anode
  N17: R8.Pin_0, LED3.anode
