# Fritzing sketch bq3287rtc_design (saved by Fritzing 0.3.12b)
breadboards: 1

parts:
  IC2 = IC, DIP package, 24 pins [chip_label=bq3287 spacing=600mil]
  Arduino1 = Arduino

nets:
  N1: IC2.pin4, Arduino1.D2
  N2: IC2.pin5, Arduino1.D3
  N3: IC2.pin6, Arduino1.D4
  N4: IC2.pin7, Arduino1.D5
  N5: IC2.pin8, Arduino1.D6
  N6: IC2.pin9, Arduino1.D7
  N7: IC2.pin10, Arduino1.D8
  N8: IC2.pin11, Arduino1.D9
  N9: IC2.pin12, IC2.pin13, Arduino1.GND
  N10: IC2.pin14, Arduino1.D10
  N11: IC2.pin15, Arduino1.D11
  N12: IC2.pin16, Arduino1.D12
  N13: IC2.pin17, IC2.pin24, Arduino1.+5V
