# Fritzing sketch brightnessIndicatorPhotocell_withTweak (saved by Fritzing 0.6.3b)
breadboards: 1

parts:
  Arduino1 = Arduino
  LED1 = LED - 5mm [color="Red (633nm)" package="5 mm [THT]"]
  LED2 = LED - 5mm [color="Red (633nm)" package="5 mm [THT]"]
  LED3 = LED - 5mm [color="Red (633nm)" package="5 mm [THT]"]
  LED4 = LED - 5mm [color="Red (633nm)" package="5 mm [THT]"]
  LED5 = LED - 5mm [color="Red (633nm)" package="5 mm [THT]"]
  LED6 = LED - 5mm [color="Red (633nm)" package="5 mm [THT]"]
  R2 = Resistor [tolerance=±5% resistance=220 package=THT]
  R3 = Resistor [tolerance=±5% resistance=220 package=THT]
  R4 = Resistor [tolerance=±5% resistance=220 package=THT]
  R5 = Resistor [tolerance=±5% resistance=220 package=THT]
  R6 = Resistor [tolerance=±5% resistance=220 package=THT]
  R7 = Resistor [tolerance=±5% resistance=220 package=THT]
  R8 = Resistor [tolerance=±5% resistance=10k package=THT]
  R9 = Photocell (LDR) [package=THT]
  R10 = Rotary Potentiometer (Small) [maximum_resistance=100kΩ]

nets:
  N1: Arduino1.GND, LED1.cathode, LED2.cathode, LED3.cathode, LED4.cathode, LED5.cathode, LED6.cathode, R8.Pin_0, R10.leg1
  N2: Arduino1.D7, R2.Pin_1
  N3: Arduino1.D6, R3.Pin_1
  N4: Arduino1.D5, R7.Pin_1
  N5: Arduino1.D4, R4.Pin_1
  N6: Arduino1.D3, R5.Pin_1
  N7: Arduino1.D2, R6.Pin_1
  N8: Arduino1.+5V, R9.pin_1, R10.leg2
  N9: Arduino1.A0, R8.Pin_1, R9.pin_0
  N10: Arduino1.A1, R10.wiper
  N11: LED1.anode, R2.Pin_0
  N12: LED2.anode, R3.Pin_0
  N13: LED3.anode, R7.Pin_0
  N14: LED4.anode, R4.Pin_0
  N15: LED5.anode, R5.Pin_0
  N16: LED6.anode, R6.Pin_0

notes:
  Lights handling =
  based on forLoopIteration
  http://arduino.cc/en/Tutorial/ForLoop
  /*
  The circuit:
  * LEDs from pins 2 through 7 to ground
  This example code is in the public domain.
  see also http://www.arduino.cc/en/Tutorial/ForLoop for the wiring
  */
  int photocellPin = 0; // the cell and 10K pulldown are connected to a0
  int photocellReading; // the analog reading from the sensor divider
  int LEDbrightness; //
  int buttonState = 0; // variable for reading the pushbutton status
  const int DEBUG = true;
  void setup() {
  // use a for loop to initialize each pin as an output:
  for (int thisPin = 2; thisPin < 8; thisPin++) {
  pinMode(thisPin, OUTPUT);
  }
  Serial.begin(9600);
  }
  void loop() {
  photocellReading = analogRead(photocellPin);
  // LED gets brighter the darker it is at the sensor
  // that means we have to -invert- the reading from 0-1023 back to 1023-0
  photocellReading = 1023 - photocellReading;
  Serial.print("Analog reading = ");
  Serial.println(photocellReading); // the raw analog reading
  // you need to tweak here based on your ambient light
  LEDbrightness = abs(map(photocellReading, 0, 1023, 0, 7));
  // some console stuff
  if(DEBUG){
  Serial.print("Cell Read:"); // the raw analog reading
  Serial.println(photocellReading);
  Serial.print("LEDBrightnessVal: ");
  Serial.println(LEDbrightness);
  Serial.println(" ");
  // some delay for reading the debug
  delay(1000);
  }
  lightsBehavior(LEDbrightness);
  }
  // map the value to the pin
  void lightsBehavior(int val){
  pinLightCtrl(val,2,0);
  pinLightCtrl(val,3,1);
  pinLightCtrl(val,4,2);
  pinLightCtrl(val,5,3);
  pinLightCtrl(val,6,4);
  pinLightCtrl(val,7,5);
  }
  void pinLightCtrl(int val, int pin, int bggrThan){
  if(val > bggrThan){ digitalWrite(pin, HIGH);}else{digitalWrite(pin, LOW); }
  }
  photocell wireing based on photocell sketch
  http://www.ladyada.net/learn/sensors/cds.html
  /*
  The circuit:
  * LEDs from pins 2 through 7 to ground
  created 2006
  by David A. Mellis
  modified 5 Jul 2009
  by Tom Igoe
  This example code is in the public domain.
  http://www.arduino.cc/en/Tutorial/ForLoop
  * Photocell coming in on analog input
  based on examples from here
  http://www.ladyada.net/learn/sensors/cds.html
  * potentiometer coming in on analog input
  based on an example by Stefan Hermann
  http://fritzing.org/projects/color-fader/
  */
  int photocellPin = 0; // the cell and 10K pulldown are connected to a0
  int photocellReading; // the analog reading from the sensor divider
  int timer = 100; // The higher the number, the slower the timing.
  int LEDbrightness; //
  int sensorPin = 1; // this is the potentiometer on A1
  int tweak; // this value is for tweakin the range of the photocell adjusting the ambient light
  const int DEBUG = false;// This is for debug and never changes
  void setup() {
  // use a for loop to initialize each used digital pin as an output:
  for (int thisPin = 2; thisPin < 8; thisPin++) {
  pinMode(thisPin, OUTPUT);
  }
  // for the console
  if(DEBUG)Serial.begin(9600);
  }
  void loop() {
  tweak = analogRead(sensorPin); // the potentiometer sends values between 1023 - 0
  photocellReading = analogRead(photocellPin); // incoming from the photocell
  // LED gets brighter the darker it is at the sensor
  // that means we have to -invert- the reading from 0-1023 back to 1023-0
  photocellReading = 1023 - photocellReading;
  // some console / debugging stuff
  if(DEBUG){
  Serial.print("Analog reading on A0 = ");
  Serial.println(photocellReading); // the raw analog reading
  Serial.print("Analog reading on A1 = ");
  Serial.println(tweak); // the raw analog reading
  delay(1000);
  }
  // you need to tweak here based on your ambient light
  // so the values from the potentiometer are used to reduce the range
  LEDbrightness = abs(map(photocellReading, tweak, 1023, 0, 7));
  // some console / debugging stuff
  if(DEBUG){
  Serial.print("Cell Read:");
  Serial.println(photocellReading);
  Serial.print("LEDBrightnessVal: ");
  Serial.println(LEDbrightness);
  Serial.println(" ");
  delay(1000);
  }
  lightsBehavior(LEDbrightness); // turns the lights on and off depending on reding from potocell
  }
  /*
  * arg val is the brightness value mapped to the number of pins
  */
  void lightsBehavior(int val){
  // these are the pins
  pinLightCtrl(val,2,0);
  pinLightCtrl(val,3,1);
  pinLightCtrl(val,4,2);
  pinLightCtrl(val,5,3);
  pinLightCtrl(val,6,4);
  pinLightCtrl(val,7,5);
  }
  /*
  * arg val is the brightness value mapped to the number of pins (0 - 5)
  * arg int pin is the pin number
  * arg bggrThan if val is bigger than this value
  */
  void pinLightCtrl(int val, int pin, int bggrThan){
  if(val > bggrThan){
  digitalWrite(pin, HIGH);
  }else{
  digitalWrite(pin, LOW);
  }
  }
