# Fritzing sketch bussola_lcd (saved by Fritzing 0.6.2b)
breadboards: 1

parts:
  Arduino_Duemilanove = Arduino
  Componente1 = Compass Module - HMC6352
  R1 = Rotary Potentiometer (Small) [maximum_resistance=10kΩ]
  LM093XMLN_LCD = LCD_screen

nets:
  N1: Arduino_Duemilanove.D12, LM093XMLN_LCD.connector3
  N2: Arduino_Duemilanove.D11, LM093XMLN_LCD.connector5
  N3: Arduino_Duemilanove.D5, LM093XMLN_LCD.connector10
  N4: Arduino_Duemilanove.D4, LM093XMLN_LCD.connector11
  N5: Arduino_Duemilanove.D3, LM093XMLN_LCD.connector12
  N6: Arduino_Duemilanove.D2, LM093XMLN_LCD.connector13
  +5V: Arduino_Duemilanove.+5V, Componente1.VCC, R1.leg1, LM093XMLN_LCD.connector1
  GND: Arduino_Duemilanove.GND, Componente1.GND, R1.leg2, LM093XMLN_LCD.connector0, LM093XMLN_LCD.connector4
  N7: Arduino_Duemilanove.A4, Componente1.SDA
  N8: Arduino_Duemilanove.A5, Componente1.SCL
  N9: R1.wiper, LM093XMLN_LCD.connector2
