# Fritzing sketch calandria (saved by Fritzing 0.4.3b)
breadboards: 1

parts:
  IC1 = IC, DIP package, 14 pins [chip_label=40106 spacing=300mil]
  VCC1 = obsolete Battery
  D1 = Rectifier Diode [package="300 mil [THT]"]
  R1 = Photocell (LDR) [package=THT]
  R2 = Resistor [resistance=470 package=THT]
  LED1 = white LED - 5mm
  C1 = Ceramic Capacitor [package=THT]
  R3 = Rotary Potentiometer (Large) [package=THT]
  R4 = Resistor [resistance=1k package=THT]
  C2 = Electrolytic Capacitor [package=THT]
  R3_2 = Rotary Potentiometer (Large) [package=THT]
  J1 = Piezo Speaker
  TRS1 = Stereo Jack (TRS) 3.5mm [package="PG203J [THT]"]
  S1 = Toggle Switch [package=THT]

nets:
  N1: IC1.pin1, R1.pin_1, C1.pin_1
  N2: IC1.pin2, R3_2.leg1, J1.pin2, TRS1.Tip
  N3: IC1.pin7, VCC1.-, R2.Pin_1, C1.pin_0, C2.-, J1.pin1, TRS1.Sleeve
  N4: IC1.pin12, LED1.anode, R3.leg2
  N5: IC1.pin13, R4.Pin_0, C2.+
  N6: IC1.pin14, D1.cathode
  N7: VCC1.+, S1.COM
  N8: D1.anode, S1.L2
  N9: R1.pin_0, R3_2.wiper
  N10: R2.Pin_0, LED1.cathode
  N11: R3.wiper, R4.Pin_1

notes:
  laboratorio de juguete
  www.sudamericaexperimental.com
