# Fritzing sketch car_project (saved by Fritzing 0.6.2b)
breadboards: 1

parts:
  Sensor1 = female pin header, 2 pins [form="♀ (female)"]
  GSM_TXRX = female pin header, 2 pins [form="♀ (female)"]
  GSM_PW = female pin header, 2 pins [form="♀ (female)"]
  U2 = atmega168 [package="DIP28 [THT]"]
  J4 = female pin header, 2 pins [form="♀ (female)"]
  XTAL2 = Crystal [frequency="16 Mhz" package=THT]
  U3 = Voltage Regulator - 5V [package="TO220 [THT]"]
  R1 = Resistor [tolerance=±5% resistance=220 package=THT]
  J5 = female pin header, 2 pins [form="♀ (female)"]
  S1 = Pushbutton [package="[THT]"]
  LED1 = Red LED - 5mm [package="5 mm [THT]"]
  R2 = Resistor [tolerance=±5% resistance=220 package=THT]
  VCC1 = obsolete Battery
  R3 = Resistor [tolerance=±5% resistance=220 package=THT]
  C1 = Ceramic Capacitor [capacitance=100nF package="100 mil [THT, multilayer]"]
  C2 = Ceramic Capacitor [capacitance=100nF package="100 mil [THT, multilayer]"]
  C3 = Electrolytic Capacitor [capacitance=1µF package="100 mil [THT, electrolytic]"]
  J6 = Screw_terminal___2_pins
  J7 = female pin header, 2 pins [form="♀ (female)"]
  J8 = female pin header, 2 pins [form="♀ (female)"]
  Q1 = NPN_Transistor
  R4 = Resistor [tolerance=±5% resistance=220 package=THT]
  R5 = Resistor [tolerance=±5% resistance=220 package=THT]
  R6 = Resistor [tolerance=±5% resistance=220 package=THT]
  R7 = Resistor [tolerance=±5% resistance=220 package=THT]
  J9 = Screw_terminal___2_pins
  J10 = Screw_terminal___2_pins
  Part1 = Untitled_Part  # not connected
  R9 = Resistor [tolerance=±5% resistance=220 package=THT]
  BAT_JST = obsolete Battery
  J11 = Screw_terminal___2_pins
  Main_vcc = obsolete Battery
  R12 = Resistor [tolerance=±5% resistance=220 package=THT]
  R13 = Resistor [tolerance=±5% resistance=220 package=THT]
  L1 = Inductor [package="400 mil [THT]"]
  C4 = Ceramic Capacitor [capacitance=100nF package="100 mil [THT, multilayer]"]
  C5 = Ceramic Capacitor [capacitance=100nF package="100 mil [THT, multilayer]"]
  D1 = Rectifier Diode [part_number=1N4001 package="300 mil [THT]"]
  C6 = Ceramic Capacitor [capacitance=100nF package="100 mil [THT, multilayer]"]

nets (from the breadboard view):
  N1: Sensor1.pin1, GSM_PW.pin1, GSM_PW.pin2, U2.Pin_8, U2.Pin_22, U3.input_voltage, U3.GND, R1.Pin_1, S1.Pin_1, S1.Pin_2, LED1.anode, VCC1.-, VCC1.+, C1.0, C2.0, C3.-, C3.+, J10.connector0, J10.connector1, R9.Pin_1, BAT_JST.-, BAT_JST.+, J11.connector0, Main_vcc.-, R12.Pin_0, R13.Pin_1, C4.0, C5.1
  N2: Sensor1.pin2, GSM_TXRX.pin1, U2.Pin_4, U2.Pin_5, U2.Pin_23, J5.pin2, Q1.connector0, Q1.connector1, Q1.connector2, R4.Pin_0, R4.Pin_1, R5.Pin_1, R6.Pin_1, R7.Pin_1, R12.Pin_1, R13.Pin_0
  N3: GSM_TXRX.pin2, R6.Pin_0, R7.Pin_0
  N4: U2.Pin_1, U2.Pin_2, U2.Pin_3, U2.Pin_7, U2.Pin_20, J4.pin2, U3.output_voltage, S1.Pin_3, S1.Pin_4, R2.Pin_1, R3.Pin_0, R3.Pin_1, J6.connector1, J7.pin1, J7.pin2, J8.pin1, J8.pin2, R5.Pin_0, L1.pin_0, L1.pin_1, C4.1, C5.0, C6.0, C6.1
  N5: U2.Pin_9, U2.Pin_10, XTAL2.pin_0, XTAL2.pin_1, C1.1, C2.1
  N6: U2.Pin_14, J6.connector0
  N7: J4.pin1, J9.connector1
  N8: LED1.cathode, R2.Pin_0
  N9: J11.connector1, Main_vcc.+, D1.anode
