# Fritzing sketch christmasStar (saved by Fritzing 0.6.4b)
breadboards: 1

parts:
  LED1 = LED - 5mm [color="Red (633nm)" package="5 mm [THT]"]
  LED2 = LED - 5mm [color="Red (633nm)" package="5 mm [THT]"]
  LED3 = LED - 5mm [color="Red (633nm)" package="5 mm [THT]"]
  LED4 = LED - 5mm [color="Red (633nm)" package="5 mm [THT]"]
  R1 = Resistor [tolerance=±5% resistance=220 package=THT]
  J1 = female pin header, 5 pins [form="♀ (female)"]

nets:
  N1: LED1.cathode, LED2.cathode, LED3.cathode, LED4.cathode, R1.Pin_1
  N2: LED1.anode, J1.pin2
  N3: LED2.anode, J1.pin3
  N4: LED3.anode, J1.pin4
  N5: LED4.anode, J1.pin5
  N6: R1.Pin_0, J1.pin1
