# Fritzing sketch concurso1 (saved by Fritzing 0.6.2b)
breadboards: 1

parts:
  Arduino1 = Arduino
  LED1 = Red LED - 5mm [package="5 mm [THT]"]
  R1 = Resistor [tolerance=±5% resistance=330 package=THT]
  R2 = Resistor [tolerance=±5% resistance=330 package=THT]
  LED2 = Blue LED - 5mm [package="5 mm [THT]"]
  Pulsador_1 = Pushbutton [package="[THT]"]
  Pulsador_2 = Pushbutton [package="[THT]"]
  R3 = Resistor [tolerance=±5% resistance=10k package=THT]
  R4 = Resistor [tolerance=±5% resistance=10k package=THT]

nets:
  GND: Arduino1.GND, LED1.cathode, LED2.cathode, R3.Pin_1, R4.Pin_1
  N1: Arduino1.D5, Pulsador_2.Pin_3, Pulsador_2.Pin_4, R3.Pin_0
  N2: Arduino1.D4, Pulsador_1.Pin_3, Pulsador_1.Pin_4, R4.Pin_0
  N3: Arduino1.D3, R2.Pin_1
  N4: Arduino1.D2, R1.Pin_1
  5V: Arduino1.+5V, Pulsador_1.Pin_1, Pulsador_1.Pin_2, Pulsador_2.Pin_1, Pulsador_2.Pin_2
  N5: LED1.anode, R1.Pin_0
  N6: R2.Pin_0, LED2.anode

notes:
  Jugador 1
  Jugador 2
