# Fritzing sketch cristaliquidos (saved by Fritzing 0.5.2b)
breadboards: 3

parts:
  U1 = 555 Timer [package="DIP8 [THT]"]
  C1 = Electrolytic Capacitor [package=THT]
  R4 = Resistor [resistance=1k package=THT]
  LED1 = white LED - 5mm [package="5 mm [THT]"]
  R5 = Photocell (LDR) [package=THT]
  R6 = Photocell (LDR) [package=THT]
  R7 = Photocell (LDR) [package=THT]
  IC1 = IC, DIP package, 16 pins [chip_label=4040 spacing=300mil]
  J1 = female pin header, 5 pins [form="♀ (female)"]
  J2 = female pin header, 2 pins [form="♀ (female)"]
  IC2 = IC, DIP package, 16 pins [chip_label=4040 spacing=300mil]
  J4 = female pin header, 2 pins [form="♀ (female)"]
  J5 = female pin header, 5 pins [form="♀ (female)"]
  IC3 = IC, DIP package, 16 pins [chip_label=4017 spacing=300mil]
  J3 = female pin header, 7 pins [form="♀ (female)"]
  J6 = female pin header, 7 pins [form="♀ (female)"]
  J7 = female pin header, 10 pins [form="♀ (female)"]
  IC4 = IC, DIP package, 14 pins [chip_label=4093 spacing=300mil]
  C2 = Electrolytic Capacitor [capacitance=10µF rated_voltage=35V package="100 mil [THT, electrolytic]"]
  C3 = Electrolytic Capacitor [capacitance=10µF rated_voltage=35V package="100 mil [THT, electrolytic]"]
  C4 = Electrolytic Capacitor [capacitance=10µF rated_voltage=35V package="100 mil [THT, electrolytic]"]
  C5 = Electrolytic Capacitor [capacitance=10µF rated_voltage=35V package="100 mil [THT, electrolytic]"]
  R8 = Trimmer Potentiometer [package=THT]
  R9 = Trimmer Potentiometer [package=THT]
  R10 = Trimmer Potentiometer [package=THT]
  R11 = Trimmer Potentiometer [package=THT]
  J8 = Piezo Speaker
  J9 = Piezo Speaker
  J10 = Piezo Speaker
  J11 = Piezo Speaker
  IC5 = IC, DIP package, 14 pins [chip_label=4093 spacing=300mil]
  C6 = Electrolytic Capacitor [capacitance=10µF rated_voltage=35V package="100 mil [THT, electrolytic]"]
  C7 = Electrolytic Capacitor [capacitance=100nF rated_voltage=35V package="100 mil [THT, electrolytic]"]
  C8 = Electrolytic Capacitor [capacitance=100nF rated_voltage=35V package="100 mil [THT, electrolytic]"]
  C9 = Electrolytic Capacitor [capacitance=100nF rated_voltage=35V package="100 mil [THT, electrolytic]"]
  R12 = Trimmer Potentiometer [package=THT]
  R13 = Trimmer Potentiometer [package=THT]
  R14 = Trimmer Potentiometer [package=THT]
  R15 = Trimmer Potentiometer [package=THT]
  J12 = Piezo Speaker
  J13 = Piezo Speaker
  J14 = Piezo Speaker
  J15 = Piezo Speaker
  IC6 = IC, DIP package, 24 pins [chip_label=4067 spacing=600mil]
  J16 = female pin header, 8 pins [form="♀ (female)"]
  J17 = female pin header, 8 pins [form="♀ (female)"]
  IC7 = IC, DIP package, 16 pins [chip_label=4017 spacing=300mil]
  J18 = female pin header, 10 pins [form="♀ (female)"]
  Part2 = LCD DISPLAY (from obsolete laptops)
  Part1 = LCD DISPLAY (from obsolete laptops)

nets:
  GND: U1.Ground, C1.-, R4.Pin_0, IC1.pin8, IC1.pin11, IC2.pin8, IC2.pin11, IC3.pin8, IC3.pin13, IC3.pin15, IC4.pin7, C2.-, C3.-, C4.-, C5.-, J8.pin1, J9.pin1, J10.pin1, J11.pin1, IC5.pin7, C6.-, C7.-, C8.-, C9.-, J12.pin1, J13.pin1, J14.pin1, J15.pin1, IC6.pin12, IC6.pin15, IC7.pin8, IC7.pin13, IC7.pin15, Part2.connector18, Part1.connector12
  N1: U1.Trigger, U1.Threshold, C1.+, R6.pin_1
  N2: U1.Output, LED1.anode, IC1.pin10, J2.pin1, IC2.pin10, J4.pin1, IC7.pin14
  5V: U1.Reset, U1.Vcc_Supply_Voltage, R7.pin_1, IC1.pin16, J1.pin1, IC2.pin16, J5.pin1, IC3.pin16, IC4.pin14, IC5.pin14, IC6.pin1, IC6.pin24, IC7.pin16
  N3: U1.Discharge, R5.pin_0, R7.pin_0
  N4: R4.Pin_1, LED1.cathode
  N5: R5.pin_1, R6.pin_0
  N6: IC1.pin1, J3.pin1, Part1.connector18
  N7: IC1.pin2, J3.pin2
  N8: IC1.pin3, J3.pin3
  N9: IC1.pin4, J3.pin4, IC5.pin13
  N10: IC1.pin5, J3.pin5, IC5.pin8, Part2.connector2
  N11: IC1.pin6, J3.pin6, IC5.pin6
  N12: IC1.pin7, J3.pin7, IC5.pin1
  N13: IC1.pin9, J2.pin2
  N14: IC1.pin12, J1.pin5
  N15: IC1.pin13, J1.pin4
  N16: IC1.pin14, J1.pin3
  N17: IC1.pin15, J1.pin2
  N18: IC2.pin1, J6.pin1
  N19: IC2.pin2, J6.pin2
  N20: IC2.pin3, J6.pin3
  N21: IC2.pin4, J6.pin4, IC6.pin13
  N22: IC2.pin5, J6.pin5, IC6.pin14, Part1.connector11
  N23: IC2.pin6, J6.pin6, IC6.pin11
  N24: IC2.pin7, J6.pin7, IC6.pin10
  N25: IC2.pin9, J4.pin2
  N26: IC2.pin12, J5.pin5
  N27: IC2.pin13, J5.pin4
  N28: IC2.pin14, J5.pin3, Part1.connector6
  N29: IC2.pin15, J5.pin2
  N30: IC3.pin1, J7.pin6, IC4.pin8, Part1.connector13
  N31: IC3.pin2, J7.pin2
  N32: IC3.pin3, J7.pin1, IC4.pin1
  N33: IC3.pin4, J7.pin3, Part2.connector1
  N34: IC3.pin5, J7.pin7
  N35: IC3.pin6, J7.pin8
  N36: IC3.pin7, J7.pin4, IC4.pin6
  N37: IC3.pin9, J7.pin9, IC4.pin13
  N38: IC3.pin10, J7.pin5
  N39: IC3.pin11, J7.pin10, Part2.connector10
  N40: IC4.pin2, C2.+, R9.wiper
  N41: IC4.pin3, R9.leg1, J10.pin2
  N42: IC4.pin4, R11.wiper, J11.pin2
  N43: IC4.pin5, C5.+, R11.leg1
  N44: IC4.pin9, C4.+, R10.leg1
  N45: IC4.pin10, R10.wiper, J9.pin2
  N46: IC4.pin11, R8.wiper, J8.pin2
  N47: IC4.pin12, C3.+, R8.leg1
  N48: IC5.pin2, C7.+, R12.wiper
  N49: IC5.pin3, R12.leg1, J15.pin2
  N50: IC5.pin4, R13.wiper, J14.pin2
  N51: IC5.pin5, C9.+, R13.leg1
  N52: IC5.pin9, C8.+, R15.wiper
  N53: IC5.pin10, R15.leg1, J13.pin2
  N54: IC5.pin11, R14.wiper, J12.pin2
  N55: IC5.pin12, C6.+, R14.leg1
  N56: IC6.pin2, J17.pin1, Part2.connector19
  N57: IC6.pin3, J17.pin2
  N58: IC6.pin4, J17.pin3, Part2.connector14
  N59: IC6.pin5, J17.pin4
  N60: IC6.pin6, J17.pin5
  N61: IC6.pin7, J17.pin6
  N62: IC6.pin8, J17.pin7
  N63: IC6.pin9, J17.pin8
  N64: IC6.pin16, J16.pin8
  N65: IC6.pin17, J16.pin7
  N66: IC6.pin18, J16.pin6, Part2.connector4
  N67: IC6.pin19, J16.pin5
  N68: IC6.pin20, J16.pin4
  N69: IC6.pin21, J16.pin3
  N70: IC6.pin22, J16.pin2
  N71: IC6.pin23, J16.pin1, Part1.connector2
  N72: IC7.pin1, J18.pin6
  N73: IC7.pin2, J18.pin2
  N74: IC7.pin3, J18.pin1
  N75: IC7.pin4, J18.pin3
  N76: IC7.pin5, J18.pin7, Part2.connector6
  N77: IC7.pin6, J18.pin8
  N78: IC7.pin7, J18.pin4
  N79: IC7.pin9, J18.pin9
  N80: IC7.pin10, J18.pin5
  N81: IC7.pin11, J18.pin10, Part1.connector0

notes:
  Esta es la estructura básica de CRISTALÍQUIDA, instalación para ser montada en una ventana (ver http://vimeo.com/17603423 ) Es un timer (555) conectado a diversos contadores por década (4017), divisores (4040) y multiplexores (4067). Los pulsos salientes de estos integrados encienden y apagan 8 multivibradores astables (construidos con 4093 - compuertas NAND tal como enseña Nicolas Collins). que generan ondas de baja frecuencias audibles a través de los buzzers. Al mismo tiempo, estos pulsos van a los displayas LCD (provenientes de laptops descartadas u obsoletas), creando patrones visuales rítmicos. La frecuencia del timer varía de acuerdo a la luz ambiente (rápido durante el día, lento durante la noche), debido a las resistencias variables por luz (LDR) conectadas a las patas 6, 7 y 8 del 555.
  Podés conectar al display cualquier pulso proveniente de los pines hembra del circuito y hacer diferentes combinaciones. Incluso podés conectar las salidas que van a los buzzer. Sólo recordá conectar al menos un cable a tierra (aunque puede funcionar de todas maneras). Usá cocodrilos para las conecciones y pintá los conectores con pintura de grafito y/o plata (probá ambas pues tienen diferente respuesta visual). Mirá http://www.flickr.com/photos/laboratoriodejuguete/5479448466/
  Ajustá los presets (trimmers) de 1M para obetener la frecuencia de sonido deseada y agregá cuantos displays puedas conseguir (usan muy poco voltaje y corriente). Incluso podés alimentar el circuito con energía solar. Si lo hacés, por favor contactame que quisiera verlo.
  Perdón por el lío en el navegador PCD. Esta obra usa sólo protoboard.
  Comentarios y preguntas: h.cosas@gmail.com
  ENGLISH
  This is the basic structure of CRISTALÍQUIDA, an installation to be mounted on a window (see http://vimeo.com/17603423). It's a timer (555) connected to several decade counters (4017) , dividers (4040), multiplexers (4067). The pulses coming out of these ICs turns on an off 8 astable multivibrators (built with 4093 NAND gates, as taught by Nicolas Collins) than generates low frequency square waves listened through the piezo speakers. At the same time these pulses go to LCD Displays (from discarded obsolete laptops), creating rhythmic visual patterns. The frequency of the timer varies according to ambience light (fast at daylight, slow at nightime), due to the LDRs on pins 6, 7 and 8 of the 555 Timer.
  You can conect any pulse coming out of the female pin headers to the displays and try different combinations. You can even use the ouput of the oscillators. Just remember make at least one ground connection (even though it may work anyway). Use alligators to make this conections and silver and/or graphite paint to draw connections on the LCD displays (try both, they have different visual results). See http://www.flickr.com/photos/laboratoriodejuguete/5479448466/
  Adjust the trimmers (1M) to obtain the desired frequency and add as many displays as you can obtain (they use very low voltage and current). It can even work on solar energy. If you use solar panels, let me know. I'd love to see that.
  Sorry for the mess at the PCB navigator. This work just uses breadboards.
  Comments & questions: h.cosas@gmail.com
