# Fritzing sketch decodificador7segmentos (saved by Fritzing 0.4.3b)
breadboards: 1

parts:
  S1 = Pushbutton [package="[THT]"]
  S2 = Pushbutton [package="[THT]"]
  S3 = Pushbutton [package="[THT]"]
  S4 = Pushbutton [package="[THT]"]
  DI1 = 7-Segment LED Display [package=THT]
  IC1 = IC, DIP package, 16 pins [chip_label=SN74LS47N spacing=300mil]
  VCC1 = Battery block 9V
  R1 = Resistor [resistance=220 package=THT]
  R2 = Resistor [resistance=220 package=THT]
  R3 = Resistor [resistance=220 package=THT]
  R4 = Resistor [resistance=220 package=THT]

nets:
  N1: S1.Pin_1, S1.Pin_2, S2.Pin_1, S2.Pin_2, S3.Pin_1, S3.Pin_2, S4.Pin_1, S4.Pin_2, IC1.pin16, VCC1.+
  N2: S1.Pin_3, S1.Pin_4, IC1.pin2, R2.Pin_1
  N3: S2.Pin_3, S2.Pin_4, IC1.pin6, R3.Pin_1
  N4: S3.Pin_3, S3.Pin_4, IC1.pin1, R1.Pin_1
  N5: S4.Pin_3, S4.Pin_4, IC1.pin7, R4.Pin_1
  N6: DI1.cathodeE, IC1.pin9
  N7: DI1.cathodeD, IC1.pin10
  N8: DI1.cathodeC, IC1.pin11
  N9: DI1.cathodeB, IC1.pin12
  N10: DI1.cathodeA, IC1.pin13
  N11: DI1.cathodeF, IC1.pin15
  N12: DI1.cathodeG, IC1.pin14
  N13: IC1.pin8, VCC1.-, R1.Pin_0, R2.Pin_0, R3.Pin_0, R4.Pin_0

notes:
  D C B A
