# Fritzing sketch digital-input-button_Button (saved by Fritzing 0.3.2b)
breadboards: 1

parts:
  LED1 = Red LED - 5mm
  S1 = Pushbutton [package=THT]
  R1 = 10k Ω Resistor [package=THT]
  Arduino2 = Arduino

nets:
  N1: LED1.cathode, R1.Pin_0, Arduino2.GND
  N2: LED1.anode, Arduino2.D13
  N3: S1.leg0, Arduino2.+5V
  N4: S1.leg1, R1.Pin_1, Arduino2.D2

notes:
  In this example, a pushbutton is used as a digital input and an LED is a digital output. Related example: http://arduino.cc/en/Tutorial/Button
