# Fritzing sketch digital-inputoutput-traffic-light_TrafficLight (saved by Fritzing 0.3.2b)
breadboards: 1

parts:
  LED1 = Red LED - 5mm
  R1 = 220 Ω Resistor [package=THT]
  LED2 = yellow LED - 5mm
  R2 = 220 Ω Resistor [package=THT]
  LED3 = green LED - 5mm
  R3 = 220 Ω Resistor [package=THT]
  S1 = Pushbutton [package=THT]
  R4 = 220 Ω Resistor [package=THT]
  LED4 = Red LED - 5mm
  LED5 = green LED - 5mm
  R5 = 220 Ω Resistor [package=THT]
  R6 = 220 Ω Resistor [package=THT]
  Arduino2 = Arduino

nets:
  N1: LED1.cathode, LED2.cathode, LED3.cathode, R4.Pin_0, LED4.cathode, LED5.cathode, Arduino2.GND
  N2: LED1.anode, R1.Pin_0
  N3: R1.Pin_1, Arduino2.D12
  N4: LED2.anode, R2.Pin_0
  N5: R2.Pin_1, Arduino2.D11
  N6: LED3.anode, R3.Pin_0
  N7: R3.Pin_1, Arduino2.D10
  N8: S1.leg0, Arduino2.+5V
  N9: S1.leg1, R4.Pin_1, Arduino2.D2
  N10: LED4.anode, R5.Pin_0
  N11: LED5.anode, R6.Pin_0
  N12: R5.Pin_1, Arduino2.D8
  N13: R6.Pin_1, Arduino2.D9

notes:
  This circuit can be coded such that both the car and pedestrian traffic lights go through their normal cycle until the button is pressed by a pedestrian. In this case, the lights will change in favor of the pedestrian.
  Car Traffic Light
  Pedestrian Traffic Light
