# Fritzing sketch digital-output-npn-power-transistor_npnPowerTransistor (saved by Fritzing 0.3.2b)
breadboards: 1

parts:
  Q1 = npn-Powertransistor [package="TO220 [THT]"]
  R1 = 1k Ω Resistor [package=THT]
  LED1 = Red LED - 5mm
  R2 = 220 Ω Resistor [package=THT]
  LED2 = Red LED - 5mm
  R3 = 220 Ω Resistor [package=THT]
  LED3 = Red LED - 5mm
  R4 = 220 Ω Resistor [package=THT]
  LED4 = Red LED - 5mm
  R5 = 220 Ω Resistor [package=THT]
  Arduino2 = Arduino

nets:
  N1: Q1.base, R1.Pin_1
  N2: Q1.collector, LED1.cathode, LED2.cathode, LED3.cathode, LED4.cathode
  N3: Q1.emitter, Arduino2.GND
  N4: R1.Pin_0, Arduino2.D9
  N5: LED1.anode, R2.Pin_0
  N6: R2.Pin_1, R3.Pin_1, R4.Pin_1, R5.Pin_1, Arduino2.+5V
  N7: LED2.anode, R3.Pin_0
  N8: LED3.anode, R4.Pin_0
  N9: LED4.anode, R5.Pin_0

notes:
  Using a power transistor with an Arduino will allow you to control outputs that need more current or higher voltages than the Arduino can provide. Related example: http://itp.nyu.edu/physcomp/Tutorials/HighCurrentLoads
