# Fritzing sketch flipper (saved by Fritzing 0.6.3b)
breadboards: 7

parts:
  Teensy++1 = Teensy++ 2.0
  Switch1 = Pushbutton 12mm omron B3F-4050, B3F-5050, B3F-4055, B3F-5051 [part_number="b3f-4050, b3f5050, b3f-4055, b3f-5051"]
  Switch2 = Pushbutton 12mm omron B3F-4050, B3F-5050, B3F-4055, B3F-5051 [part_number="b3f-4050, b3f5050, b3f-4055, b3f-5051"]
  Switch3 = Pushbutton 12mm omron B3F-4050, B3F-5050, B3F-4055, B3F-5051 [part_number="b3f-4050, b3f5050, b3f-4055, b3f-5051"]
  Switch4 = Pushbutton 12mm omron B3F-4050, B3F-5050, B3F-4055, B3F-5051 [part_number="b3f-4050, b3f5050, b3f-4055, b3f-5051"]
  Switch5 = Pushbutton 12mm omron B3F-4050, B3F-5050, B3F-4055, B3F-5051 [part_number="b3f-4050, b3f5050, b3f-4055, b3f-5051"]
  Switch6 = Pushbutton 12mm omron B3F-4050, B3F-5050, B3F-4055, B3F-5051 [part_number="b3f-4050, b3f5050, b3f-4055, b3f-5051"]
  D1 = Rectifier Diode [part_number=1N4001 package="300 mil [THT]"]
  D2 = Rectifier Diode [part_number=1N4001 package="300 mil [THT]"]
  D3 = Rectifier Diode [part_number=1N4001 package="300 mil [THT]"]
  D4 = Rectifier Diode [part_number=1N4001 package="300 mil [THT]"]
  D5 = Rectifier Diode [part_number=1N4001 package="300 mil [THT]"]
  D6 = Rectifier Diode [part_number=1N4001 package="300 mil [THT]"]
  Switch7 = Pushbutton 12mm omron B3F-4050, B3F-5050, B3F-4055, B3F-5051 [part_number="b3f-4050, b3f5050, b3f-4055, b3f-5051"]
  Switch8 = Pushbutton 12mm omron B3F-4050, B3F-5050, B3F-4055, B3F-5051 [part_number="b3f-4050, b3f5050, b3f-4055, b3f-5051"]
  Switch9 = Pushbutton 12mm omron B3F-4050, B3F-5050, B3F-4055, B3F-5051 [part_number="b3f-4050, b3f5050, b3f-4055, b3f-5051"]
  D7 = Rectifier Diode [part_number=1N4001 package="300 mil [THT]"]
  D8 = Rectifier Diode [part_number=1N4001 package="300 mil [THT]"]
  D9 = Rectifier Diode [part_number=1N4001 package="300 mil [THT]"]
  Switch10 = Pushbutton 12mm omron B3F-4050, B3F-5050, B3F-4055, B3F-5051 [part_number="b3f-4050, b3f5050, b3f-4055, b3f-5051"]
  Switch11 = Pushbutton 12mm omron B3F-4050, B3F-5050, B3F-4055, B3F-5051 [part_number="b3f-4050, b3f5050, b3f-4055, b3f-5051"]
  Switch12 = Pushbutton 12mm omron B3F-4050, B3F-5050, B3F-4055, B3F-5051 [part_number="b3f-4050, b3f5050, b3f-4055, b3f-5051"]
  D10 = Rectifier Diode [part_number=1N4001 package="300 mil [THT]"]
  D11 = Rectifier Diode [part_number=1N4001 package="300 mil [THT]"]
  D12 = Rectifier Diode [part_number=1N4001 package="300 mil [THT]"]
  Switch13 = Pushbutton 12mm omron B3F-4050, B3F-5050, B3F-4055, B3F-5051 [part_number="b3f-4050, b3f5050, b3f-4055, b3f-5051"]
  D13 = Rectifier Diode [part_number=1N4001 package="300 mil [THT]"]
  Switch14 = Pushbutton 12mm omron B3F-4050, B3F-5050, B3F-4055, B3F-5051 [part_number="b3f-4050, b3f5050, b3f-4055, b3f-5051"]
  Switch15 = Pushbutton 12mm omron B3F-4050, B3F-5050, B3F-4055, B3F-5051 [part_number="b3f-4050, b3f5050, b3f-4055, b3f-5051"]
  Switch16 = Pushbutton 12mm omron B3F-4050, B3F-5050, B3F-4055, B3F-5051 [part_number="b3f-4050, b3f5050, b3f-4055, b3f-5051"]
  Switch17 = Pushbutton 12mm omron B3F-4050, B3F-5050, B3F-4055, B3F-5051 [part_number="b3f-4050, b3f5050, b3f-4055, b3f-5051"]
  Switch18 = Pushbutton 12mm omron B3F-4050, B3F-5050, B3F-4055, B3F-5051 [part_number="b3f-4050, b3f5050, b3f-4055, b3f-5051"]
  Switch19 = Pushbutton 12mm omron B3F-4050, B3F-5050, B3F-4055, B3F-5051 [part_number="b3f-4050, b3f5050, b3f-4055, b3f-5051"]
  D14 = Rectifier Diode [part_number=1N4001 package="300 mil [THT]"]
  D15 = Rectifier Diode [part_number=1N4001 package="300 mil [THT]"]
  D16 = Rectifier Diode [part_number=1N4001 package="300 mil [THT]"]
  D17 = Rectifier Diode [part_number=1N4001 package="300 mil [THT]"]
  D18 = Rectifier Diode [part_number=1N4001 package="300 mil [THT]"]
  D19 = Rectifier Diode [part_number=1N4001 package="300 mil [THT]"]
  Switch20 = Pushbutton 12mm omron B3F-4050, B3F-5050, B3F-4055, B3F-5051 [part_number="b3f-4050, b3f5050, b3f-4055, b3f-5051"]
  Switch21 = Pushbutton 12mm omron B3F-4050, B3F-5050, B3F-4055, B3F-5051 [part_number="b3f-4050, b3f5050, b3f-4055, b3f-5051"]
  Switch22 = Pushbutton 12mm omron B3F-4050, B3F-5050, B3F-4055, B3F-5051 [part_number="b3f-4050, b3f5050, b3f-4055, b3f-5051"]
  D20 = Rectifier Diode [part_number=1N4001 package="300 mil [THT]"]
  D21 = Rectifier Diode [part_number=1N4001 package="300 mil [THT]"]
  D22 = Rectifier Diode [part_number=1N4001 package="300 mil [THT]"]
  Switch23 = Pushbutton 12mm omron B3F-4050, B3F-5050, B3F-4055, B3F-5051 [part_number="b3f-4050, b3f5050, b3f-4055, b3f-5051"]
  Switch24 = Pushbutton 12mm omron B3F-4050, B3F-5050, B3F-4055, B3F-5051 [part_number="b3f-4050, b3f5050, b3f-4055, b3f-5051"]
  Switch25 = Pushbutton 12mm omron B3F-4050, B3F-5050, B3F-4055, B3F-5051 [part_number="b3f-4050, b3f5050, b3f-4055, b3f-5051"]
  D23 = Rectifier Diode [part_number=1N4001 package="300 mil [THT]"]
  D24 = Rectifier Diode [part_number=1N4001 package="300 mil [THT]"]
  D25 = Rectifier Diode [part_number=1N4001 package="300 mil [THT]"]
  Switch26 = Pushbutton 12mm omron B3F-4050, B3F-5050, B3F-4055, B3F-5051 [part_number="b3f-4050, b3f5050, b3f-4055, b3f-5051"]
  D26 = Rectifier Diode [part_number=1N4001 package="300 mil [THT]"]
  LED1 = LED 3mm Bicolor red/green common cathode
  LED2 = LED 3mm Bicolor red/green common cathode
  LED3 = LED 3mm Bicolor red/green common cathode
  LED4 = LED 3mm Bicolor red/green common cathode
  LED5 = LED 3mm Bicolor red/green common cathode
  LED6 = LED 3mm Bicolor red/green common cathode
  LED7 = LED 3mm Bicolor red/green common cathode
  LED8 = LED 3mm Bicolor red/green common cathode
  LED9 = LED 3mm Bicolor red/green common cathode
  R1 = Resistor [tolerance=±5% resistance=180 package=THT]
  R2 = Resistor [tolerance=±5% resistance=180 package=THT]
  R3 = Resistor [tolerance=±5% resistance=180 package=THT]
  R4 = Resistor [tolerance=±5% resistance=180 package=THT]
  R5 = Resistor [tolerance=±5% resistance=180 package=THT]
  R6 = Resistor [tolerance=±5% resistance=180 package=THT]
  R8 = Resistor [tolerance=±5% resistance=180 package=THT]
  R9 = Resistor [tolerance=±5% resistance=180 package=THT]
  R10 = Resistor [tolerance=±5% resistance=180 package=THT]
  R11 = Resistor [tolerance=±5% resistance=180 package=THT]
  R12 = Resistor [tolerance=±5% resistance=180 package=THT]
  R13 = Resistor [tolerance=±5% resistance=180 package=THT]
  R14 = Resistor [tolerance=±5% resistance=180 package=THT]
  R16 = Resistor [tolerance=±5% resistance=180 package=THT]
  R17 = Resistor [tolerance=±5% resistance=180 package=THT]
  R18 = Resistor [tolerance=±5% resistance=180 package=THT]
  R19 = Resistor [tolerance=±5% resistance=180 package=THT]
  R20 = Resistor [tolerance=±5% resistance=180 package=THT]
  S1 = Toggle Switch [package=THT]
  C1 = Ceramic Capacitor [capacitance=100nF package="100 mil [THT, multilayer]"]
  Q1 = NPN-Transistor [package="TO92 [THT]"]
  R22 = Resistor [tolerance=±5% resistance=1k package=THT]
  R23 = Resistor [tolerance=±5% resistance=9 package=THT]
  GLCD_128x1 = 128 x 64 Graphic LCD
  VCC1 = Battery
  DC-DC1 = VPACK DC-DC 5V
  R21 = Rotary Potentiometer (Small) [maximum_resistance=100kΩ]
  PCB1 = Custom PCB - platinen_form_0 - toddd  # not connected
  R24 = Resistor [tolerance=±5% resistance=220 package=THT]
  J1 = Piezo Speaker

nets:
  N1: Teensy++1.GND#0, LED1.common_cathode, LED2.common_cathode, LED3.common_cathode, LED4.common_cathode, LED5.common_cathode, LED6.common_cathode, LED7.common_cathode, LED8.common_cathode, LED9.common_cathode, GLCD_128x1.1_Vss, GLCD_128x1.20_K(-), VCC1.-, DC-DC1.GND, R21.leg2, J1.pin1
  N2: Teensy++1.B7, R22.Pin_0
  N3: Teensy++1.D0, R9.Pin_1
  N4: Teensy++1.D1, R13.Pin_1
  N5: Teensy++1.D2, R11.Pin_1
  N6: Teensy++1.D3, R8.Pin_1
  N7: Teensy++1.D4, R5.Pin_1
  N8: Teensy++1.D5, R6.Pin_1
  N9: Teensy++1.D6, R3.Pin_1
  N10: Teensy++1.D7, R4.Pin_1
  N11: Teensy++1.E0, Switch1.no_name_yet#0, Switch1.no_name_yet#1, Switch4.no_name_yet#0, Switch4.no_name_yet#1, Switch7.no_name_yet#0, Switch7.no_name_yet#1, Switch10.no_name_yet#0, Switch10.no_name_yet#1
  N12: Teensy++1.E1, Switch2.no_name_yet#0, Switch2.no_name_yet#1, Switch5.no_name_yet#0, Switch5.no_name_yet#1, Switch8.no_name_yet#0, Switch8.no_name_yet#1, Switch11.no_name_yet#0, Switch11.no_name_yet#1
  N13: Teensy++1.C0, GLCD_128x1.7_DB0
  N14: Teensy++1.C1, GLCD_128x1.8_DB1
  N15: Teensy++1.C2, GLCD_128x1.9_BD2
  N16: Teensy++1.C3, GLCD_128x1.10_DB3
  N17: Teensy++1.C4, GLCD_128x1.11_DB4
  N18: Teensy++1.C5, GLCD_128x1.12_DB5
  N19: Teensy++1.C6, GLCD_128x1.13_DB6
  N20: Teensy++1.C7, GLCD_128x1.14_DB7
  N21: Teensy++1.VCC, Q1.C, GLCD_128x1.2_Vdd, GLCD_128x1.17_RST, DC-DC1.Vout
  N22: Teensy++1.F7, R24.Pin_1
  N23: Teensy++1.F6, Switch15.no_name_yet#2, Switch15.no_name_yet#3, Switch18.no_name_yet#2, Switch18.no_name_yet#3, Switch21.no_name_yet#2, Switch21.no_name_yet#3, Switch24.no_name_yet#2, Switch24.no_name_yet#3
  N24: Teensy++1.F5, D13.anode, D26.anode
  N25: Teensy++1.F4, D7.anode, D8.anode, D9.anode, D20.anode, D21.anode, D22.anode
  N26: Teensy++1.F3, D4.anode, D5.anode, D6.anode, D17.anode, D18.anode, D19.anode
  N27: Teensy++1.F2, D1.anode, D2.anode, D3.anode, D14.anode, D15.anode, D16.anode
  N28: Teensy++1.AREF, C1.1
  N29: Teensy++1.GND#32, C1.0
  N30: Teensy++1.E6, Switch3.no_name_yet#0, Switch3.no_name_yet#1, Switch6.no_name_yet#0, Switch6.no_name_yet#1, Switch9.no_name_yet#0, Switch9.no_name_yet#1, Switch12.no_name_yet#0, Switch12.no_name_yet#1, Switch13.no_name_yet#0, Switch13.no_name_yet#1
  N31: Teensy++1.E7, R20.Pin_1
  N32: Teensy++1.B0, R17.Pin_1
  N33: Teensy++1.B1, R16.Pin_1
  N34: Teensy++1.B2, R18.Pin_1
  N35: Teensy++1.B3, R19.Pin_1
  N36: Teensy++1.B4, R12.Pin_1
  N37: Teensy++1.B5, R10.Pin_1
  N38: Teensy++1.B6, R14.Pin_1
  N39: Teensy++1.E4, R1.Pin_1
  N40: Teensy++1.E5, R2.Pin_1
  N41: Teensy++1.PA0, GLCD_128x1.16_CS2
  N42: Teensy++1.PA1, D10.anode, D11.anode, D12.anode, D23.anode, D24.anode, D25.anode
  N43: Teensy++1.PA2, Switch16.no_name_yet#2, Switch16.no_name_yet#3, Switch19.no_name_yet#2, Switch19.no_name_yet#3, Switch22.no_name_yet#2, Switch22.no_name_yet#3, Switch25.no_name_yet#2, Switch25.no_name_yet#3
  N44: Teensy++1.PA3, Switch14.no_name_yet#2, Switch14.no_name_yet#3, Switch17.no_name_yet#2, Switch17.no_name_yet#3, Switch20.no_name_yet#2, Switch20.no_name_yet#3, Switch23.no_name_yet#2, Switch23.no_name_yet#3, Switch26.no_name_yet#2, Switch26.no_name_yet#3
  N45: Teensy++1.PA4, GLCD_128x1.15_CS1
  N46: Teensy++1.PA5, GLCD_128x1.6_Enable
  N47: Teensy++1.PA6, GLCD_128x1.5_R/W
  N48: Teensy++1.PA7, GLCD_128x1.4_D/I
  N49: Switch1.no_name_yet#2, Switch1.no_name_yet#3, D1.cathode
  N50: Switch2.no_name_yet#2, Switch2.no_name_yet#3, D2.cathode
  N51: Switch3.no_name_yet#2, Switch3.no_name_yet#3, D3.cathode
  N52: Switch4.no_name_yet#2, Switch4.no_name_yet#3, D4.cathode
  N53: Switch5.no_name_yet#2, Switch5.no_name_yet#3, D5.cathode
  N54: Switch6.no_name_yet#2, Switch6.no_name_yet#3, D6.cathode
  N55: Switch7.no_name_yet#2, Switch7.no_name_yet#3, D7.cathode
  N56: Switch8.no_name_yet#2, Switch8.no_name_yet#3, D8.cathode
  N57: Switch9.no_name_yet#2, Switch9.no_name_yet#3, D9.cathode
  N58: Switch10.no_name_yet#2, Switch10.no_name_yet#3, D10.cathode
  N59: Switch11.no_name_yet#2, Switch11.no_name_yet#3, D11.cathode
  N60: Switch12.no_name_yet#2, Switch12.no_name_yet#3, D12.cathode
  N61: Switch13.no_name_yet#2, Switch13.no_name_yet#3, D13.cathode
  N62: Switch14.no_name_yet#0, Switch14.no_name_yet#1, D16.cathode
  N63: Switch15.no_name_yet#0, Switch15.no_name_yet#1, D15.cathode
  N64: Switch16.no_name_yet#0, Switch16.no_name_yet#1, D14.cathode
  N65: Switch17.no_name_yet#0, Switch17.no_name_yet#1, D18.cathode
  N66: Switch18.no_name_yet#0, Switch18.no_name_yet#1, D17.cathode
  N67: Switch19.no_name_yet#0, Switch19.no_name_yet#1, D19.cathode
  N68: Switch20.no_name_yet#0, Switch20.no_name_yet#1, D22.cathode
  N69: Switch21.no_name_yet#0, Switch21.no_name_yet#1, D20.cathode
  N70: Switch22.no_name_yet#0, Switch22.no_name_yet#1, D21.cathode
  N71: Switch23.no_name_yet#0, Switch23.no_name_yet#1, D23.cathode
  N72: Switch24.no_name_yet#0, Switch24.no_name_yet#1, D24.cathode
  N73: Switch25.no_name_yet#0, Switch25.no_name_yet#1, D25.cathode
  N74: Switch26.no_name_yet#0, Switch26.no_name_yet#1, D26.cathode
  N75: LED1.red_anode, R2.Pin_0
  N76: LED1.green_anode, R1.Pin_0
  N77: LED2.red_anode, R3.Pin_0
  N78: LED2.green_anode, R4.Pin_0
  N79: LED3.red_anode, R5.Pin_0
  N80: LED3.green_anode, R6.Pin_0
  N81: LED4.red_anode, R11.Pin_0
  N82: LED4.green_anode, R8.Pin_0
  N83: LED5.red_anode, R9.Pin_0
  N84: LED5.green_anode, R13.Pin_0
  N85: LED6.red_anode, R10.Pin_0
  N86: LED6.green_anode, R14.Pin_0
  N87: LED7.red_anode, R19.Pin_0
  N88: LED7.green_anode, R12.Pin_0
  N89: LED8.red_anode, R16.Pin_0
  N90: LED8.green_anode, R18.Pin_0
  N91: LED9.red_anode, R20.Pin_0
  N92: LED9.green_anode, R17.Pin_0
  N93: S1.COM, VCC1.+
  N94: S1.L2, DC-DC1.Vin
  N95: Q1.E, R23.Pin_0
  N96: Q1.B, R22.Pin_1
  N97: R23.Pin_1, GLCD_128x1.19_A(+)
  N98: GLCD_128x1.3_Vo, R21.wiper
  N99: GLCD_128x1.18_Vout, R21.leg1
  N100: R24.Pin_0, J1.pin2

custom parts:
  Pushbutton 12mm omron B3F-4050, B3F-5050, B3F-4055, B3F-5051: An Omron pushbutton. 12mm
  LED 3mm Bicolor red/green common cathode: LED 3mm bicolor red/green 3pin with common cathode
  Battery: Your special 3x AAA battery pack (4.5 Volts)
  VPACK DC-DC 5V: Description: The VPACK_PCB (http://www.sparkfun.com) is a 1V DC-DC converter. The breakout board will accept voltage inputs between 1 and 4.5 Volts (such as 1 or 2 or 3 AA batteries) and output a constant, low ripple 5V output capable of sourcing up to 300 mA. The breakout board includes the necessary peripheral components. The input, ouput and ground pins are broken out on a 0.1" grid to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
  Custom PCB - platinen_form_0 - toddd: Custom platinen_form_0 - toddd - 188.352x105.354mm Circuit Board 2011-09-05 20:45:32
