# Fritzing sketch forkuino05 (saved by Fritzing 0.6.2b)
breadboards: 1

parts:
  D0RX = header hole
  D1TX = header hole
  D2 = header hole
  D3 = header hole
  D4 = header hole
  D5 = header hole
  D8 = header hole
  D7 = header hole
  D9 = header hole
  D6 = header hole
  D12 = header hole
  D11 = header hole
  D13 = header hole
  D10 = header hole
  AREF = header hole
  GND = header hole
  A5 = header hole
  A4 = header hole
  A3 = header hole
  A2 = header hole
  A1 = header hole
  A0 = header hole
  VIN = header hole
  GND_2 = header hole
  GND_3 = header hole
  5V = header hole
  ? = header hole
  RST = header hole
  Atmega328 = atmega168 [package="DIP28 [THT]"]
  D1TX1 = header hole
  D1TX2 = header hole
  D1TX3 = header hole
  3mm_hole1 = 3mm hole [form="♀ (female)"]  # not connected
  3mm_hole2 = 3mm hole [form="♀ (female)"]  # not connected
  3mm_hole3 = 3mm hole [form="♀ (female)"]  # not connected
  16mhz = header hole
  104 = Ceramic Capacitor [capacitance=100nF package="100 mil [THT, multilayer]"]
  ICSP = header hole
  D1TX5 = header hole
  D1TX6 = header hole
  D1TX7 = header hole
  D1TX8 = header hole
  10k = Resistor [tolerance=±5% resistance=10k package=THT]
  reset = Pushbutton [package="[THT]"]
  104_2 = Ceramic Capacitor [capacitance=100nF package="100 mil [THT, multilayer]"]
  hole6 = header hole
  hole2 = header hole
  hole4 = header hole
  hole5 = header hole
  CTS = header hole  # not connected
  gnd/black = header hole
  DC+)- = Power plug
  47uf = Electrolytic Capacitor [capacitance=1µF package="100 mil [THT, electrolytic]"]
  47uf_2 = Electrolytic Capacitor [capacitance=1µF package="100 mil [THT, electrolytic]"]
  78l05 = NPN-Transistor [package="TO92 [THT]"]
  ?1 = header hole
  R1 = Resistor [tolerance=±5% resistance=1k package=THT]
  LED1 = Red LED - 5mm [package="5 mm [THT]"]
  104_3 = Ceramic Capacitor [capacitance=100nF package="100 mil [THT, multilayer]"]
  USB = header hole
  EXT1 = header hole
  EXT = header hole
  4001 = Rectifier Diode [part_number=1N4001 package="300 mil [THT]"]
  C1 = Ceramic Capacitor [capacitance=100nF package="100 mil [THT, multilayer]"]
  C2 = Ceramic Capacitor [capacitance=100nF package="100 mil [THT, multilayer]"]
  3mm_hole4 = 3mm hole [form="♀ (female)"]  # not connected

nets:
  N1: D0RX.pin_0, Atmega328.Pin_2, hole4.pin_0
  N2: D1TX.pin_0, Atmega328.Pin_3, hole2.pin_0
  N3: D2.pin_0, Atmega328.Pin_4
  N4: D3.pin_0, Atmega328.Pin_5
  N5: D4.pin_0, Atmega328.Pin_6
  N6: D5.pin_0, Atmega328.Pin_11
  N7: D8.pin_0, Atmega328.Pin_14
  N8: D7.pin_0, Atmega328.Pin_13
  N9: D9.pin_0, Atmega328.Pin_15
  N10: D6.pin_0, Atmega328.Pin_12
  N11: D12.pin_0, Atmega328.Pin_18, D1TX6.pin_0
  N12: D11.pin_0, Atmega328.Pin_17, D1TX3.pin_0
  N13: D13.pin_0, Atmega328.Pin_19, D1TX7.pin_0, LED1.anode
  N14: D10.pin_0, Atmega328.Pin_16
  N15: AREF.pin_0, Atmega328.Pin_21
  N16: GND.pin_0, GND_2.pin_0, GND_3.pin_0, Atmega328.Pin_8, Atmega328.Pin_22, D1TX2.pin_0, 104.0, D1TX5.pin_0, reset.Pin_3, reset.Pin_4, 104_2.1, gnd/black.pin_0, DC+)-.pin_2, DC+)-.pin_3, 47uf.-, 47uf_2.-, 78l05.B, R1.Pin_0, 4001.anode, C1.1, C2.1
  N17: A5.pin_0, Atmega328.Pin_28
  N18: A4.pin_0, Atmega328.Pin_27
  N19: A3.pin_0, Atmega328.Pin_26
  N20: A2.pin_0, Atmega328.Pin_25
  N21: A1.pin_0, Atmega328.Pin_24
  N22: A0.pin_0, Atmega328.Pin_23
  N23: VIN.pin_0, DC+)-.pin_1, 47uf_2.+, 78l05.C, 4001.cathode
  N24: 5V.pin_0, Atmega328.Pin_7, Atmega328.Pin_20, 104.1, ICSP.pin_0, 10k.Pin_0, 104_2.0, 47uf.+, 78l05.E, EXT1.pin_0, EXT.pin_0
  N25: ?.pin_0, ?1.pin_0
  N26: RST.pin_0, Atmega328.Pin_1, D1TX8.pin_0, 10k.Pin_1, reset.Pin_1, reset.Pin_2, 104_3.1
  N27: Atmega328.Pin_9, 16mhz.pin_0, C2.0
  N28: Atmega328.Pin_10, D1TX1.pin_0, C1.0
  N29: hole6.pin_0, 104_3.0
  N30: hole5.pin_0, USB.pin_0
  N31: R1.Pin_1, LED1.cathode

notes:
  Forkuino
  gijs gieskes

custom parts:
  header hole: hole
  3mm hole: Generic female header
  Power plug: power plug
