# Fritzing sketch fritzing-project (saved by Fritzing 0.6.3b)
breadboards: 1

parts:
  Arduino1 = Arduino
  LED3 = LED - 5mm [color="Red (633nm)" package="5 mm [THT]"]
  R1 = Resistor [tolerance=±5% resistance=220 package=THT]
  R2 = Resistor [tolerance=±5% resistance=220 package=THT]
  R3 = Resistor [tolerance=±5% resistance=220 package=THT]
  R4 = Resistor [tolerance=±5% resistance=220 package=THT]
  R5 = Resistor [tolerance=±5% resistance=220 package=THT]
  LED7 = LED - 5mm [color="Red (633nm)" package="5 mm [THT]"]
  LED8 = LED - 5mm [color="Red (633nm)" package="5 mm [THT]"]
  LED9 = LED - 5mm [color="Red (633nm)" package="5 mm [THT]"]
  LED10 = LED - 5mm [color="Red (633nm)" package="5 mm [THT]"]

nets:
  N1: Arduino1.GND, R1.Pin_0, R2.Pin_0, R3.Pin_0, R4.Pin_0, R5.Pin_0
  N2: Arduino1.D10, LED3.anode
  N3: Arduino1.D9, LED10.anode
  N4: Arduino1.D6, LED7.anode
  N5: Arduino1.D5, LED8.anode
  N6: Arduino1.D3, LED9.anode
  N7: LED3.cathode, R1.Pin_1
  N8: R2.Pin_1, LED9.cathode
  N9: R3.Pin_1, LED8.cathode
  N10: R4.Pin_1, LED7.cathode
  N11: R5.Pin_1, LED10.cathode
