# Fritzing sketch fritzing (saved by Fritzing 0.6.3b)
breadboards: 1

parts:
  Arduino1 = Arduino
  LED1 = LED - 5mm [color="Red (633nm)" package="5 mm [THT]"]
  LED2 = LED - 5mm [color="Red (633nm)" package="5 mm [THT]"]
  LED3 = LED - 5mm [color="Red (633nm)" package="5 mm [THT]"]
  J1 = Piezo Speaker
  Q1 = NPN-Transistor [package="TO92 [THT]"]
  LED5 = LED - 5mm [color="Infrared (940nm)" package="5 mm [THT]"]
  LED6 = LED - 5mm [color="Red (633nm)" package="5 mm [THT]"]
  LED7 = LED - 5mm [color="Green (560nm)" package="5 mm [THT]"]
  R1 = Resistor [tolerance=±5% resistance=220 package=THT]
  R2 = Resistor [tolerance=±5% resistance=220 package=THT]
  LED8 = LED - 5mm [color="Infrared (850nm)" package="5 mm [THT]"]
  R3 = Resistor [tolerance=±5% resistance=220 package=THT]
  R4 = Resistor [tolerance=±5% resistance=220 package=THT]
  R5 = Resistor [tolerance=±5% resistance=220 package=THT]
  R6 = Resistor [tolerance=±5% resistance=220 package=THT]
  R7 = Resistor [tolerance=±5% resistance=220 package=THT]

nets:
  N1: Arduino1.D12, LED6.anode
  N2: Arduino1.D11, LED8.anode
  N3: Arduino1.D8, J1.pin2
  N4: Arduino1.D7, LED7.anode
  N5: Arduino1.D6, LED1.anode
  N6: Arduino1.D5, LED2.anode
  N7: Arduino1.D4, LED3.anode
  N8: Arduino1.D3, R1.Pin_0
  N9: Arduino1.GND, R2.Pin_0, R3.Pin_0, R4.Pin_0
  N10: LED1.cathode, R2.Pin_1
  N11: LED2.cathode, R3.Pin_1
  N12: LED3.cathode, R4.Pin_1
  N13: J1.pin1, R5.Pin_1
  N14: Q1.E, LED5.cathode
  N15: Q1.B, R1.Pin_1
  N16: Q1.C, R5.Pin_0, R6.Pin_0, R7.Pin_0
  N17: LED6.cathode, LED7.cathode, R6.Pin_1
  N18: LED8.cathode, R7.Pin_1

notes:
  blackstufflabs.wordpress.com
  Status Leds
  IR Receiver with 2 colors led
  IR Emitter
