# Fritzing sketch garduino (saved by Fritzing 0.4.3b)
breadboards: 3

parts:
  Arduino1 = Arduino
  LCD1 = LCD screen
  R1 = Rotary Potentiometer (Small)
  R2 = Rotary Potentiometer (Small)
  S1 = Pushbutton [package="[THT]"]
  S2 = Toggle Switch [package=THT]
  R3 = Resistor [resistance=220 package=THT]
  S3 = Pushbutton [package="[THT]"]
  R4 = Resistor [resistance=220 package=THT]
  LED1 = Red LED - 5mm
  K1 = Relay [package=THT]
  Power_plug1 = Power plug
  LED2 = Blue LED - 5mm
  Power_plug2 = Power plug
  K2 = Relay [package=THT]
  M1 = DC Motor
  R5 = Resistor [resistance=220 package=THT]
  Q1 = NPN-Transistor [package="TO92 [THT]"]
  R6 = Resistor [resistance=220 package=THT]
  Q2 = NPN-Transistor [package="TO92 [THT]"]
  D1 = Rectifier Diode [package="300 mil [THT]"]
  D2 = Rectifier Diode [package="300 mil [THT]"]

nets:
  GND: Arduino1.GND, LCD1.VSS, LCD1.LED-, R1.leg1, R2.leg2, S2.L1, R3.Pin_0, R4.Pin_1, K2.COIL2, Q1.C, Q2.C, D2.cathode
  +5V: Arduino1.D12, Arduino1.+5V, LCD1.VDD, LCD1.R/W, R1.leg2, R2.leg1, S1.Pin_3, S1.Pin_4, S2.L2, R3.Pin_1, S3.Pin_3, S3.Pin_4
  N1: Arduino1.D11, S3.Pin_1, S3.Pin_2, LED1.cathode
  N2: Arduino1.D9, R5.Pin_0
  N3: Arduino1.D8, R6.Pin_0
  N4: Arduino1.D7, LCD1.DB7
  N5: Arduino1.D6, LCD1.DB6
  N6: Arduino1.D5, LCD1.DB5
  N7: Arduino1.D4, LCD1.DB4
  N8: Arduino1.D3, LCD1.E
  N9: Arduino1.D2, LCD1.RS
  N10: Arduino1.3V3, K1.COIL2, D1.cathode
  N11: Arduino1.A0, R2.wiper
  N12: LCD1.V0, R1.wiper
  N13: LCD1.LED+, S2.COM
  N14: R4.Pin_0, LED1.anode
  N15: K1.COIL1, Q2.E, D1.anode
  N16: K1.C1, K1.C2, Power_plug1.VCC
  N17: K1.B, LED2.cathode
  N18: Power_plug1.GND, LED2.anode
  N19: Power_plug2.GND, M1.pin_2
  N20: Power_plug2.VCC, K2.C1
  N21: K2.A, M1.pin_1
  N22: K2.COIL1, Q1.E, D2.anode
  N23: R5.Pin_1, Q1.B
  N24: R6.Pin_1, Q2.B

notes:
  water pump
  light tube
  display on of
  pump on momentary
  user controls
