# Fritzing sketch gasSensor (saved by Fritzing 0.6.3b)
breadboards: 1

parts:
  Arduino1 = Arduino
  J1 = female pin header, 2 pins [form="♀ (female)"]
  J2 = female pin header, 2 pins [form="♀ (female)"]
  J3 = female pin header, 2 pins [form="♀ (female)"]
  J4 = female pin header, 2 pins [form="♀ (female)"]
  R1 = Rotary Potentiometer (Small)
  Figaro_TGS_2602_Gas_Sensor1 = Figaro TGS 2602 Gas Sensor

nets:
  N1: Arduino1.GND, J3.pin1, J4.pin1, R1.leg1, Figaro_TGS_2602_Gas_Sensor1.pin_1
  N2: Arduino1.+5V, J1.pin2, J2.pin2, J3.pin2, J4.pin2, Figaro_TGS_2602_Gas_Sensor1.pin_3, Figaro_TGS_2602_Gas_Sensor1.pin_4
  N3: Arduino1.A0, R1.wiper
  N4: J1.pin1, J2.pin1
  N5: R1.leg2, Figaro_TGS_2602_Gas_Sensor1.pin_2

notes:
  mctouch

custom parts:
  Figaro TGS 2602 Gas Sensor: The sensing element is comprised of a metal oxide semiconductor layer formed on the alumina substrate of a sensing chip together with an integrated heater. In the presence of detectable gas, sensor conductivity increases depending on gas concentration in the air. A simple electrical circuit can convert the change in conductivity to an output signal which corresponds to the gas concentration.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
