# Fritzing sketch gogo-arduino (saved by Fritzing 0.6.3b)
breadboards: 1

parts:
  GogoBoard_4_1 = GogoBoard 4.0
  Arduino1 = Arduino

nets:
  GND: GogoBoard_4_1.GND, Arduino1.GND, Arduino1.VIN
  N1: GogoBoard_4_1.SV1/A, Arduino1.D0RX
  N2: GogoBoard_4_1.SV2/B, Arduino1.D1TX
  N3: GogoBoard_4_1.SV3/C, Arduino1.D2
  N4: GogoBoard_4_1.SV4/D, Arduino1.D3
  N5: GogoBoard_4_1.A1, Arduino1.A5
  N6: GogoBoard_4_1.A2, Arduino1.A4
  N7: GogoBoard_4_1.A3, Arduino1.A3
  N8: GogoBoard_4_1.A4, Arduino1.A2
  N9: GogoBoard_4_1.A5, Arduino1.A1
  N10: GogoBoard_4_1.A6, Arduino1.A0
  +5V: GogoBoard_4_1.+5V, Arduino1.+5V
