# Fritzing sketch headset2 (saved by Fritzing 0.3.19b)

parts:
  Arduino1 = Arduino
  Q1 = NPN-Transistor [package="TO92 [THT]"]
  R1 = Resistor [resistance=10 package=THT]

nets:
  GND: Arduino1.GND, Q1.C
  N1: Arduino1.D12, Q1.B
  N2: Q1.E, R1.Pin_0

notes:
  Q1 emitter is connected to cellphone microphone line via R1
  NPN emitter is connected to cellphone microphone line via protective resistor
  NPN collector is grounded to Arduino and cellphone
  Q1 collector is grounded to Arduino and cellphone
