# Fritzing sketch iterationWithPushbutton (saved by Fritzing 0.6.3b)
breadboards: 1

parts:
  Arduino1 = Arduino
  R1 = Resistor [tolerance=±5% resistance=10k power=10k package=THT]
  S1 = Pushbutton [package=THT]
  LED1 = LED - 5mm [color="Red (633nm)" package="5 mm [THT]"]
  LED2 = LED - 5mm [color="Red (633nm)" package="5 mm [THT]"]
  LED3 = LED - 5mm [color="Red (633nm)" package="5 mm [THT]"]
  LED4 = LED - 5mm [color="Red (633nm)" package="5 mm [THT]"]
  LED5 = LED - 5mm [color="Red (633nm)" package="5 mm [THT]"]
  LED6 = LED - 5mm [color="Red (633nm)" package="5 mm [THT]"]
  R2 = Resistor [tolerance=±5% resistance=220 package=THT]
  R3 = Resistor [tolerance=±5% resistance=220 package=THT]
  R4 = Resistor [tolerance=±5% resistance=220 package=THT]
  R5 = Resistor [tolerance=±5% resistance=220 package=THT]
  R6 = Resistor [tolerance=±5% resistance=220 package=THT]
  R7 = Resistor [tolerance=±5% resistance=220 package=THT]

nets:
  N1: Arduino1.GND, R1.Pin_0, LED1.cathode, LED2.cathode, LED3.cathode
  N2: Arduino1.D7, R2.Pin_1
  N3: Arduino1.D6, R3.Pin_1
  N4: Arduino1.D5, R7.Pin_1
  N5: Arduino1.D4, R4.Pin_1
  N6: Arduino1.D3, R5.Pin_1
  N7: Arduino1.D2, R6.Pin_1
  N8: Arduino1.+5V, S1.leg0
  N9: R1.Pin_1, S1.leg1
  N10: LED1.anode, R2.Pin_0
  N11: LED2.anode, R3.Pin_0
  N12: LED3.anode, R7.Pin_0
  N13: LED4.cathode, LED5.cathode, LED6.cathode
  N14: LED4.anode, R4.Pin_0
  N15: LED5.anode, R5.Pin_0
  N16: LED6.anode, R6.Pin_0

notes:
  Button Handling =
  Based on Button Example
  Lights handling =
  based on forLoopIteration
  /*
  For Loop Iteration
  Demonstrates the use of a for() loop.
  Lights multiple LEDs in sequence, then in reverse.
  The circuit:
  * LEDs from pins 2 through 7 to ground
  created 2006
  by David A. Mellis
  modified 5 Jul 2009
  by Tom Igoe
  This example code is in the public domain.
  http://www.arduino.cc/en/Tutorial/ForLoop
  */
  const int buttonPin = 8; // the number of the pushbutton pin
  int timer = 100; // The higher the number, the slower the timing.
  int buttonState = 0; // variable for reading the pushbutton status
  void setup() {
  // use a for loop to initialize each pin as an output:
  for (int thisPin = 2; thisPin < 8; thisPin++) {
  pinMode(thisPin, OUTPUT);
  }
  pinMode(buttonPin, INPUT);
  }
  void loop() {
  buttonState = digitalRead(buttonPin);
  if (buttonState == HIGH) {
  // loop from the lowest pin to the highest:
  for (int thisPin = 2; thisPin < 8; thisPin++) {
  // turn the pin on:
  digitalWrite(thisPin, HIGH);
  delay(timer);
  // turn the pin off:
  digitalWrite(thisPin, LOW);
  }
  // loop from the highest pin to the lowest:
  for (int thisPin = 7; thisPin >= 2; thisPin--) {
  // turn the pin on:
  digitalWrite(thisPin, HIGH);
  delay(timer);
  // turn the pin off:
  digitalWrite(thisPin, LOW);
  }
  }
  }
