# Fritzing sketch keyboardMusic (saved by Fritzing 0.4.0b)
breadboards: 1

parts:
  Fa = Pushbutton [package="[THT]"]
  So = Pushbutton [package="[THT]"]
  La = Pushbutton [package="[THT]"]
  Ti = Pushbutton [package="[THT]"]
  Dooo = Pushbutton [package="[THT]"]
  Ray = Pushbutton [package="[THT]"]
  Do = Pushbutton [package="[THT]"]
  Arduino1 = Arduino
  LED1 = Red LED - 5mm
  LED1_2 = yellow LED - 5mm
  LED1_3 = Blue LED - 5mm
  LED1_4 = green LED - 5mm
  LED1_5 = white LED - 5mm
  LED1_6 = yellow LED - 5mm
  LED1_7 = Blue LED - 5mm
  LED1_8 = green LED - 5mm
  J1 = Piezo Speaker
  Mei = Pushbutton [package="[THT]"]
  R1 = Resistor [resistance=1k package=THT]
  R1_2 = Resistor [resistance=1k package=THT]
  R1_3 = Resistor [resistance=1k package=THT]
  R1_4 = Resistor [resistance=1k package=THT]
  R1_5 = Resistor [resistance=1k package=THT]
  R1_6 = Resistor [resistance=1k package=THT]
  R1_7 = Resistor [resistance=1k package=THT]
  R1_8 = Resistor [resistance=1k package=THT]
  Playback = Pushbutton [package="[THT]"]
  R2 = Resistor [resistance=10 package=THT]

nets:
  N1: Fa.Pin_1, Fa.Pin_2, Arduino1.D6, LED1_5.anode
  N2: Fa.Pin_3, Fa.Pin_4, So.Pin_3, So.Pin_4, La.Pin_3, La.Pin_4, Ti.Pin_3, Ti.Pin_4, Dooo.Pin_3, Dooo.Pin_4, Ray.Pin_3, Ray.Pin_4, Do.Pin_3, Do.Pin_4, Arduino1.+5V, Mei.Pin_3, Mei.Pin_4, Playback.Pin_3, Playback.Pin_4
  N3: So.Pin_1, So.Pin_2, Arduino1.D5, LED1.anode
  N4: La.Pin_1, La.Pin_2, Arduino1.D4, LED1_6.anode
  N5: Ti.Pin_1, Ti.Pin_2, Arduino1.D3, LED1_7.anode
  N6: Dooo.Pin_1, Dooo.Pin_2, Arduino1.D2, LED1_8.anode
  N7: Ray.Pin_1, Ray.Pin_2, Arduino1.D8, LED1_3.anode
  N8: Do.Pin_1, Do.Pin_2, Arduino1.D9, LED1_2.anode
  N9: Arduino1.GND, J1.pin1, R1.Pin_0, R1_2.Pin_0, R1_3.Pin_0, R1_4.Pin_0, R1_5.Pin_0, R1_6.Pin_0, R1_7.Pin_0, R1_8.Pin_0, R2.Pin_0
  N10: Arduino1.D13, J1.pin2
  N11: Arduino1.D12, Playback.Pin_1, Playback.Pin_2, R2.Pin_1
  N12: Arduino1.D7, LED1_4.anode, Mei.Pin_1, Mei.Pin_2
  N13: LED1.cathode, R1_5.Pin_1
  N14: LED1_2.cathode, R1.Pin_1
  N15: LED1_3.cathode, R1_2.Pin_1
  N16: LED1_4.cathode, R1_3.Pin_1
  N17: LED1_5.cathode, R1_4.Pin_1
  N18: LED1_6.cathode, R1_6.Pin_1
  N19: LED1_7.cathode, R1_7.Pin_1
  N20: LED1_8.cathode, R1_8.Pin_1

notes:
  In output mode, LED lights up on HIGH. (This is good for playback.)
  In input mode, LED lights up when button is pressed.
  **DON'T FORGET TO SET THE PINMODE.
