# Fritzing sketch knock_Knock (saved by Fritzing 0.3.1b)
breadboards: 1

parts:
  Arduino1 = Arduino
  J1 = Piezo Speaker
  R3 = 1M Ω Resistor [package=THT]

nets:
  N1: Arduino1.GND, J1.pin1, R3.Pin_0
  N2: Arduino1.A0, J1.pin2, R3.Pin_1
