# Fritzing sketch knockbox (saved by Fritzing 0.5.2b)
breadboards: 1

parts:
  Arduino1 = Arduino
  Piezo_Tonabnehmer = Piezo Speaker
  R1 = Resistor [resistance=100k package=THT]
  R2 = Resistor [resistance=10k package=THT]
  IRF630 = Basic FET N-Channel [package="TO220 [THT]"]
  Läutwerk_aus_einer_Klingel = mystery part, 2 pins [chip_label=? spacing=300mil]

nets:
  N1: Arduino1.D9, R2.Pin_0
  N2: Arduino1.+5V, Läutwerk_aus_einer_Klingel.pin2
  N3: Arduino1.GND, Piezo_Tonabnehmer.pin2, R1.Pin_0, IRF630.source
  N4: Arduino1.A0, Piezo_Tonabnehmer.pin1, R1.Pin_1
  N5: R2.Pin_1, IRF630.gate
  N6: IRF630.drain, Läutwerk_aus_einer_Klingel.pin1
