# Fritzing sketch lauflicht (saved by Fritzing 0.6.3b)
breadboards: 1

parts:
  LED1 = LED - 5mm [color="Red (633nm)" package="5 mm [THT]"]
  LED2 = LED - 5mm [color="Red (633nm)" package="5 mm [THT]"]
  LED3 = LED - 5mm [color="Red (633nm)" package="5 mm [THT]"]
  LED4 = LED - 5mm [color="Red (633nm)" package="5 mm [THT]"]
  LED5 = LED - 5mm [color="Red (633nm)" package="5 mm [THT]"]
  LED6 = LED - 5mm [color="Red (633nm)" package="5 mm [THT]"]
  S1 = Pushbutton [package=THT]
  S2 = Pushbutton [package=THT]
  R1 = Rotary Potentiometer (Small) [maximum_resistance=100kΩ]
  R2 = Resistor [tolerance=±5% resistance=220 package=THT]
  R3 = Resistor [tolerance=±5% resistance=220 package=THT]
  R4 = Resistor [tolerance=±5% resistance=220 package=THT]
  R5 = Resistor [tolerance=±5% resistance=220 package=THT]
  R6 = Resistor [tolerance=±5% resistance=220 package=THT]
  R7 = Resistor [tolerance=±5% resistance=220 package=THT]
  R8 = Resistor [tolerance=±5% resistance=1k package=THT]
  R9 = Resistor [tolerance=±5% resistance=1k package=THT]
  Arduino1 = Arduino

nets:
  N1: LED1.cathode, LED2.cathode, LED3.cathode, LED4.cathode, LED5.cathode, LED6.cathode, R1.leg1, R8.Pin_0, R9.Pin_0, Arduino1.GND
  N2: LED1.anode, R2.Pin_0
  N3: LED2.anode, R3.Pin_0
  N4: LED3.anode, R4.Pin_0
  N5: LED4.anode, R5.Pin_0
  N6: LED5.anode, R6.Pin_0
  N7: LED6.anode, R7.Pin_0
  N8: S1.leg0, S2.leg0, R1.leg2, Arduino1.+5V
  N9: S1.leg1, R8.Pin_1, Arduino1.D3
  N10: S2.leg1, R9.Pin_1, Arduino1.D2
  N11: R1.wiper, Arduino1.A0
  N12: R2.Pin_1, Arduino1.D13
  N13: R3.Pin_1, Arduino1.D12
  N14: R4.Pin_1, Arduino1.D11
  N15: R5.Pin_1, Arduino1.D10
  N16: R6.Pin_1, Arduino1.D9
  N17: R7.Pin_1, Arduino1.D8
