# Fritzing sketch layout (saved by Fritzing 0.6.4b)
breadboards: 1

parts:
  S1 = Pushbutton [package=THT]
  R1 = Rotary Potentiometer (Small) [maximum_resistance=100kΩ]
  LED1 = RGB LED (com. anode, rbg) [package="5 mm [THT]"]
  Arduino1 = Arduino
  R2 = Resistor [tolerance=±5% resistance=220 package=THT]

nets:
  N1: S1.leg0, Arduino1.D8, R2.Pin_0
  N2: S1.leg1, R1.leg2, LED1.common_anode, Arduino1.+5V
  N3: R1.leg1, Arduino1.GND, R2.Pin_1
  N4: R1.wiper, Arduino1.A1
  N5: LED1.red_cathode, Arduino1.D9
  N6: LED1.blue_cathode, Arduino1.D10
  N7: LED1.green_cathode, Arduino1.D11
