# Fritzing sketch ldr-schema (saved by Fritzing 0.3.16b)
breadboards: 1

parts:
  R1 = Photocell (LDR) [package=THT]
  Arduino1 = Arduino
  R2 = Resistor [resistance=550 package=THT]

nets:
  N1: R1.pin_0, Arduino1.A0, R2.Pin_1
  N2: R1.pin_1, Arduino1.+5V
  N3: Arduino1.GND, R2.Pin_0

notes:
  La résistance : entre 500 ohm et quelques K en fonction du capteur
