# Fritzing sketch lm317 (saved by Fritzing 0.6.2b)
breadboards: 1

parts:
  U2 = Voltage Regulator - Variable [package="TO220 [THT]"]
  R1 = Resistor [tolerance=±5% resistance=220 package=THT]
  R2 = Resistor [tolerance=±5% resistance=220 package=THT]
  VCC1 = obsolete Battery
  C1 = Ceramic Capacitor [capacitance=100nF package="100 mil [THT, multilayer]"]
  C2 = Tantalum Capacitor [capacitance="1 μF" package="100 mil [THT, tantalum]"]

nets:
  N1: U2.ADJ, R1.Pin_0, R2.Pin_1
  N2: U2.OUT, R2.Pin_0, C2.+
  N3: U2.IN, VCC1.+, C1.1
  N4: R1.Pin_1, VCC1.-, C1.0, C2.-
