# Fritzing sketch lm335_temperature_sensor_serlcd (saved by Fritzing 0.3.19b)
breadboards: 1

parts:
  Arduino_Mega = Arduino Mega
  LM335_Temperature_Sensor1 = DIP - 4 pins
  2k_Resistor = Resistor [resistance=2.2k package=THT]
  10k_potentiometer = Rotary Potentiometer (Large) [package=THT]
  SerLCD_2_5_Module_hooked_to_a_16x2_LCD1 = SerLCD 2.5 16x2

nets:
  N1: Arduino_Mega.GND, Arduino_Mega.A1, LM335_Temperature_Sensor1.connector0, LM335_Temperature_Sensor1.connector1, LM335_Temperature_Sensor1.connector2, 2k_Resistor.Pin_1, 10k_potentiometer.leg1, 10k_potentiometer.wiper, 10k_potentiometer.leg2, SerLCD_2_5_Module_hooked_to_a_16x2_LCD1.connector1
  N2: Arduino_Mega.D1TX, SerLCD_2_5_Module_hooked_to_a_16x2_LCD1.connector2
  N3: Arduino_Mega.+5V, 2k_Resistor.Pin_0, SerLCD_2_5_Module_hooked_to_a_16x2_LCD1.connector0
