# Fritzing sketch lm335_temperature_sensor_tellymate (saved by Fritzing 0.3.19b)
breadboards: 1

parts:
  Arduino_Mega_with_Tellymate = Arduino Mega
  LM335_Temperature_Sensor1 = DIP - 4 pins
  2k_Resistor = Resistor [resistance=2.2k package=THT]

nets:
  N1: Arduino_Mega_with_Tellymate.GND, LM335_Temperature_Sensor1.connector2
  N2: Arduino_Mega_with_Tellymate.+5V, 2k_Resistor.Pin_0
  N3: Arduino_Mega_with_Tellymate.A1, LM335_Temperature_Sensor1.connector0, LM335_Temperature_Sensor1.connector1, 2k_Resistor.Pin_1
