# Fritzing sketch lm335_temperature_sensor_tellymate_calibrated_v3 (saved by Fritzing 0.3.19b)
breadboards: 1

parts:
  LM335_Temperature_Sensor1 = DIP - 4 pins
  2k_Resistor = Resistor [resistance=2.2k package=THT]
  Arduino_Duemilanove_328_(4_98v) = Arduino
  10k_potentiometer = Rotary Potentiometer (Large) [package=THT]

nets:
  N1: LM335_Temperature_Sensor1.connector0, LM335_Temperature_Sensor1.connector1, LM335_Temperature_Sensor1.connector2, 2k_Resistor.Pin_1, Arduino_Duemilanove_328_(4_98v).GND, Arduino_Duemilanove_328_(4_98v).A1, 10k_potentiometer.leg1, 10k_potentiometer.wiper, 10k_potentiometer.leg2
  N2: 2k_Resistor.Pin_0, Arduino_Duemilanove_328_(4_98v).+5V

notes:
  Tellymate jumpers:
  j1 on
  j2 on
  j3 on
  j4 on
  j5 off
  j6 off
  j7 on
  Jumper
  Use
  J1
  Baud rate selection
  J2
  J3
  J4
  Auto Line Overflow
  J5
  Auto LF on CR
  J6
  PAL/NTSC selection
  J7
  75ohm termination resistor
  Note: Not all TellyMates have J7
  J1-3 : Baud rate selection
  The format for the serial data is 8n1 - eight bits, no parity and a single stop bit.
  The baud rate is determined by jumpers J1, J2 and J3 as follows:
  J3
  J2
  J1
  Baud Rate
  Off
  Off
  Off
  Autobauding
  Off
  Off
  On
  300
  Off
  On
  Off
  1200
  Off
  On
  On
  4800
  On
  Off
  Off
  9k6
  On
  Off
  On
  19k2
  On
  On
  Off
  38k4
  On
  On
  On
  57k6
  Arduino Duemilanove 328
  Arduino Ethernet Shield
  Batsocks Tellymate
  LM335Z temperature sensor
  Pachube.com
  Feed 8281
  "Canberra indoor weather"
  By sirleech
