# Fritzing sketch medidor_temperatura (saved by Fritzing 0.5.2b)
breadboards: 1

parts:
  LM_35 = NPN-Transistor [package="TO92 [THT]"]
  16x2 = LCD screen
  10K = Rotary Potentiometer (Small)
  Arduino_UNO = Arduino

nets:
  N1: LM_35.E, 16x2.LED+, 10K.leg1, Arduino_UNO.+5V
  N2: LM_35.B, Arduino_UNO.A0
  N3: LM_35.C, 16x2.DB5, 16x2.LED-, 10K.leg2, Arduino_UNO.GND
  N4: 16x2.V0, Arduino_UNO.D2
  N5: 16x2.RS, Arduino_UNO.D3
  N6: 16x2.R/W, Arduino_UNO.D4
  N7: 16x2.E, Arduino_UNO.D5
  N8: 16x2.DB4, Arduino_UNO.D11
  N9: 16x2.DB6, Arduino_UNO.D12
  N10: 16x2.DB7, 10K.wiper

notes:
  Medidor de temperatura com saída no Serial Monitor e LCD.
  Auto: Cleber Moretti
  www.binarycodec.blogspot.com
