# Fritzing sketch mysketch-ethernet-relay (saved by Fritzing 0.6.3b)
breadboards: 1

parts:
  Arduino_Ethernet_Shield1 = Arduino Ethernet Shield
  LED1 = LED - 5mm [color="Red (633nm)" package="5 mm [THT]"]
  LED2 = LED - 5mm [color="Red (633nm)" package="5 mm [THT]"]
  LED3 = LED - 5mm [color="Green (570nm)" package="5 mm [THT]"]
  LED4 = LED - 5mm [color="Green (570nm)" package="5 mm [THT]"]
  R1 = Resistor [tolerance=±5% resistance=100 package=THT]
  R2 = Resistor [tolerance=±5% resistance=100 package=THT]
  R3 = Resistor [tolerance=±5% resistance=100 package=THT]
  R4 = Resistor [tolerance=±5% resistance=100 package=THT]

nets:
  N1: Arduino_Ethernet_Shield1.GND, LED1.cathode, LED2.cathode, LED3.cathode, LED4.cathode
  N2: Arduino_Ethernet_Shield1.D9, R3.Pin_1
  N3: Arduino_Ethernet_Shield1.D8, R4.Pin_1
  N4: Arduino_Ethernet_Shield1.D7, R1.Pin_1
  N5: Arduino_Ethernet_Shield1.D6, R2.Pin_1
  N6: LED1.anode, R4.Pin_0
  N7: LED2.anode, R2.Pin_0
  N8: LED3.anode, R3.Pin_0
  N9: LED4.anode, R1.Pin_0

notes:
  Geräteschalter 2
  Geräteschalter 1
