# Fritzing sketch mysketch-ultrasonic (saved by Fritzing 0.6.3b)
breadboards: 1

parts:
  Arduino1 = Arduino
  LED1 = LED - 5mm [color="Yellow (595nm)" package="5 mm [THT]"]
  LED2 = LED - 5mm [color="Green (570nm)" package="5 mm [THT]"]
  LED3 = LED - 5mm [color="Green (570nm)" package="5 mm [THT]"]
  LED4 = LED - 5mm [color="Green (570nm)" package="5 mm [THT]"]
  LED5 = LED - 5mm [color="Orange (620nm)" package="5 mm [THT]"]
  LED6 = LED - 5mm [color="Yellow (595nm)" package="5 mm [THT]"]
  LED7 = LED - 5mm [color="Red (633nm)" package="5 mm [THT]"]
  LED8 = LED - 5mm [color="Red (633nm)" package="5 mm [THT]"]
  LED9 = LED - 5mm [color="Yellow (595nm)" package="5 mm [THT]"]
  LED10 = LED - 5mm [color="Orange (620nm)" package="5 mm [THT]"]
  R1 = Resistor [tolerance=±5% resistance=220 package=THT]
  R2 = Resistor [tolerance=±5% resistance=220 package=THT]
  R3 = Resistor [tolerance=±5% resistance=220 package=THT]
  R4 = Resistor [tolerance=±5% resistance=220 package=THT]
  R5 = Resistor [tolerance=±5% resistance=220 package=THT]
  R6 = Resistor [tolerance=±5% resistance=220 package=THT]
  R7 = Resistor [tolerance=±5% resistance=220 package=THT]
  R8 = Resistor [tolerance=±5% resistance=220 package=THT]
  R9 = Resistor [tolerance=±5% resistance=220 package=THT]
  R10 = Resistor [tolerance=±5% resistance=220 package=THT]

nets:
  N1: Arduino1.GND, LED1.cathode, LED2.cathode, LED3.cathode, LED4.cathode, LED5.cathode, LED6.cathode, LED7.cathode, LED8.cathode, LED9.cathode, LED10.cathode
  N2: Arduino1.D11, R2.Pin_0
  N3: Arduino1.D10, R1.Pin_0
  N4: Arduino1.D9, R4.Pin_0
  N5: Arduino1.D8, R8.Pin_0
  N6: Arduino1.D7, R10.Pin_0
  N7: Arduino1.D6, R9.Pin_0
  N8: Arduino1.D5, R3.Pin_0
  N9: Arduino1.D4, R7.Pin_0
  N10: Arduino1.D3, R6.Pin_0
  N11: Arduino1.D2, R5.Pin_0
  N12: LED1.anode, R9.Pin_1
  N13: LED2.anode, R4.Pin_1
  N14: LED3.anode, R2.Pin_1
  N15: LED4.anode, R1.Pin_1
  N16: LED5.anode, R3.Pin_1
  N17: LED6.anode, R10.Pin_1
  N18: LED7.anode, R5.Pin_1
  N19: LED8.anode, R6.Pin_1
  N20: LED9.anode, R8.Pin_1
  N21: LED10.anode, R7.Pin_1

notes:
  HC-SR04
  5V TRIG ECHO GND
  100cm<------------------------------------------>10cm
