# Fritzing sketch nak (saved by Fritzing 0.6.3b)
breadboards: 1

parts:
  Arduino1 = Arduino
  Takt = Rotary Potentiometer (Small) [maximum_resistance=100kΩ]
  Vol = Basic Force Sensing Resistor (FSR) [package=THT]
  Lautsprecher = Piezo Speaker
  Infrarotsensor = Infrared Proximity Sensor
  Servo = Basic Servo
  Takt-LED = LED - 5mm [color="Yellow (595nm)" package="5 mm [THT]"]
  LED-R = Resistor [tolerance=±5% resistance=220 package=THT]

nets:
  GND: Arduino1.GND, Takt.leg1, Lautsprecher.pin1, Infrarotsensor.GND, Servo.gnd, Takt-LED.cathode
  N1: Arduino1.D7, LED-R.Pin_1
  N2: Arduino1.D5, Servo.pulse
  N3: Arduino1.D3, Vol.pin_1
  5V: Arduino1.+5V, Takt.leg2, Infrarotsensor.Vcc, Servo.vcc
  N4: Arduino1.A0, Takt.wiper
  N5: Arduino1.A1, Infrarotsensor.Vout
  N6: Vol.pin_0, Lautsprecher.pin2
  N7: Takt-LED.anode, LED-R.Pin_0
