# Fritzing sketch nets (saved by Fritzing 0.6.4b)
breadboards: 1

parts:
  R1 = Resistor [tolerance=±5% resistance=220 package=THT]
  D1 = Rectifier Diode [part_number=1N4001 package="Melf DO-213 AB [SMD]"]
  L1 = Inductor [package="400 mil [THT]"]

nets:
  N1: R1.Pin_0, R1.Pin_1, D1.cathode
  N2: D1.anode, L1.pin_0
