# Fritzing sketch nightcandle (saved by Fritzing 0.4.3b)
breadboards: 1

parts:
  Arduino1 = Arduino
  LED1 = Red LED - 5mm
  R1 = Photocell (LDR) [package=THT]
  R2 = Resistor [resistance=220 package=THT]
  R3 = Resistor [resistance=470 package=THT]
  R4 = Resistor [resistance=120k package=THT]
  S1 = Pushbutton [package="[THT]"]

nets:
  N1: Arduino1.GND, LED1.cathode, R4.Pin_1, S1.Pin_1, S1.Pin_2
  N2: Arduino1.D13, R2.Pin_0, S1.Pin_3, S1.Pin_4
  N3: Arduino1.D9, R3.Pin_1
  N4: Arduino1.+5V, R1.pin_1, R2.Pin_1
  N5: Arduino1.A0, R1.pin_0, R4.Pin_0
  N6: LED1.anode, R3.Pin_0
