# Fritzing sketch number86 (saved by Fritzing 0.4.3b)
breadboards: 1

parts:
  Arduino1 = Arduino
  R9 = Resistor [resistance=220 package=THT]
  R10 = Resistor [resistance=220 package=THT]
  TRS1 = Stereo Jack (TRS) 3.5mm [package="PG203J [THT]"]
  R1 = Resistor [resistance=220 package=THT]
  R2 = Resistor [resistance=220 package=THT]
  R3 = Resistor [resistance=220 package=THT]
  R4 = Resistor [resistance=220 package=THT]
  R5 = Resistor [resistance=220 package=THT]
  R6 = Resistor [resistance=220 package=THT]
  R7 = Resistor [resistance=220 package=THT]
  R8 = Resistor [resistance=220 package=THT]
  S2 = Pushbutton [package=THT]
  S1 = mystery part, 6 pins [chip_label=? spacing=300mil]
  C1 = Electrolytic Capacitor [package=THT]
  C2 = Electrolytic Capacitor [package=THT]

nets:
  N1: Arduino1.GND, TRS1.Sleeve, S2.leg1, S1.pin2, C1.-, C2.-
  N2: Arduino1.D13, S1.pin6
  N3: Arduino1.D12, S1.pin3
  N4: Arduino1.D11, S1.pin4
  N5: Arduino1.D10, R10.Pin_1
  N6: Arduino1.D9, R9.Pin_1
  N7: Arduino1.D8, S1.pin1
  N8: Arduino1.D7, R1.Pin_1
  N9: Arduino1.D6, R2.Pin_1
  N10: Arduino1.D5, R3.Pin_1
  N11: Arduino1.D4, R4.Pin_1
  N12: Arduino1.D3, R5.Pin_1
  N13: Arduino1.D2, R6.Pin_1
  N14: Arduino1.D1TX, R7.Pin_1
  N15: Arduino1.D0RX, R8.Pin_1
  N16: Arduino1.RST, S2.leg0
  N17: R9.Pin_0, TRS1.Tip, C1.+
  N18: R10.Pin_0, TRS1.Ring, C2.+

notes:
  gnd
  13
  12
  11
  10
  9
  1
  2
  3
  4
  0
  5
  6
  7
  8
  aref
  ->
  rst
  -
  vin
  5v
  3v3
  red
  yel
  grn
  blu
  com
  e
  m
  k
  c
  a
  h
  d
  r
  i
  n
  t
  feed your head shield
  by theEntropyWorks
  oakland ca
  cc3.0-by-sa
  <----polarity mod
