# Fritzing sketch optocoupler_Optocoupler (saved by Fritzing 0.3.2b)
breadboards: 1

parts:
  U1 = Optocoupler [package=THT]
  VCC1 = obsolete Battery
  LED1 = Red LED - 5mm
  R1 = 220 Ω Resistor [package=THT]
  R2 = 220 Ω Resistor [package=THT]
  Arduino2 = Arduino

nets:
  N1: U1.Pin_1, R2.Pin_1
  N2: U1.Pin_2, Arduino2.GND
  N3: U1.Pin_4, VCC1.-
  N4: U1.Pin_5, LED1.cathode
  N5: VCC1.+, R1.Pin_1
  N6: LED1.anode, R1.Pin_0
  N7: R2.Pin_0, Arduino2.D11

notes:
  An optocoupler can be used to control a circuit that's completely isolated from your microcontroller in order to avoid the risk of short-circuit. In this case, imagine that the LED + battery pack combo is a hacked toy that you're turning on and off with the Arduino.
