# Fritzing sketch oscillateur_de_schmitt (saved by Fritzing 0.4.2b)
breadboards: 1

parts:
  VCC1 = obsolete Battery
  VCC1_2 = obsolete Battery
  VCC1_3 = obsolete Battery
  IC2 = Schmitt-trigger SN74LS14N
  R3 = Resistor [resistance=220 package=THT]
  C1 = Tantalum Capacitor [package=THT]
  J1 = Piezo Speaker
  U1 = Voltage Regulator - 5V [package="TO220 [THT]"]

nets:
  N1: VCC1.-, IC2.GND, J1.pin1
  N2: VCC1.+, VCC1_2.-
  N3: VCC1_2.+, VCC1_3.-
  N4: VCC1_3.+, U1.input_voltage
  N5: IC2.1A, R3.Pin_0, C1.+
  N6: IC2.1Y, R3.Pin_1, J1.pin2
  N7: IC2.VCC, U1.output_voltage
  N8: C1.-, U1.GND

notes:
  T~= 0,7 RC
  Avec le circuit SN74LS14N
  6 triggers de schmitt
  on cree un oscillateur carré avec une resistance et un condensateur

custom parts:
  Schmitt-trigger SN74LS14N: Quadruple Half H-Bridge Motor Driver. Drive two motors with 1.1A with this chip. (SN754410 data sheet from TI here http://focus.ti.com/lit/ds/symlink/sn754410.pdf )
