# Fritzing sketch pap2pul (saved by Fritzing 0.4.3b)
breadboards: 1

parts:
  Arduino1 = Arduino
  S1 = Pushbutton [package="[THT]"]
  S2 = Pushbutton [package="[THT]"]
  R1 = Resistor [resistance=220 package=THT]
  R2 = Resistor [resistance=220 package=THT]
  LED1 = Red LED - 5mm
  LED2 = Red LED - 5mm
  M1 = Stepper Motor - Bipolar  # not connected
  VCC1 = obsolete Battery  # not connected

nets:
  N1: Arduino1.D5, LED1.cathode
  N2: Arduino1.D4, LED2.cathode
  N3: Arduino1.D3, Arduino1.GND, S2.Pin_1, S2.Pin_2, R1.Pin_0, R1.Pin_1, R2.Pin_1, LED1.anode, LED2.anode
  N4: Arduino1.D2, S1.Pin_1, S1.Pin_2, R2.Pin_0
  N5: Arduino1.+5V, S1.Pin_3, S1.Pin_4, S2.Pin_3, S2.Pin_4

notes:
  VM y GND Motor
  Driver de potencia
  DRIVER EN:
  http://txapuzas.blogspot.com/
  5v y GND Driver de potencia
  L1,L2,L3,L4 Driver de potencia
  D1,D2 Driver de potencia
