# Fritzing sketch phoneboothadapt7 (saved by Fritzing 0.6.3b)
perfboards: 1

parts:
  U1 = mystery part, 20 pins [chip_label=? spacing=100mil]
  R1 = Resistor [tolerance=±1% resistance=10k package=THT]
  R2 = Resistor [tolerance=±1% resistance=10k package=THT]
  R3 = Resistor [tolerance=±1% resistance=10k package=THT]
  R4 = Resistor [tolerance=±1% resistance=22k package=THT]
  R5 = Resistor [tolerance=±1% resistance=22k package=THT]
  R6 = Resistor [tolerance=±1% resistance=22k package=THT]
  R7 = Resistor [tolerance=±1% resistance=22k package=THT]
  R8 = Resistor [tolerance=±1% resistance=22k package=THT]
  R9 = Resistor [tolerance=±1% resistance=10k package=THT]
  R10 = Resistor [tolerance=±1% resistance=10k package=THT]
  R11 = Resistor [tolerance=±1% resistance=10k package=THT]
  R12 = Resistor [tolerance=±1% resistance=10k package=THT]
  R13 = Resistor [tolerance=±1% resistance=4.7k package=THT]
  R14 = Resistor [tolerance=±1% resistance=4.7k package=THT]
  R15 = Resistor [tolerance=±1% resistance=4.7k package=THT]
  R16 = Resistor [tolerance=±1% resistance=4.7k package=THT]
  R17 = Resistor [tolerance=±1% resistance=4.7k package=THT]
  R18 = Resistor [tolerance=±1% resistance=4.7k package=THT]
  J1 = female pin header, 2 pins [form="♀ (female)"]
  R19 = Resistor [tolerance=±1% resistance=100k package=THT]

nets:
  N1: U1.pin1, R9.Pin_1, R10.Pin_0
  N2: U1.pin2, R10.Pin_1, R11.Pin_0
  N3: U1.pin3, R11.Pin_1, R12.Pin_0
  N4: U1.pin4, R12.Pin_1, R13.Pin_0
  N5: U1.pin5, R13.Pin_1, R14.Pin_0
  N6: U1.pin6, R14.Pin_1, R15.Pin_0
  N7: U1.pin7, R15.Pin_1, R16.Pin_0
  N8: U1.pin8, R16.Pin_1, R17.Pin_0
  N9: U1.pin9, R17.Pin_1, R18.Pin_1
  N10: U1.pin12, R8.Pin_1
  N11: U1.pin13, R7.Pin_1, R8.Pin_0
  N12: U1.pin14, R6.Pin_1, R7.Pin_0
  N13: U1.pin15, R5.Pin_1, R6.Pin_0
  N14: U1.pin16, R4.Pin_1, R5.Pin_0
  N15: U1.pin17, R3.Pin_1, R4.Pin_0
  N16: U1.pin18, R2.Pin_1, R3.Pin_0
  N17: U1.pin19, R1.Pin_1, R2.Pin_0
  N18: U1.pin20, R1.Pin_0, R9.Pin_0
  N19: R18.Pin_0, J1.pin1, R19.Pin_0
  N20: J1.pin2, R19.Pin_1

notes:
  CIA
  WFB
  PBE
  v1.0
