# Fritzing sketch pointer_instrument (saved by Fritzing 0.3.16b)
breadboards: 1

parts:
  Arduino1 = Arduino
  D1 = Rectifier Diode [package="300 mil [THT]"]
  J2 = female pin header, 2 pins [form="♀ (female)"]
  J3 = Basic Servo
  R1 = Resistor [resistance=1k package=THT]
  R2 = Resistor [resistance=100k package=THT]
  J1 = female pin header, 2 pins [form="♀ (female)"]
  Side1 = Paper_A3_Vertical  # not connected

nets:
  GND: Arduino1.GND, D1.anode, J2.pin1, J3.gnd, R2.Pin_0, J1.pin1
  N1: Arduino1.D9, J3.pulse
  +5V: Arduino1.+5V, J3.vcc
  N2: Arduino1.VIN, J2.pin2
  N3: Arduino1.A0, D1.cathode, R1.Pin_1
  N4: R1.Pin_0, R2.Pin_1, J1.pin2

notes:
  Pointer instrument with servo
  Universal measure instrument
  Michael J. / 07.03.2010
  07.03.2010
  Here you can measure voltages from 0 V up to 5 V
  Servo displays the measured value.
  Print out the scale and you will have a funny analog pointer instrument.
  Modify it for your aim.

custom parts:
  Paper_A3_Vertical: Paper A3 Vertical
