# Fritzing sketch power_switch_lcd_routing (saved by Fritzing 0.5.2b)
breadboards: 1

parts:
  Q1 = NPN-Transistor [package="TO92 [THT]"]
  R1 = Resistor [resistance=1k package=THT]
  D1 = Rectifier Diode [package="300 mil [THT]"]
  J1 = Screw terminal - 2 pins [package=THT]
  IC1 = IC, DIP package, 16 pins [chip_label=4050 spacing=300mil]
  J2 = female pin header, 8 pins [form="♀ (female)"]
  C1 = Ceramic Capacitor [capacitance=0.1mF rated_voltage=35V package="100 mil [THT, multilayer]"]
  J3 = Screw terminal - 2 pins [package=THT]
  IC3 = DIP - 8 pins
  Arduino1 = Arduino

nets:
  N1: Q1.E, IC1.pin8, J2.pin8, C1.0, J3.pin2, IC3.connector0, IC3.connector1, Arduino1.GND
  N2: Q1.B, R1.Pin_1
  N3: Q1.C, D1.anode, J1.pin1
  N4: R1.Pin_0, Arduino1.D8
  N5: D1.cathode, J1.pin2, C1.1, IC3.connector3, Arduino1.+5V
  N6: IC1.pin1, J2.pin1, J2.pin7, Arduino1.3V3
  N7: IC1.pin2, J2.pin2
  N8: IC1.pin3, Arduino1.D3
  N9: IC1.pin4, J2.pin3
  N10: IC1.pin5, Arduino1.D4
  N11: IC1.pin6, J2.pin4
  N12: IC1.pin7, Arduino1.D5
  N13: IC1.pin11, Arduino1.D7
  N14: IC1.pin12, J2.pin6
  N15: IC1.pin14, Arduino1.D6
  N16: IC1.pin15, J2.pin5
  N17: J3.pin1, IC3.connector2
  N18: IC3.connector4, Arduino1.D13
  N19: IC3.connector5, Arduino1.D10
  N20: IC3.connector6, Arduino1.D12

notes:
  PCD8544 LCD
  http://www.sparkfun.com/datasheets/LCD/Monochrome/Nokia5110.pdf
  http://ladyada.net/products/nokia5110/
  HEF4050BP
  http://www.datasheetcatalog.org/datasheet/philips/HEF4050BP.pdf
  Powerswitch needs 40mA
  Transistor for more current.
  TODO:
  1. Get two buttons for temp input
  2.
  LCD Control
  Thermocouple Control
  Power Control
  - Powertail
  + Powertail
  http://powerswitchtail.com/Documents/PST%20I%20Product%20Insert.pdf
  Thermocouple scaler
  http://datasheets.maxim-ic.com/en/ds/MAX6675.pdf
