# Fritzing sketch preamp (saved by Fritzing 0.6.3b)
breadboards: 3

parts:
  LED1 = LED - 5mm [color="Red (633nm)" package="5 mm [THT]"]
  LED2 = LED - 5mm [color="Red (633nm)" package="5 mm [THT]"]
  LED3 = LED - 5mm [color="Red (633nm)" package="5 mm [THT]"]
  LED4 = LED - 5mm [color="Red (633nm)" package="5 mm [THT]"]
  LED5 = LED - 5mm [color="Red (633nm)" package="5 mm [THT]"]
  LED6 = LED - 5mm [color="Red (633nm)" package="5 mm [THT]"]
  LED7 = LED - 5mm [color="Red (633nm)" package="5 mm [THT]"]
  LED8 = LED - 5mm [color="Red (633nm)" package="5 mm [THT]"]
  LED9 = LED - 5mm [color="Red (633nm)" package="5 mm [THT]"]
  LED10 = LED - 5mm [color="Red (633nm)" package="5 mm [THT]"]
  LED12 = LED - 5mm [color="Red (633nm)" package="5 mm [THT]"]
  LED13 = LED - 5mm [color="Red (633nm)" package="5 mm [THT]"]
  LED14 = LED - 5mm [color="Red (633nm)" package="5 mm [THT]"]
  LED15 = LED - 5mm [color="Red (633nm)" package="5 mm [THT]"]
  LED16 = LED - 5mm [color="Red (633nm)" package="5 mm [THT]"]
  LED17 = LED - 5mm [color="Red (633nm)" package="5 mm [THT]"]
  LED18 = LED - 5mm [color="Red (633nm)" package="5 mm [THT]"]
  LED19 = LED - 5mm [color="Red (633nm)" package="5 mm [THT]"]
  LED20 = LED - 5mm [color="Blue (430nm)" package="5 mm [THT]"]
  LED21 = LED - 5mm [color="Blue (430nm)" package="5 mm [THT]"]
  LED22 = LED - 5mm [color="Blue (430nm)" package="5 mm [THT]"]
  U1 = 74HC595 [package="DIP16 [THT]"]
  IC1 = IC, DIP package, 24 pins [chip_label=MAX7219 spacing=300mil]
  U2 = atmega168 [package="DIP28 [THT]"]
  Y1 = Resonator [frequency="16 Mhz" package=THT]
  R1 = Resistor [tolerance=±5% resistance=10k package=THT]
  K1 = Relay [part_number=FRS1B-S package=THT]
  K2 = Relay [part_number=FRS1B-S package=THT]
  K3 = Relay [part_number=FRS1B-S package=THT]
  RE1 = Rotary Encoder [package=THT]
  RE2 = Rotary Encoder [package=THT]
  S1 = Pushbutton [package="[THT]"]
  S2 = Pushbutton [package="[THT]"]
  K4 = Relay [part_number=FRS1B-S package=THT]
  K5 = Relay [part_number=FRS1B-S package=THT]
  K6 = Relay [part_number=FRS1B-S package=THT]
  K7 = Relay [part_number=FRS1B-S package=THT]
  K8 = Relay [part_number=FRS1B-S package=THT]
  LED23 = LED - 5mm [color="Red (633nm)" package="5 mm [THT]"]
  R2 = Resistor [tolerance=±5% resistance=10k package=THT]
  C1 = Electrolytic Capacitor [capacitance=1µF package="100 mil [THT, electrolytic]"]  # not connected
  C2 = Ceramic Capacitor [capacitance=100nF package="100 mil [THT, multilayer]"]
  R3 = Resistor [tolerance=±5% resistance=47k package=THT]  # not connected
  VCC1 = 4 x AAA Battery Mount
  D8 = Rectifier Diode [part_number=1N4001 package="300 mil [THT]"]
  D7 = Rectifier Diode [part_number=1N4001 package="300 mil [THT]"]
  D6 = Rectifier Diode [part_number=1N4001 package="300 mil [THT]"]
  D5 = Rectifier Diode [part_number=1N4001 package="300 mil [THT]"]
  D4 = Rectifier Diode [part_number=1N4001 package="300 mil [THT]"]
  D3 = Rectifier Diode [part_number=1N4001 package="300 mil [THT]"]
  D2 = Rectifier Diode [part_number=1N4001 package="300 mil [THT]"]
  D1 = Rectifier Diode [part_number=1N4001 package="300 mil [THT]"]

nets (from the schematic view):
  N1: LED1.cathode, LED2.cathode, LED3.cathode, LED4.cathode, LED5.cathode, LED6.cathode, LED7.cathode, LED8.cathode, IC1.pin11
  N2: LED1.anode, LED9.anode, LED12.anode, LED21.anode, IC1.pin22
  N3: LED2.anode, LED10.anode, LED13.anode, LED22.anode, IC1.pin14
  N4: LED3.anode, LED14.anode, LED20.anode, LED23.anode
  N5: LED4.anode, LED15.anode
  N6: LED5.anode, LED16.anode, IC1.pin23
  N7: LED6.anode, LED17.anode
  N8: LED7.anode, LED18.anode, IC1.pin15
  N9: LED8.anode, LED19.anode
  N10: LED9.cathode, LED10.cathode, LED20.cathode, LED21.cathode, LED22.cathode, LED23.cathode
  N11: LED12.cathode, LED13.cathode, LED14.cathode, LED15.cathode, LED16.cathode, LED17.cathode, LED18.cathode, LED19.cathode, C2.1, VCC1.+
  N12: U1.Q1, K1.COIL2, D7.cathode
  N13: U1.Q2, K2.COIL2, D6.cathode
  N14: U1.Q3, K4.COIL2, D5.cathode
  N15: U1.Q4, IC1.pin8, K5.COIL2, D4.cathode
  N16: U1.Q5, K6.COIL2, D3.cathode
  N17: U1.Q6, K7.COIL2, D2.cathode
  N18: U1.Q7, K8.COIL2, D1.cathode
  GND: U1.GND, IC1.pin1, U2.Pin_8, U2.Pin_18, U2.Pin_22, Y1.GND, R1.Pin_1, RE1.EncoderPinC, RE2.EncoderPinC, S1.Pin_3, S1.Pin_4, S2.Pin_3, S2.Pin_4
  N19: U1.MR, U1.VCC, IC1.pin2, IC1.pin3, U2.Pin_7, U2.Pin_20, U2.Pin_21, R2.Pin_0
  N20: U1.SH_CP, U2.Pin_12
  N21: U1.OE, U2.Pin_28, R2.Pin_1
  N22: U1.DS, U2.Pin_19
  N23: U1.Q0, K3.COIL2, D8.cathode
  N24: IC1.pin12, U2.Pin_16
  N25: IC1.pin13, U2.Pin_17
  N26: U2.Pin_1, R1.Pin_0
  N27: U2.Pin_4, RE1.EncoderPinB
  N28: U2.Pin_5, RE1.EncoderPinA
  N29: U2.Pin_6, RE2.EncoderPinB
  N30: U2.Pin_9, Y1.pin_1
  N31: U2.Pin_10, Y1.0
  N32: U2.Pin_11, RE2.EncoderPinA
  N33: U2.Pin_14, S1.Pin_1, S1.Pin_2
  N34: U2.Pin_15, S2.Pin_1, S2.Pin_2
  N35: K1.COIL1, K2.COIL1, K3.COIL1, K4.COIL1, K5.COIL1, K7.COIL1, K8.COIL1, VCC1.-, D8.anode, D7.anode, D6.anode, D5.anode, D4.anode, D3.anode, D2.anode, D1.anode
  N36: K1.C1, K1.C2
  N37: K2.C1, K2.C2
  N38: K3.C1, K3.C2
  N39: K4.C1, K4.C2
  N40: K5.C1, K5.C2
  N41: K6.C1, K6.C2
  N42: K7.C1, K7.C2
  N43: K8.C1, K8.C2
