# Fritzing sketch presenter (saved by Fritzing 0.6.4b)
stripboards: 1

parts:
  Arduino1 = Arduino
  LED1 = LED - 5mm [color="Red (633nm)" package="5 mm [THT]"]
  LED4 = RGB LED (com. cathode, rbg) [package="5 mm [THT]"]
  U1 = mystery part, 3 pins [chip_label=? spacing=300mil]
  U2 = mystery part, 3 pins [chip_label=? spacing=300mil]

nets:
  N1: Arduino1.D11, LED1.anode
  N2: Arduino1.D10, LED4.blue_anode
  N3: Arduino1.D9, LED4.common_cathode, U2.pin1, U2.pin2, U2.pin3
  N4: Arduino1.GND, LED1.cathode, LED4.green_anode
  N5: U1.pin1, U1.pin2, U1.pin3
