# Fritzing sketch proximidade_sonoro_LDR (saved by Fritzing 0.5.2b)
breadboards: 1

parts:
  Arduino = Arduino
  LDR = Photocell (LDR) [package=THT]
  SPKR1 = Loudspeaker
  330_ohms = Resistor [resistance=330 package=THT]
  33_Kohms = Resistor [resistance=33k package=THT]

nets:
  N1: Arduino.GND, LDR.pin_0, 330_ohms.Pin_1
  N2: Arduino.D9, SPKR1.pin2
  N3: Arduino.+5V, 33_Kohms.Pin_1
  N4: Arduino.A0, LDR.pin_1, 33_Kohms.Pin_0
  N5: SPKR1.pin1, 330_ohms.Pin_0

notes:
  o alto falante abaixo pode ser substituido por uma caixa de som de PC, por exemplo, caso queira uma maior intensidade sonora.
