# Fritzing sketch pwm (saved by Fritzing 0.6.3b)
breadboards: 1

parts:
  Arduino1 = Arduino
  R1 = Trimmer Potentiometer [maximum_resistance=10kΩ package=THT]
  R2 = Resistor [tolerance=±5% resistance=330 package=THT]
  D1 = Rectifier Diode [part_number=1N4001 package="300 mil [THT]"]
  M1 = DC Motor
  Q1 = NPN-Transistor [package="TO92 [THT]"]

nets:
  N1: Arduino1.D9, R2.Pin_0
  N2: Arduino1.+5V, R1.leg2, D1.cathode, M1.pin_1
  N3: Arduino1.GND, R1.leg1, Q1.C
  N4: Arduino1.A5, R1.wiper
  N5: R2.Pin_1, Q1.E
  N6: D1.anode, M1.pin_2, Q1.B
