# Fritzing sketch quiz_o_matic (saved by Fritzing 0.6.2b)
breadboards: 1

parts:
  Arduino1 = Arduino
  S1 = Pushbutton [package="[THT]"]
  S2 = Pushbutton [package="[THT]"]
  S3 = Pushbutton [package="[THT]"]
  S4 = Pushbutton [package="[THT]"]
  R1 = Resistor [tolerance=±5% resistance=1k package=THT]
  R2 = Resistor [tolerance=±5% resistance=470 package=THT]
  J1 = Screw terminal - 2 pins [package=THT]

nets:
  N1: Arduino1.GND, S2.Pin_1, S2.Pin_2, J1.pin1
  N2: Arduino1.D9, R1.Pin_0
  N3: Arduino1.D7, R2.Pin_0
  N4: Arduino1.A2, S1.Pin_3, S1.Pin_4
  N5: Arduino1.A3, S2.Pin_3, S2.Pin_4
  N6: Arduino1.A4, S3.Pin_3, S3.Pin_4
  N7: Arduino1.A5, S4.Pin_3, S4.Pin_4
  N8: R1.Pin_1, R2.Pin_1, J1.pin2
