# Fritzing sketch regulador_voltaje (saved by Fritzing 0.4.3b)
breadboards: 1

parts:
  U1 = Voltage Regulator - 5V [package="TO220 [THT]"]
  1n4004 = Rectifier Diode [package="300 mil [THT]"]
  1n4004_2 = Rectifier Diode [package="300 mil [THT]"]
  1n4004_3 = Rectifier Diode [package="300 mil [THT]"]
  1n4004_4 = Rectifier Diode [package="300 mil [THT]"]
  1n4004_5 = Rectifier Diode [package="300 mil [THT]"]
  1n4004_6 = Rectifier Diode [package="300 mil [THT]"]
  104 = Ceramic Capacitor [package=THT]
  104_2 = Ceramic Capacitor [package=THT]
  100uf = Electrolytic Capacitor [package=THT]

nets:
  5V: U1.input_voltage, 1n4004_6.cathode, 104_2.pin_1, 100uf.+
  GND: U1.GND, 1n4004_6.anode, 104.pin_1, 104_2.pin_0, 100uf.-
  N1: U1.output_voltage, 1n4004.anode, 1n4004_2.anode, 1n4004_3.anode, 1n4004_4.anode, 1n4004_5.anode, 104.pin_0

notes:
  OUT PUTS
  Usar 9 volts para reducir a 5 volts
  Usar 12 volts para reducir a 9 volts. (con un 7809)
  CGG
  http://cgg.dossier.wordpress.com
