# Fritzing sketch relay_control (saved by Fritzing 0.3.19b)
breadboards: 1

parts:
  R1 = Resistor [resistance=470 package=THT]
  R1_2 = Resistor [resistance=470 package=THT]
  R1_3 = Resistor [resistance=470 package=THT]
  R1_4 = Resistor [resistance=470 package=THT]
  R1_5 = Resistor [resistance=470 package=THT]
  R1_6 = Resistor [resistance=470 package=THT]
  R1_7 = Resistor [resistance=470 package=THT]
  R1_8 = Resistor [resistance=470 package=THT]
  O8_O7 = Screw terminal - 2 pins [package=THT]
  GND_15V = Screw terminal - 2 pins [package=THT]
  O6_O5 = Screw terminal - 2 pins [package=THT]
  O4_O3 = Screw terminal - 2 pins [package=THT]
  O2_O1 = Screw terminal - 2 pins [package=THT]
  R2 = Resistor [resistance=2.2k package=THT]
  LED1 = green LED - 5mm
  R2_2 = Resistor [resistance=2.2k package=THT]
  LED1_2 = green LED - 5mm
  R2_3 = Resistor [resistance=2.2k package=THT]
  R2_4 = Resistor [resistance=2.2k package=THT]
  LED1_3 = green LED - 5mm
  R2_5 = Resistor [resistance=2.2k package=THT]
  R2_6 = Resistor [resistance=2.2k package=THT]
  R2_7 = Resistor [resistance=2.2k package=THT]
  LED1_4 = green LED - 5mm
  Made = green LED - 5mm
  LED1_5 = green LED - 5mm
  LED1_6 = green LED - 5mm
  Relay_Controller = Arduino
  ULN2803A = ULN2803A [package=THT]
  C1 = Electrolytic Capacitor [package=THT]
  C2 = Ceramic Capacitor [package=THT]
  LED = green LED - 5mm
  R2_8 = Resistor [resistance=2.2k package=THT]

nets:
  N1: R1.Pin_0, ULN2803A.In_1
  N2: R1.Pin_1, Relay_Controller.D0RX
  N3: R1_2.Pin_0, ULN2803A.In_2
  N4: R1_2.Pin_1, Relay_Controller.D1TX
  N5: R1_3.Pin_0, ULN2803A.In_3
  N6: R1_3.Pin_1, Relay_Controller.D2
  N7: R1_4.Pin_0, ULN2803A.In_4
  N8: R1_4.Pin_1, Relay_Controller.D4
  N9: R1_5.Pin_0, ULN2803A.In_5
  N10: R1_5.Pin_1, Relay_Controller.D7
  N11: R1_6.Pin_0, ULN2803A.In_6
  N12: R1_6.Pin_1, Relay_Controller.D8
  N13: R1_7.Pin_0, ULN2803A.In_7
  N14: R1_7.Pin_1, Relay_Controller.D12
  N15: R1_8.Pin_0, ULN2803A.In_8
  N16: R1_8.Pin_1, Relay_Controller.D13
  N17: O8_O7.pin1, O8_O7.pin2, R2.Pin_0, R2_2.Pin_0, ULN2803A.Out_8, ULN2803A.Out_7
  N18: GND_15V.pin1, LED1.cathode, LED1_2.cathode, LED1_3.cathode, LED1_4.cathode, Made.cathode, LED1_5.cathode, LED1_6.cathode, Relay_Controller.GND, ULN2803A.0V, C1.-, C2.pin_0, LED.cathode
  N19: GND_15V.pin2, ULN2803A.COM_-_Common, C1.+, C2.pin_1
  N20: O6_O5.pin1, R2_3.Pin_0, ULN2803A.Out_5
  N21: O6_O5.pin2, R2_4.Pin_0, ULN2803A.Out_6
  N22: O4_O3.pin1, R2_5.Pin_0, ULN2803A.Out_3
  N23: O4_O3.pin2, ULN2803A.Out_4, R2_8.Pin_0
  N24: O2_O1.pin1, R2_7.Pin_0, ULN2803A.Out_1
  N25: O2_O1.pin2, R2_6.Pin_0, ULN2803A.Out_2
  N26: R2.Pin_1, LED1.anode
  N27: R2_2.Pin_1, LED1_2.anode
  N28: R2_3.Pin_1, LED1_6.anode
  N29: R2_4.Pin_1, LED1_3.anode
  N30: R2_5.Pin_1, Made.anode
  N31: R2_6.Pin_1, LED1_5.anode
  N32: R2_7.Pin_1, LED1_4.anode
  N33: LED.anode, R2_8.Pin_1

notes:
  by Tarzan
  V0.1 not yet tested
