# Fritzing sketch rele_acionamento (saved by Fritzing 0.5.2b)
breadboards: 1

parts:
  Arduino = Arduino
  Q1 = PNP-Transistor [package="TO92 [THT]"]
  K1 = Relay [package=THT]
  D1 = Rectifier Diode [package="300 mil [THT]"]
  R1 = Resistor [resistance=470 package=THT]

nets:
  N1: Arduino.GND, K1.A, D1.anode
  N2: Arduino.D13, R1.Pin_0
  N3: Arduino.+5V, Q1.E
  N4: Q1.B, R1.Pin_1
  N5: Q1.C, K1.B, D1.cathode
  N6: K1.C1, K1.C2

notes:
  Para este acionamento estamos utilizando um transitor PNP- 3906 http://www.datasheetcatalog.org/datasheet/vishay/85129.pdf
  saida 2 (multimetro -ohms
  saida1 (multimetro - ohms)
