# Fritzing sketch rf (saved by Fritzing 0.4.3b)
breadboards: 1

parts:
  Arduino1 = Arduino Nano v2.3
  LED1 = Red LED - 5mm
  R1 = Resistor [resistance=220 package=THT]
  R3 = Resistor [resistance=220 package=THT]
  R4 = Resistor [resistance=220 package=THT]
  R5 = Resistor [resistance=220 package=THT]
  R1_2 = Resistor [resistance=220 package=THT]
  R2 = Resistor [resistance=220 package=THT]
  R7 = Resistor [resistance=220 package=THT]
  R8 = Resistor [resistance=220 package=THT]
  R6 = Resistor [resistance=220 package=THT]
  R10 = Resistor [resistance=220 package=THT]
  R9 = Resistor [resistance=220 package=THT]
  U1 = mystery part, 8 pins [chip_label=rfm spacing=300mil]

nets:
  N1: Arduino1.GND, LED1.cathode, R3.Pin_1, R4.Pin_1, R5.Pin_1, R1_2.Pin_1, R2.Pin_1, U1.pin8
  N2: Arduino1.D3, R10.Pin_0
  N3: Arduino1.D4, R9.Pin_0
  N4: Arduino1.D5, R8.Pin_0
  N5: Arduino1.D7, R7.Pin_0
  N6: Arduino1.D8, R6.Pin_0
  N7: Arduino1.+5V, R1.Pin_0
  N8: LED1.anode, R1.Pin_1
  N9: R3.Pin_0, R8.Pin_1, U1.pin4
  N10: R4.Pin_0, R9.Pin_1, U1.pin5
  N11: R5.Pin_0, R10.Pin_1, U1.pin6
  N12: R1_2.Pin_0, R6.Pin_1, U1.pin2
  N13: R2.Pin_0, R7.Pin_1, U1.pin3
