# Fritzing sketch rj45breakout (saved by Fritzing 0.6.4b)

parts:
  RJ45 = RJ45
  Header = female pin header, 8 pins [form="♀ (female)"]

nets:
  N1: RJ45.connector0, Header.pin1
  N2: RJ45.connector1, Header.pin2
  N3: RJ45.connector2, Header.pin3
  N4: RJ45.connector3, Header.pin4
  N5: RJ45.connector4, Header.pin5
  N6: RJ45.connector5, Header.pin6
  N7: RJ45.connector6, Header.pin7
  N8: RJ45.connector7, Header.pin8

notes:
  ---
  EBO
