# Fritzing sketch robot_moteurCC_switch2_Hbridge (saved by Fritzing 0.5.2b)
breadboards: 1

parts:
  IC1 = H-Bridge [package=THT]
  Arduino1 = Arduino
  S4 = Toggle Switch [package=THT]
  S5 = Toggle Switch [package=THT]
  M1 = DC Motor
  M2 = DC Motor
  VCC1 = obsolete Battery

nets:
  N1: IC1.1_2EN, IC1.VCC2, VCC1.+
  N2: IC1.1A, Arduino1.D5
  N3: IC1.1Y, M2.pin_1
  GND1: IC1.GND1, IC1.GND2, VCC1.-
  N4: IC1.2Y, M2.pin_2
  N5: IC1.2A, Arduino1.D4
  N6: IC1.3_4EN, IC1.VCC1
  N7: IC1.3A, Arduino1.D2
  N8: IC1.3Y, M1.pin_2
  GND3: IC1.GND3, IC1.GND4
  N9: IC1.4Y, M1.pin_1
  N10: IC1.4A, Arduino1.D3
  N11: Arduino1.GND, S4.COM, S5.COM
  N12: Arduino1.D7, S5.L1
  N13: Arduino1.D6, S4.L1
  N14: Arduino1.+5V, S4.L2, S5.L2
