# Fritzing sketch rommelrubot (saved by Fritzing 0.4.3b)
breadboards: 1

parts:
  Dwengo_Board1 = Dwengo Board
  M1 = DC Motor
  J1 = Basic Servo
  J2 = Infrared Proximity Sensor
  J3 = Infrared Proximity Sensor
  R1 = Resistor [resistance=10k package=THT]  # not connected
  R2 = Resistor [resistance=10k package=THT]
  U1 = mystery part, 6 pins [chip_label=BlueSMIRF spacing=300mil]

nets:
  VCC: Dwengo_Board1.PIC_pin_11_VCC, J2.Vcc, J3.Vcc, U1.pin5
  GND: Dwengo_Board1.PIC_pin_12_GND, J2.GND, J3.GND, R2.Pin_0, U1.pin4
  N1: Dwengo_Board1.PIC_pin_25_Pinguino_pin_8, U1.pin2
  N2: Dwengo_Board1.PIC_pin_26_Pinguino_pin_9, U1.pin3
  N3: Dwengo_Board1.pin_41_Dwengo_Driver_Out_1, M1.pin_1
  N4: Dwengo_Board1.pin_42_Dwengo_Driver_Out_2, J1.pulse
  N5: Dwengo_Board1.pin_43_Dwengo_Driver_Out_3, M1.pin_2
  N6: J2.Vout, R2.Pin_1
  N7: U1.pin1, U1.pin6

custom parts:
  Dwengo Board: A flexible, programmable, electronics prototyping platform with in its core a PIC from Microchip. See http://www.dwengo.org
