# Fritzing sketch schematic (saved by Fritzing 0.4.3b)
breadboards: 1

parts:
  Arduino1 = Arduino
  LED2 = white LED - 5mm
  LED2_2 = white LED - 5mm
  LED2_3 = white LED - 5mm
  LED2_4 = white LED - 5mm
  LED2_5 = white LED - 5mm
  LED2_6 = Red LED - 5mm
  LED2_7 = green LED - 5mm
  LED2_8 = Blue LED - 5mm
  LED2_9 = Red LED - 5mm
  LED2_10 = white LED - 5mm
  LED2_11 = Red LED - 5mm
  LED2_12 = white LED - 5mm
  LED2_13 = white LED - 5mm
  R1 = Resistor [resistance=10k package=THT]
  R1_2 = Resistor [resistance=10k package=THT]
  R1_3 = Resistor [resistance=10k package=THT]
  R1_4 = Resistor [resistance=10k package=THT]
  R1_5 = Resistor [resistance=10k package=THT]
  R1_6 = Resistor [resistance=10k package=THT]
  VCC1 = obsolete Battery

nets:
  N1: Arduino1.D11, LED2_6.anode, LED2_7.anode, LED2_8.anode, LED2_9.anode, LED2_10.anode, LED2_11.anode, LED2_12.anode, LED2_13.anode
  N2: Arduino1.D10, LED2_5.anode
  N3: Arduino1.D9, LED2_4.anode
  N4: Arduino1.D8, LED2_3.anode
  N5: Arduino1.D7, LED2_2.anode
  N6: Arduino1.D6, LED2.anode
  N7: Arduino1.GND, R1_3.Pin_1, R1_4.Pin_1, R1_5.Pin_1, R1_6.Pin_1
  N8: LED2.cathode, R1_6.Pin_0
  N9: LED2_2.cathode, R1_5.Pin_0
  N10: LED2_3.cathode, R1_4.Pin_0
  N11: LED2_4.cathode, R1_3.Pin_0
  N12: LED2_5.cathode, R1_2.Pin_0
  N13: LED2_6.cathode, LED2_7.cathode, LED2_8.cathode, LED2_9.cathode, LED2_10.cathode, LED2_11.cathode, LED2_12.cathode, LED2_13.cathode, R1.Pin_0
  N14: R1.Pin_1, R1_2.Pin_1, VCC1.-
