# Fritzing sketch servo_iphone (saved by Fritzing 0.5.2b)
breadboards: 1

parts:
  LED1 = Red LED - 5mm [package="5 mm [THT]"]
  J1 = Basic Servo
  Arduino1 = Arduino
  R1 = Resistor [resistance=220 package=THT]
  R2 = Resistor [resistance=220 package=THT]
  R3 = Resistor [resistance=220 package=THT]
  LED1_2 = Red LED - 5mm [package="5 mm [THT]"]
  LED1_3 = Red LED - 5mm [package="5 mm [THT]"]

nets:
  N1: LED1.cathode, R1.Pin_1
  N2: LED1.anode, Arduino1.D11
  GND: J1.gnd, Arduino1.GND, R1.Pin_0, R2.Pin_1, R3.Pin_1
  VCC: J1.vcc, Arduino1.+5V
  N3: J1.pulse, Arduino1.D9
  N4: Arduino1.D7, LED1_2.cathode
  N5: Arduino1.D3, LED1_3.anode
  N6: R2.Pin_0, LED1_2.anode
  N7: R3.Pin_0, LED1_3.cathode
