# Fritzing sketch servo_ldr (saved by Fritzing 0.5.2b)
breadboards: 1

parts:
  Arduino1 = Arduino
  R1 = Photocell (LDR) [package=THT]
  J1 = Basic Servo
  R2 = Resistor [resistance=220 package=THT]

nets:
  N1: Arduino1.D9, J1.pulse
  +5V: Arduino1.+5V, R1.pin_1, J1.vcc
  GND: Arduino1.GND, J1.gnd, R2.Pin_0
  N2: Arduino1.A2, R1.pin_0, R2.Pin_1
