# Fritzing sketch sharePower33 (saved by Fritzing 0.3.8b)
breadboards: 1

parts:
  J1 = Screw terminal [package=THT]
  J2 = Screw terminal [package=THT]
  U1 = Voltage Regulator -- 3.3 V -- LM1117
  C2 = Tantalum Capacitor
  C3 = Tantalum Capacitor

nets:
  N1: J1.pin1, J2.pin2, U1.GND, C2.NEG, C3.NEG
  N2: J1.pin2, U1.IN, C2.POS
  N3: J2.pin1, U1.OUT, C3.POS

notes:
  +V in -->
  in gnd -->
  <-- +3.3 V out
  <-- out gnd

custom parts:
  Voltage Regulator -- 3.3 V -- LM1117: LM1117-3.3 Voltage regulator, 3.3 V output. Note that the pinout order is not the same as LM7805 or LM7833.
