# Fritzing sketch socail_coffee_schematics (saved by Fritzing 0.6.5b)
breadboards: 1

parts:
  Arduino_Ethernet_Shield1 = Arduino Ethernet Shield
  IC1 = ULN2003A [package="SO16 [SMD]"]
  RGB_Strip = RGB
  VCC1 = Battery block 9V
  LEM_10_B5_Current_sensor1 = Current_Sensor
  Water_sensor_level1 = Fluid_level_sensor
  R1 = Resistor [tolerance=±5% resistance=10k package=THT]

nets:
  N1: Arduino_Ethernet_Shield1.GND#1, VCC1.-
  N2: Arduino_Ethernet_Shield1.D8, IC1.In_1
  N3: Arduino_Ethernet_Shield1.D7, Water_sensor_level1.connector1, R1.Pin_1
  N4: Arduino_Ethernet_Shield1.D5, IC1.In_2
  N5: Arduino_Ethernet_Shield1.D3, IC1.In_3
  N6: Arduino_Ethernet_Shield1.+5V, Water_sensor_level1.connector0
  N7: Arduino_Ethernet_Shield1.GND#19, LEM_10_B5_Current_sensor1.connector0, R1.Pin_0
  N8: Arduino_Ethernet_Shield1.A2, LEM_10_B5_Current_sensor1.connector1
  N9: IC1.Out_3, RGB_Strip.connector0
  N10: IC1.Out_2, RGB_Strip.connector1
  N11: IC1.Out_1, RGB_Strip.connector2
  N12: RGB_Strip.connector3, VCC1.+

notes:
  VCC [9,12V]
