# Fritzing sketch solenoid_driver (saved by Fritzing 0.6.3b)
breadboards: 1

parts:
  Q1 = npn-Powertransistor [package="TO220 [THT]"]
  R1 = Resistor [resistance=150 tolerance=±5% package=THT]
  Valve = Screw terminal - 2 pins [package=THT]
  D1 = Rectifier Diode [part_number=1N4001 package="300 mil [THT]"]
  C1 = Ceramic Capacitor [capacitance=0.1µF rated_voltage=35V package="100 mil [THT, multilayer]"]
  24V_DC = Screw terminal - 2 pins [package=THT]
  R2 = Resistor [resistance=220 tolerance=±5% package=THT]
  J1 = female pin header, 2 pins [form="♀ (female)"]
  J2 = Screw_terminal___2_pins

nets:
  N1: Q1.base, R1.Pin_1
  N2: Q1.collector, Valve.pin2, D1.anode, C1.0
  N3: Q1.emitter, 24V_DC.pin1, R2.Pin_1, J1.pin1
  N4: R1.Pin_0, J1.pin2
  N5: Valve.pin1, D1.cathode, C1.1, 24V_DC.pin2
  N6: R2.Pin_0, J2.connector1
