# Fritzing sketch sonic (saved by Fritzing 0.3.16b)
breadboards: 1

parts:
  Arduino1 = Arduino
  LCD1 = LCD screen
  HC-SR04 = IC, SIP package, 4 pins [chip_label=IC spacing=300mil]

nets:
  GND: Arduino1.GND, LCD1.VSS, LCD1.V0, HC-SR04.pin4
  N1: Arduino1.D13, HC-SR04.pin2
  N2: Arduino1.D12, HC-SR04.pin3
  N3: Arduino1.D11, LCD1.RS
  N4: Arduino1.D10, LCD1.R/W
  N5: Arduino1.D9, LCD1.E
  N6: Arduino1.D7, LCD1.DB4
  N7: Arduino1.D6, LCD1.DB5
  N8: Arduino1.D5, LCD1.DB6
  N9: Arduino1.D4, LCD1.DB7
  +5V: Arduino1.+5V, LCD1.VDD, HC-SR04.pin1
