# Fritzing sketch spectrum_msgeq7-arduino-display (saved by Fritzing 0.6.5b)
breadboards: 1

parts:
  IC1 = IC, DIP package, 8 pins [chip_label=MSGEQ7 spacing=300mil]
  LCD1 = LCD screen
  TRS1 = Stereo Jack (TRS) 3.5mm [package="PG203J [THT]"]
  R1 = Rotary Potentiometer (Small) [maximum_resistance=100kΩ]
  R2 = Resistor [tolerance=±5% resistance=200k package=THT]
  C3 = Ceramic Capacitor [capacitance=33pF package="100 mil [THT, multilayer]"]
  C4 = Ceramic Capacitor [capacitance=0.1µF package="100 mil [THT, multilayer]"]
  C5 = Ceramic Capacitor [capacitance=0.1µF package="100 mil [THT, multilayer]"]
  C6 = Ceramic Capacitor [capacitance=100nF package="100 mil [THT, multilayer]"]
  Arduino1 = Arduino

nets:
  VDD: IC1.pin1, LCD1.VDD, LCD1.LED+, R2.Pin_0, C4.0, Arduino1.+5V
  VSS: IC1.pin2, LCD1.VSS, LCD1.R/W, LCD1.LED-, TRS1.Sleeve, R1.wiper, C3.0, C4.1, C5.1, Arduino1.GND
  N1: IC1.pin3, Arduino1.A0
  N2: IC1.pin4, Arduino1.D4
  N3: IC1.pin5, C6.0
  N4: IC1.pin6, C5.0
  N5: IC1.pin7, Arduino1.D5
  N6: IC1.pin8, R2.Pin_1, C3.1
  N7: LCD1.V0, R1.leg1
  N8: LCD1.RS, Arduino1.D12
  N9: LCD1.E, Arduino1.D11
  N10: LCD1.DB4, Arduino1.D7
  N11: LCD1.DB5, Arduino1.D6
  N12: LCD1.DB6, Arduino1.D3
  N13: LCD1.DB7, Arduino1.D2
  N14: TRS1.Ring, C6.1

notes:
  Part List
  1xPoti
  1xHD44780 Display
  1xMSGEQ7 IC
  1x200KOhm Resistor
  1x33pF Capacitor
  1x100nF Capacitor
  2x0,1uF Capacitor
  1xAudioJack
