# Fritzing sketch spectrum_msgeq7-atmega-display (saved by Fritzing 0.6.5b)
breadboards: 1

parts:
  U1 = atmega168 [package="DIP28 [THT]"]
  IC1 = IC, DIP package, 8 pins [chip_label=MSGEQ7 spacing=300mil]
  XTAL1 = Crystal [frequency="16 Mhz" package=THT]
  C1 = Ceramic Capacitor [capacitance=22pF voltage=6.3V package="100 mil [THT, multilayer]"]
  C2 = Ceramic Capacitor [capacitance=22pF package="100 mil [THT, multilayer]"]
  LCD1 = LCD screen
  TRS1 = Stereo Jack (TRS) 3.5mm [package="PG203J [THT]"]
  R1 = Rotary Potentiometer (Small) [maximum_resistance=100kΩ]
  R2 = Resistor [tolerance=±5% resistance=200k package=THT]
  C3 = Ceramic Capacitor [capacitance=33pF package="100 mil [THT, multilayer]"]
  C4 = Ceramic Capacitor [capacitance=0.1µF package="100 mil [THT, multilayer]"]
  C5 = Ceramic Capacitor [capacitance=0.1µF package="100 mil [THT, multilayer]"]
  C6 = Ceramic Capacitor [capacitance=100nF package="100 mil [THT, multilayer]"]
  VCC1 = Battery block 9V
  R3 = Resistor [tolerance=±5% resistance=220 package=THT]

nets:
  N1: U1.Pin_4, LCD1.DB7
  N2: U1.Pin_5, LCD1.DB6
  N3: U1.Pin_6, IC1.pin4
  N4: U1.Pin_7, U1.Pin_20, IC1.pin1, LCD1.VDD, LCD1.LED+, R2.Pin_0, C4.0, R3.Pin_1
  N5: U1.Pin_8, U1.Pin_22, IC1.pin2, C1.0, C2.1, LCD1.VSS, LCD1.R/W, LCD1.LED-, TRS1.Sleeve, R1.wiper, C3.0, C4.1, C5.1, VCC1.-
  N6: U1.Pin_9, XTAL1.pin_1, C2.0
  N7: U1.Pin_10, XTAL1.pin_0, C1.1
  N8: U1.Pin_11, IC1.pin7
  N9: U1.Pin_12, LCD1.DB5
  N10: U1.Pin_13, LCD1.DB4
  N11: U1.Pin_17, LCD1.E
  N12: U1.Pin_18, LCD1.RS
  N13: U1.Pin_23, IC1.pin3
  N14: IC1.pin5, C6.0
  N15: IC1.pin6, C5.0
  N16: IC1.pin8, R2.Pin_1, C3.1
  N17: LCD1.V0, R1.leg1
  N18: TRS1.Ring, C6.1
  N19: VCC1.+, R3.Pin_0

notes:
  Part List
  1xPoti
  1xHD44780 Display
  1xMSGEQ7 IC
  1xATMEGA168 IC
  1x16MHZ Quarz
  1x200KOhm Resistor
  1x220Ohm Resistor
  1x33pF Capacitor
  1x100nF Capacitor
  2x0,1uF Capacitor
  2x22pF Capacitor
  1xAudioJack
  1x9V BatteryBlock
