# Fritzing sketch stroboskop (saved by Fritzing 0.6.3b)
breadboards: 1

parts:
  LED1 = LED - 5mm [color="White (8000K)" current=25mA package="5 mm [THT]"]
  LED2 = LED - 5mm [color="White (8000K)" package="5 mm [THT]"]
  LED3 = LED - 5mm [color="White (8000K)" package="5 mm [THT]"]
  LED4 = LED - 5mm [color="White (8000K)" package="5 mm [THT]"]
  LED5 = LED - 5mm [color="White (8000K)" package="5 mm [THT]"]
  LED6 = LED - 5mm [color="White (8000K)" package="5 mm [THT]"]
  R4 = Resistor [tolerance=±5% resistance=470 package=THT]
  R5 = Resistor [tolerance=±5% resistance=47 package=THT]
  R6 = Resistor [tolerance=±5% resistance=47 package=THT]
  R7 = Resistor [tolerance=±5% resistance=470 package=THT]
  R8 = Resistor [tolerance=±5% resistance=470 package=THT]
  R9 = Resistor [tolerance=±5% resistance=470 package=THT]
  R1 = Resistor [tolerance=±5% resistance=10k package=THT]
  R3 = Resistor [tolerance=±5% resistance=10k package=THT]
  R2 = Resistor [tolerance=±5% resistance=4.7k package=THT]
  C1 = Electrolytic Capacitor [capacitance=100µF voltage=35V package="100 mil [THT, electrolytic]"]
  C2 = Ceramic Capacitor [capacitance=10nF package="100 mil [THT, multilayer]"]
  C3 = Electrolytic Capacitor [capacitance=4.7µF voltage=100V package="100 mil [THT, electrolytic]"]
  U1 = 555 Timer [package="DIP8 [THT]"]
  P1 = Rotary Potentiometer (Small) [maximum_resistance=1MΩ]
  Power_plug1 = Power plug [part_number="12V DC"]
  Q1 = PNP-Transistor [package="TO92 [THT]"]

nets:
  N1: LED1.cathode, R4.Pin_0
  N2: LED1.anode, LED2.anode, LED3.anode, LED4.anode, LED5.anode, LED6.anode, R3.Pin_0, C1.+, U1.Reset, U1.Vcc_Supply_Voltage, P1.leg1, Power_plug1.VCC
  N3: LED2.cathode, R5.Pin_0
  N4: LED3.cathode, R6.Pin_0
  N5: LED4.cathode, R7.Pin_0
  N6: LED5.cathode, R8.Pin_0
  N7: LED6.cathode, R9.Pin_0
  N8: R4.Pin_1, R5.Pin_1, R6.Pin_1, R7.Pin_1, R8.Pin_1, R9.Pin_1, Q1.E
  N9: R1.Pin_0, C3.+, U1.Trigger, U1.Threshold
  N10: R1.Pin_1, U1.Discharge, P1.leg2
  N11: R3.Pin_1, R2.Pin_1, Q1.B
  N12: R2.Pin_0, U1.Output
  N13: C1.-, C2.1, C3.-, U1.Ground, Power_plug1.GND, Q1.C
  N14: C2.0, U1.Control_Voltage
