# Fritzing sketch strom_und_Spannung (saved by Fritzing 0.6.3b)
breadboards: 1

parts:
  ACS709_Stromsensor = ACS709_Stromsensor_Breakout_Board__75_to__75A
  Arduino1 = Arduino
  Spannungsquelle = Power plug
  Verbraucher = Power plug
  R1 = Resistor [tolerance=±5% resistance=390 package=THT]
  R2 = Resistor [tolerance=±5% resistance=100 package=THT]

nets:
  N1: ACS709_Stromsensor.connector0, Spannungsquelle.VCC
  N2: ACS709_Stromsensor.connector1, Verbraucher.VCC, R1.Pin_1
  N3: ACS709_Stromsensor.connector7, Arduino1.A0
  N4: ACS709_Stromsensor.connector8, Arduino1.+5V
  GND: ACS709_Stromsensor.connector9, Arduino1.GND, Spannungsquelle.GND, Verbraucher.GND, R2.Pin_1
  N5: Arduino1.A1, R1.Pin_0, R2.Pin_0

notes:
  Stromquelle
  Stromabnehmer
