# Fritzing sketch tb_projekt_motor_shield_v1_2 (saved by Fritzing 0.6.5b)
breadboards: 1

parts:
  C2 = Electrolytic Capacitor [package=THT]
  C1 = Electrolytic Capacitor [package=THT]
  IC2 = IC, DIP package, 14 pins [chip_label=74HC00 spacing=300mil]
  IC1 = H-Bridge [package=THT]
  C3 = Ceramic Capacitor [capacitance=100nF voltage=50V package="100 mil [THT, multilayer]"]
  R1 = Resistor [tolerance=±5% resistance=10k package=THT]
  R2 = Resistor [tolerance=±5% resistance=10k package=THT]
  R3 = Resistor [tolerance=±5% resistance=10k package=THT]
  R4 = Resistor [tolerance=±5% resistance=10k package=THT]
  C4 = Ceramic Capacitor [capacitance=100nF voltage=50V package="100 mil [THT, multilayer]"]
  C5 = Ceramic Capacitor [capacitance=100nF voltage=50V package="100 mil [THT, multilayer]"]
  C6 = Ceramic Capacitor [capacitance=100nF voltage=50V package="100 mil [THT, multilayer]"]
  Arduino1 = Arduino
  Power_plug1 = Power plug
  R5 = Resistor [tolerance=±5% resistance=0 package=THT]
  M2 = Screw terminal - 2 pins [package=THT]
  Vin = Screw terminal - 2 pins [package=THT]
  M1 = Screw terminal - 2 pins [package=THT]

nets:
  GND: C2.-, C1.-, IC2.pin7, IC1.GND1, IC1.GND2, IC1.GND3, IC1.GND4, C3.1, R1.Pin_1, R2.Pin_1, R3.Pin_1, R4.Pin_1, C4.0, C5.1, C6.0, Arduino1.GND, Power_plug1.GND, Vin.pin2
  N1: C2.+, IC2.pin14, IC1.VCC1, Arduino1.+5V
  N2: C1.+, IC1.VCC2, Power_plug1.VCC, R5.Pin_0, Vin.pin1
  N3: IC2.pin1, IC2.pin2, R3.Pin_0, Arduino1.D13
  N4: IC2.pin3, IC2.pin9, IC2.pin10, IC1.4A
  N5: IC2.pin4, IC2.pin5, IC2.pin11, IC1.1A
  N6: IC2.pin6, IC1.2A
  N7: IC2.pin8, IC1.3A
  N8: IC2.pin12, IC2.pin13, R4.Pin_0, Arduino1.D12
  N9: IC1.1_2EN, R2.Pin_0, Arduino1.D10
  N10: IC1.1Y, C3.0, M2.pin2
  N11: IC1.2Y, C4.1, M2.pin1
  N12: IC1.3_4EN, R1.Pin_0, Arduino1.D9
  N13: IC1.3Y, C6.1, M1.pin2
  N14: IC1.4Y, C5.0, M1.pin1
  N15: Arduino1.VIN, R5.Pin_1

notes:
  Motor Shield
  V1.1
  arduino-praxis.ch
  +
