# Fritzing sketch temp-plug (saved by Fritzing 0.4.3b)
breadboards: 1

parts:
  Q1 = PNP-Transistor [package="TO92 [THT]"]
  R1 = Resistor [resistance=4.7k package=THT]
  J1 = female pin header, 6 pins [form="♂ (male)"]

nets:
  N1: Q1.E, R1.Pin_0, J1.pin3
  N2: Q1.B, R1.Pin_1, J1.pin2
  N3: Q1.C, J1.pin4
