# Fritzing sketch temp_sen_LM35 (saved by Fritzing 0.6.3b)
breadboards: 1

parts:
  Arduino1 = Arduino
  T1 = LM35 Temperature Sensor [package="TO92 [THT]"]
  S2 = Toggle Switch [package=THT]

nets:
  N1: Arduino1.D3, S2.L2
  N2: Arduino1.+5V, T1.+Vs, S2.COM
  GND: Arduino1.GND, T1.GND, S2.L1
  N3: Arduino1.A0, T1.Vout
