# Fritzing sketch thermistorToLCD (saved by Fritzing 0.3.14b)
breadboards: 1

parts:
  Arduino1 = Arduino
  R1 = Temperature Sensor (Thermistor) [package=THT]
  R2 = Resistor [resistance=10k package=THT]
  Part1 = LCD
  R3 = Trimmer Potentiometer [package=THT]

nets:
  N1: Arduino1.GND, R2.Pin_0, Part1.connector4, Part1.connector15
  N2: Arduino1.D12, Part1.connector3
  N3: Arduino1.D11, Part1.connector5
  N4: Arduino1.D5, Part1.connector10
  N5: Arduino1.D4, Part1.connector11
  N6: Arduino1.D3, Part1.connector12
  N7: Arduino1.D2, Part1.connector13
  N8: Arduino1.+5V, R1.pin_1, Part1.connector14
  N9: Arduino1.A5, R1.pin_0, R2.Pin_1
  N10: Part1.connector0, R3.leg2
  N11: Part1.connector1, R3.leg1
  N12: Part1.connector2, R3.wiper

notes:
  I used a rotary shaft POT here, but for the diagram had to use the trimmer to get it to fit.
