# Fritzing sketch thermotemp1 (saved by Fritzing 0.5.2b)
breadboards: 1

parts:
  R1 = Temperature Sensor (Thermistor) [package=THT]
  R2 = Resistor [resistance=10k package=THT]
  Arduino1 = Arduino
  R3 = Resistor [resistance=10k package=THT]
  S1 = Pushbutton [package=THT]
  DI1 = 7-Segment LED Display [package=THT]
  R4 = Resistor [resistance=470 package=THT]
  R4_2 = Resistor [resistance=470 package=THT]
  R4_3 = Resistor [resistance=470 package=THT]
  R4_4 = Resistor [resistance=470 package=THT]
  R4_5 = Resistor [resistance=470 package=THT]
  R4_6 = Resistor [resistance=470 package=THT]
  R4_7 = Resistor [resistance=470 package=THT]

nets:
  N1: R1.pin_0, R2.Pin_0, Arduino1.A5
  N2: R1.pin_1, Arduino1.+5V, R3.Pin_0
  N3: R2.Pin_1, Arduino1.GND, S1.leg0, DI1.commAnode#7
  N4: Arduino1.D9, R3.Pin_1, S1.leg1
  N5: Arduino1.D8, R4.Pin_0
  N6: Arduino1.D7, R4_2.Pin_0
  N7: Arduino1.D6, R4_6.Pin_1
  N8: Arduino1.D5, R4_5.Pin_1
  N9: Arduino1.D4, R4_7.Pin_1
  N10: Arduino1.D3, R4_3.Pin_0
  N11: Arduino1.D2, R4_4.Pin_0
  N12: DI1.cathodeE, R4_6.Pin_0
  N13: DI1.cathodeD, R4_5.Pin_0
  N14: DI1.cathodeC, R4_7.Pin_0
  N15: DI1.cathodeB, R4_4.Pin_1
  N16: DI1.cathodeA, R4_3.Pin_1
  N17: DI1.cathodeF, R4_2.Pin_1
  N18: DI1.cathodeG, R4.Pin_1

notes:
  common cathode 7-segment display
