# Fritzing sketch tilt-switch_TiltSwitch (saved by Fritzing 0.3.2b)
breadboards: 1

parts:
  LED1 = Red LED - 5mm
  R1 = 10k Ω Resistor [package=THT]
  S1 = Tilt Switch [package=THT]
  Arduino1 = Arduino

nets:
  N1: LED1.cathode, R1.Pin_1, Arduino1.GND
  N2: LED1.anode, Arduino1.D13
  N3: R1.Pin_0, S1.Pin_2, Arduino1.D2
  N4: S1.Pin_1, Arduino1.+5V

notes:
  In this example, a tilt switch is used (just like a button) as a digital input, and an LED is a digital output. The resistor is a pull-down resistor.
  Related example: http://www.arduino.cc/en/Tutorial/TiltSensor
