# Fritzing sketch tima (saved by Fritzing 0.3.13b)
breadboards: 1

parts:
  J1 = Basic Servo
  Arduino2 = Arduino
  M1 = DC Motor
  R1 = Resistor [resistance=220 package=THT]
  LED1 = green LED - 5mm
  LED2 = green LED - 5mm
  LED3 = Red LED - 5mm
  R2 = Resistor [resistance=220 package=THT]

nets:
  GND: J1.gnd, Arduino2.GND, M1.pin_2
  VCC: J1.vcc, Arduino2.+5V
  N1: J1.pulse, Arduino2.D9
  N2: Arduino2.D4, R2.Pin_0
  N3: R1.Pin_1, LED2.cathode
  N4: LED1.anode, LED3.anode
  N5: LED3.cathode, R2.Pin_1

notes:
  Tima the Creativity Knight
  - ventola da computer riciclata come sensore di soffio
  - servomotore alza il barccio
  - doppio LED green ad alta intensità come occhio pulsant
  - led rosso come feedback del sensore
  - BlinkM come metafora del mondo
