# Fritzing sketch touch (saved by Fritzing 0.3.16b)
breadboards: 1

parts:
  Arduino1 = Arduino
  IC1 = IC, DIP package, 40 pins [chip_label=ITDB02_40pins spacing=300mil]

nets:
  N1: Arduino1.GND, IC1.pin1
  N2: Arduino1.D11, IC1.pin17
  N3: Arduino1.D10, IC1.pin15
  N4: Arduino1.D9, IC1.pin5
  N5: Arduino1.D8, IC1.pin4
  N6: Arduino1.D7, IC1.pin14
  N7: Arduino1.D6, IC1.pin13
  N8: Arduino1.D5, IC1.pin12
  N9: Arduino1.D4, IC1.pin11
  N10: Arduino1.D3, IC1.pin10
  N11: Arduino1.D2, IC1.pin9
  N12: Arduino1.D1TX, IC1.pin8
  N13: Arduino1.D0RX, IC1.pin7
  N14: Arduino1.3V3, IC1.pin6, IC1.pin19
  N15: Arduino1.+5V, IC1.pin2
  N16: Arduino1.A0, IC1.pin26
  N17: Arduino1.A1, IC1.pin27
  N18: Arduino1.A2, IC1.pin28
  N19: Arduino1.A3, IC1.pin29
  N20: Arduino1.A4, IC1.pin30
  N21: Arduino1.A5, IC1.pin31
