# Fritzing sketch tvbg (saved by Fritzing 0.6.5b)
breadboards: 1

parts:
  LED1 = LED - 5mm [color="Red (633nm)" package="5 mm [THT]"]
  Arduino2 = Arduino
  LED2 = LED - 5mm [color="Infrared (940nm)" package="5 mm [THT]"]
  S1 = Pushbutton [package="[THT]"]

nets:
  N1: LED1.cathode, Arduino2.GND, LED2.cathode, S1.Pin_1, S1.Pin_2
  N2: LED1.anode, Arduino2.D13
  N3: Arduino2.D3, LED2.anode
  N4: Arduino2.D1TX, S1.Pin_3, S1.Pin_4
