# Fritzing sketch twoServosBot_sonar_v2 (saved by Fritzing 0.3.19b)
breadboards: 1

parts:
  SerLCD_2_5_Module_hooked_to_a_16x2_LCD = SerLCD 2.5 16x2
  Mega = Arduino Mega
  Serial_RX_switch = Toggle Switch [package=THT]
  Neck_Servo_Pin_10 = Basic Servo
  Hip_Servo_Pin_9 = Basic Servo
  Sonar_Rangefinder_SRF05 = SRF05 Ultrasonic Rangefinder

nets:
  VCC: SerLCD_2_5_Module_hooked_to_a_16x2_LCD.connector0, Mega.+5V, Neck_Servo_Pin_10.vcc, Hip_Servo_Pin_9.vcc, Sonar_Rangefinder_SRF05.connector0
  GND: SerLCD_2_5_Module_hooked_to_a_16x2_LCD.connector1, Mega.GND, Neck_Servo_Pin_10.gnd, Hip_Servo_Pin_9.gnd, Sonar_Rangefinder_SRF05.connector4
  N1: SerLCD_2_5_Module_hooked_to_a_16x2_LCD.connector2, Serial_RX_switch.L2
  N2: Mega.D10, Neck_Servo_Pin_10.pulse
  N3: Mega.D9, Hip_Servo_Pin_9.pulse
  N4: Mega.D3, Sonar_Rangefinder_SRF05.connector1
  N5: Mega.D2, Sonar_Rangefinder_SRF05.connector2
  N6: Mega.D1TX, Serial_RX_switch.COM
