# Fritzing sketch ultrasonic-hc-sr04-display (saved by Fritzing 0.6.3b)
breadboards: 1

parts:
  Arduino1 = Arduino
  LCD1 = LCD screen
  HC-SR04 = IC, SIP package, 4 pins [chip_label=IC spacing=300mil]

nets:
  GND: Arduino1.GND, LCD1.VSS, LCD1.V0, LCD1.R/W, LCD1.LED-, HC-SR04.pin4
  N1: Arduino1.D12, LCD1.RS
  N2: Arduino1.D11, LCD1.E
  N3: Arduino1.D9, HC-SR04.pin2
  N4: Arduino1.D8, HC-SR04.pin3
  N5: Arduino1.D5, LCD1.DB4
  N6: Arduino1.D4, LCD1.DB5
  N7: Arduino1.D3, LCD1.DB6
  N8: Arduino1.D2, LCD1.DB7
  +5V: Arduino1.+5V, LCD1.VDD, LCD1.LED+, HC-SR04.pin1
