# Fritzing sketch voltage-regulator_VoltageRegulator_with_switch (saved by Fritzing 0.3.2b)
breadboards: 1

parts:
  S1 = Toggle Switch [package=THT]
  C1 = Electrolytic Capacitor [package=THT]
  C2 = Electrolytic Capacitor [package=THT]
  U1 = Voltage Regulator - 5V [package="TO220 [THT]"]
  Power_plug1 = Power plug
  J2 = Generic male header - 2 pins [package=THT]

nets:
  N1: S1.COM, C1.+, U1.input_voltage
  N2: S1.L2, Power_plug1.VCC
  GND: C1.-, C2.-, U1.GND, Power_plug1.GND, J2.pin2
  N3: C2.+, U1.output_voltage, J2.pin1

notes:
  This example uses a 7805 voltage regulator to regulate voltage to 5 volts. There is a switch to turn power to the circuit on and off. The battery should be at least 7V DC.
