# Fritzing sketch weather_station (saved by Fritzing 0.5.2b)
breadboards: 1

parts:
  U1 = IC, SIP package, 4 pins [chip_label=SHT10 spacing=300mil]
  C1 = Ceramic Capacitor [capacitance=100nF rated_voltage=35V package="200 mil [THT, multilayer]"]
  R1 = Resistor [resistance=10k package=THT]
  Arduino1 = Arduino
  R2 = Resistor [resistance=33k package=THT]
  R3 = Resistor [resistance=1k package=THT]
  V1 = FD-263-01
  U2 = IC, SIP package, 6 pins [chip_label=MPX4115AP spacing=300mil]
  C2 = Ceramic Capacitor [capacitance=100nF rated_voltage=35V package="100 mil [THT, multilayer]"]
  R4 = Resistor [resistance=47k package=THT]

nets:
  N1: U1.pin1, C1.1, R1.Pin_1, Arduino1.+5V, R2.Pin_1, U2.pin3
  N2: U1.pin2, Arduino1.D11
  N3: U1.pin3, R1.Pin_0, Arduino1.D10
  N4: U1.pin4, C1.0, Arduino1.GND, R3.Pin_1, U2.pin2, C2.0, R4.Pin_1
  N5: Arduino1.A0, R2.Pin_0, V1.connector0
  N6: Arduino1.A1, U2.pin1, C2.1, R4.Pin_0
  N7: R3.Pin_0, V1.connector1
