# Fritzing sketch wiithing (saved by Fritzing 0.6.3b)
breadboards: 1

parts:
  Arduino1 = Arduino
  J1 = Basic Servo
  J2 = Basic Servo
  U1 = 3-Axis Accelerometer Breakout

nets:
  GND: Arduino1.GND, U1.GND
  N1: Arduino1.D7, J1.pulse
  N2: Arduino1.D6, J2.pulse
  +5V: Arduino1.+5V, U1.VDD
  N3: Arduino1.A4, U1.Y
  N4: Arduino1.A5, U1.X
