# Fritzing sketch youthrepellent (saved by Fritzing 0.6.3b)
breadboards: 1

parts:
  MBED1 = mbed
  SPKR1 = Loudspeaker
  R1 = Trimmer Potentiometer [maximum_resistance=10kΩ package=THT]

nets:
  N1: MBED1.GND, SPKR1.pin1, R1.leg1
  N2: MBED1.pin21, R1.leg2
  N3: SPKR1.pin2, R1.wiper
